# Fritzing sketch ESP32_TCA9548A (saved by Fritzing 0.9.6b)
stripboards: 1

parts:
  U1 = Adafruit TCA9548A
  M1 = DOIT Esp32 DevKit v1 (30 pins long, 11 pins width) [part_number=ESP32S-PIN30]  # not connected
  J7 = male pin header, 4 pins [form="♂ (male)"]
  J8 = male pin header, 4 pins [form="♂ (male)"]
  J9 = male pin header, 4 pins [form="♂ (male)"]

nets:
  I2C_05SDA: U1.5SDA, J9.pin2
  I2C_05SCL: U1.5SCL, J9.pin3
  I2C_06SDA: U1.6SDA, J8.pin2
  I2C_06SCL: U1.6SCL, J8.pin3
  I2C_07SDA: U1.7SDA, J7.pin2
  I2C_07SCL: U1.7SCL, J7.pin3
  N1: J7.pin1, J8.pin1, J9.pin1
  3.3V: J7.pin4, J8.pin4, J9.pin4

custom parts:
  Adafruit TCA9548A: You just found the perfect I2C sensor, and you want to wire up two or three or more of them to your Arduino when you realize "Uh oh, this chip has a fixed I2C address, and from what I know about I2C, you cannot have two devices with the same address on the same SDA/SCL pins!" Are you out of luck? You would be, if you didn't have this ultra-cool TCA9548A 1-to-8 I2C multiplexer! Finally, a way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
  DOIT Esp32 DevKit v1 (30 pins long, 11 pins width): The DOIT Esp32 DevKit v1 is one of the development board created by DOIT to evaluate the ESP-WROOM-32 module. It is based on the ESP32 microcontroller that boasts Wifi, Bluetooth, Ethernet and Low Power support all in a single chip. (vanepp) made breadboard work, adjusted pin numbering and labels and reduced size of schematic and cleaned up pcb. This chip is 30pins long (2 x15) and 11 pins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
