# Fritzing sketch SPSK_Styring (saved by Fritzing 0.9.6b)

parts:
  R1 = Resistor [tolerance=±5% power=0.25 resistance=220 package=THT]
  D1 = Rectifier Diode [part_number=1N4001 package="300 mil [THT]"]
  J2 = male pin header, 3 pins [form="♂ (male)"]
  J3 = male pin header, 5 pins [form="♂ (male)"]
  J4 = male pin header, 6 pins [form="♂ (male)"]
  Q5b2 = NPN-Transistor [package="TO92 [THT]"]
  Q5b3 = NPN-Transistor [package="TO92 [THT]"]
  Q2 = npn-Powertransistor [package="TO220 [THT]"]
  Q1 = npn-Powertransistor [package="TO220 [THT]"]
  Q3 = npn-Powertransistor [package="TO220 [THT]"]
  Q4 = npn-Powertransistor [package="TO220 [THT]"]
  D5 = Rectifier Diode [part_number=1N4001 package="300 mil [THT]"]
  D6 = Rectifier Diode [part_number=1N4001 package="300 mil [THT]"]
  R3 = Resistor [tolerance=±5% power=0.25 resistance=220 package=THT]
  R4 = Resistor [tolerance=±5% power=0.25 resistance=220 package=THT]
  R5 = Resistor [tolerance=±5% power=0.25 resistance=220 package=THT]
  R6 = Resistor [tolerance=±5% power=0.25 resistance=220 package=THT]
  D7 = Rectifier Diode [part_number=1N4001 package="300 mil [THT]"]
  R7 = Resistor [tolerance=±5% power=0.25 resistance=220 package=THT]
  D8 = Rectifier Diode [part_number=1N4001 package="300 mil [THT]"]
  D9 = Rectifier Diode [part_number=1N4001 package="300 mil [THT]"]
  D10 = Rectifier Diode [part_number=1N4001 package="300 mil [THT]"]
  Q5b4 = NPN-Transistor [package="TO92 [THT]"]
  D11 = Rectifier Diode [part_number=1N4001 package="300 mil [THT]"]
  Q5b1 = NPN-Transistor [package="TO92 [THT]"]
  D12 = Rectifier Diode [part_number=1N4001 package="300 mil [THT]"]
  LED1 = LED - 5mm [color="Red (633nm)" current=0.030 package="5 mm [THT]"]
  R8 = Resistor [tolerance=±5% power=0.25 resistance=220 package=THT]

nets:
  N1: R1.Pin_0, R5.Pin_0, D9.cathode, D10.cathode, D11.cathode, D12.cathode, LED1.anode
  N2: R1.Pin_1, Q1.base
  12V: D1.cathode, J2.pin3, J4.pin2, J4.pin5, D5.cathode, D6.cathode
  N3: D1.anode, J4.pin1, Q1.collector
  GND: J2.pin1, Q5b2.E, Q5b3.E, Q2.emitter, Q1.emitter, Q3.emitter, Q4.emitter, R6.Pin_0, R7.Pin_0, Q5b4.E, Q5b1.E, R8.Pin_1
  5V: J2.pin2
  tilbage1: J3.pin1
  Tilbage2: J3.pin2
  Ind1: J3.pin3
  Ind2: J3.pin4
  N4: J4.pin3, Q2.collector, D5.anode
  N5: J4.pin4, Q3.collector, D6.anode
  N6: J4.pin6, Q4.collector
  N7: Q5b2.C, D10.anode
  N8: Q5b3.C, D9.anode
  N9: Q2.base, R3.Pin_1
  N10: Q3.base, R4.Pin_1
  N11: Q4.base, R5.Pin_1
  N12: R3.Pin_0, R6.Pin_1, D7.anode
  N13: R4.Pin_0, R7.Pin_1, D8.anode
  N14: Q5b4.C, D11.anode
  N15: Q5b1.C, D12.anode
  N16: LED1.cathode, R8.Pin_0
