# Fritzing sketch input_track (saved by Fritzing 0.9.6b)
stripboards: 1

parts:
  R1 = Resistor [tolerance=±5% power=0.25 resistance=100 package=THT]
  R2 = Resistor [tolerance=±5% power=0.25 resistance=100 package=THT]
  R3 = Resistor [tolerance=±5% power=0.25 resistance=100 package=THT]
  R4 = Resistor [tolerance=±5% power=0.25 resistance=100 package=THT]
  R5 = Resistor [tolerance=±5% power=0.25 resistance=100 package=THT]
  R6 = Resistor [tolerance=±5% power=0.25 resistance=100 package=THT]
  R7 = Resistor [tolerance=±5% power=0.25 resistance=100 package=THT]
  R8 = Resistor [tolerance=±5% power=0.25 resistance=100 package=THT]
  R9 = Resistor [tolerance=±5% power=0.25 resistance=100 package=THT]
  R10 = Resistor [tolerance=±5% power=0.25 resistance=100 package=THT]
  R11 = Resistor [tolerance=±5% power=0.25 resistance=100 package=THT]
  R12 = Resistor [tolerance=±5% power=0.25 resistance=100 package=THT]
  R13 = Resistor [tolerance=±5% power=0.25 resistance=100 package=THT]
  R14 = Resistor [tolerance=±5% power=0.25 resistance=100 package=THT]
  R15 = Resistor [tolerance=±5% power=0.25 resistance=100 package=THT]
  R16 = Resistor [tolerance=±5% power=0.25 resistance=100 package=THT]
  R17 = Resistor [tolerance=±5% power=0.25 resistance=100 package=THT]
  R18 = Resistor [tolerance=±5% power=0.25 resistance=100 package=THT]
  R19 = Resistor [tolerance=±5% power=0.25 resistance=100 package=THT]
  R20 = Resistor [tolerance=±5% power=0.25 resistance=100 package=THT]
  R21 = Resistor [tolerance=±5% power=0.25 resistance=100 package=THT]
  R22 = Resistor [tolerance=±5% power=0.25 resistance=100 package=THT]
  R23 = Resistor [tolerance=±5% power=0.25 resistance=100 package=THT]
  R24 = Resistor [tolerance=±5% power=0.25 resistance=100 package=THT]
  J1 = male pin header, 9 pins [form="♂ (male)"]
  J3 = male pin header, 9 pins [form="♂ (male)"]
  U15 = TLP620-4 [package="DIP (Dual Inline) [THT]"]
  U18 = TLP620-4 [package="DIP (Dual Inline) [THT]"]
  U17 = TLP620-4 [package="DIP (Dual Inline) [THT]"]
  U14 = TLP620-4 [package="DIP (Dual Inline) [THT]"]
  J16 = male pin header, 1 pin [form="♂ (male)"]
  J17 = male pin header, 1 pin [form="♂ (male)"]
  J18 = male pin header, 1 pin [form="♂ (male)"]
  J19 = male pin header, 1 pin [form="♂ (male)"]
  J20 = male pin header, 1 pin [form="♂ (male)"]
  J21 = male pin header, 1 pin [form="♂ (male)"]
  J22 = male pin header, 1 pin [form="♂ (male)"]
  J23 = male pin header, 1 pin [form="♂ (male)"]
  J24 = male pin header, 1 pin [form="♂ (male)"]
  J25 = male pin header, 1 pin [form="♂ (male)"]
  J26 = male pin header, 1 pin [form="♂ (male)"]
  J27 = male pin header, 1 pin [form="♂ (male)"]
  U12 = TLP620-4 [package="DIP (Dual Inline) [THT]"]
  U11 = TLP620-4 [package="DIP (Dual Inline) [THT]"]
  J31 = male pin header, 1 pin [form="♂ (male)"]
  J32 = male pin header, 1 pin [form="♂ (male)"]
  J33 = male pin header, 1 pin [form="♂ (male)"]
  J34 = male pin header, 1 pin [form="♂ (male)"]
  J35 = male pin header, 1 pin [form="♂ (male)"]
  J36 = male pin header, 1 pin [form="♂ (male)"]
  J37 = male pin header, 1 pin [form="♂ (male)"]
  J38 = male pin header, 1 pin [form="♂ (male)"]
  U10 = PCF8574 [package="DIP16 [THT]"]
  U13 = PCF8574 [package="DIP16 [THT]"]
  J39 = male pin header, 4 pins [form="♂ (male)"]
  J40 = male pin header, 4 pins [form="♂ (male)"]
  R25 = Resistor [tolerance=±5% power=0.25 resistance=100k package=THT]
  R26 = Resistor [tolerance=±5% power=0.25 resistance=100k package=THT]
  U16 = PCF8574 [package="DIP16 [THT]"]
  J41 = male pin header, 1 pin [form="♂ (male)"]
  J42 = male pin header, 1 pin [form="♂ (male)"]
  J44 = male pin header, 1 pin [form="♂ (male)"]
  J45 = male pin header, 1 pin [form="♂ (male)"]
  J46 = male pin header, 1 pin [form="♂ (male)"]
  J47 = male pin header, 1 pin [form="♂ (male)"]
  J48 = male pin header, 1 pin [form="♂ (male)"]
  J49 = male pin header, 1 pin [form="♂ (male)"]
  J50 = male pin header, 1 pin [form="♂ (male)"]
  J51 = male pin header, 1 pin [form="♂ (male)"]
  J52 = male pin header, 1 pin [form="♂ (male)"]
  J53 = male pin header, 1 pin [form="♂ (male)"]
  J54 = male pin header, 1 pin [form="♂ (male)"]
  J55 = male pin header, 1 pin [form="♂ (male)"]
  J56 = male pin header, 1 pin [form="♂ (male)"]
  J57 = male pin header, 4 pins [form="♂ (male)"]
  J58 = male pin header, 4 pins [form="♂ (male)"]
  J59 = male pin header, 4 pins [form="♂ (male)"]
  J60 = male pin header, 4 pins [form="♂ (male)"]
  A00 = male pin header, 2 pins [form="♂ (male)"]
  A01 = male pin header, 2 pins [form="♂ (male)"]
  A02 = male pin header, 2 pins [form="♂ (male)"]
  J64 = male pin header, 2 pins [form="♂ (male)"]
  J65 = male pin header, 2 pins [form="♂ (male)"]
  J66 = male pin header, 2 pins [form="♂ (male)"]
  J67 = male pin header, 2 pins [form="♂ (male)"]
  J68 = male pin header, 2 pins [form="♂ (male)"]
  J69 = male pin header, 2 pins [form="♂ (male)"]
  R27 = Resistor [tolerance=±5% power=0.25 resistance=100k package=THT]
  J70 = male pin header, 1 pin [form="♂ (male)"]
  J71 = male pin header, 1 pin [form="♂ (male)"]
  J72 = male pin header, 1 pin [form="♂ (male)"]
  J73 = male pin header, 1 pin [form="♂ (male)"]
  J74 = male pin header, 1 pin [form="♂ (male)"]
  J75 = male pin header, 1 pin [form="♂ (male)"]
  J76 = male pin header, 1 pin [form="♂ (male)"]
  J77 = male pin header, 1 pin [form="♂ (male)"]
  J78 = male pin header, 1 pin [form="♂ (male)"]
  J79 = male pin header, 1 pin [form="♂ (male)"]
  J80 = male pin header, 1 pin [form="♂ (male)"]
  J81 = male pin header, 1 pin [form="♂ (male)"]
  J43 = male pin header, 1 pin [form="♂ (male)"]
  J82 = male pin header, 4 pins [form="♂ (male)"]
  J83 = male pin header, 9 pins [form="♂ (male)"]
  R28 = Resistor [tolerance=±5% power=0.25 resistance=100k package=THT]
  R29 = Resistor [tolerance=±5% power=0.25 resistance=100k package=THT]
  R30 = Resistor [tolerance=±5% power=0.25 resistance=100k package=THT]
  R31 = Resistor [tolerance=±5% power=0.25 resistance=100k package=THT]
  R32 = Resistor [tolerance=±5% power=0.25 resistance=100k package=THT]
  R33 = Resistor [tolerance=±5% power=0.25 resistance=100k package=THT]

nets:
  N1: R1.Pin_0, J3.pin8
  N2: R1.Pin_1, J78.pin1
  N3: R2.Pin_0, J3.pin7
  N4: R2.Pin_1, U18.pin7
  N5: R3.Pin_0, J3.pin6
  N6: R3.Pin_1, J80.pin1
  N7: R4.Pin_0, J3.pin5
  N8: R4.Pin_1, U18.pin5
  N9: R5.Pin_0, J3.pin4
  N10: R5.Pin_1, J79.pin1
  N11: R6.Pin_0, J3.pin3
  N12: R6.Pin_1, U18.pin3
  N13: R7.Pin_0, J3.pin1
  N14: R7.Pin_1, U18.pin1
  N15: R8.Pin_0, J3.pin2
  N16: R8.Pin_1, J81.pin1
  N17: R9.Pin_0, J83.pin1
  N18: R9.Pin_1, U15.pin1
  N19: R10.Pin_0, J83.pin2
  N20: R10.Pin_1, J77.pin1
  N21: R11.Pin_0, J83.pin8
  N22: R11.Pin_1, J74.pin1
  N23: R12.Pin_0, J83.pin7
  N24: R12.Pin_1, U15.pin7
  N25: R13.Pin_0, J83.pin6
  N26: R13.Pin_1, J76.pin1
  N27: R14.Pin_0, J83.pin4
  N28: R14.Pin_1, J75.pin1
  N29: R15.Pin_0, J83.pin3
  N30: R15.Pin_1, U15.pin3
  N31: R16.Pin_0, J83.pin5
  N32: R16.Pin_1, U15.pin5
  N33: R17.Pin_0, J1.pin1
  N34: R17.Pin_1, U12.pin1
  N35: R18.Pin_0, J1.pin2
  A00: R18.Pin_1, U11.pin1, J31.pin1, J71.pin1
  N36: R19.Pin_0, J1.pin8
  A03: R19.Pin_1, U11.pin7, J34.pin1, J70.pin1
  N37: R20.Pin_0, J1.pin7
  N38: R20.Pin_1, U12.pin7
  N39: R21.Pin_0, J1.pin6
  A02: R21.Pin_1, U11.pin5, J33.pin1, J73.pin1
  N40: R22.Pin_0, J1.pin4
  A01: R22.Pin_1, U11.pin3, J32.pin1, J72.pin1
  N41: R23.Pin_0, J1.pin3
  N42: R23.Pin_1, U12.pin3
  N43: R24.Pin_0, J1.pin5
  N44: R24.Pin_1, U12.pin5
  LINE: J1.pin9, U12.pin2, U12.pin4, U12.pin6, U12.pin8, U11.pin2, U11.pin4, U11.pin6, U11.pin8
  N45: J3.pin9, U18.pin2, U18.pin4, U18.pin6, U18.pin8, U17.pin2, U17.pin4, U17.pin6, U17.pin8
  N46: U15.pin2, U15.pin4, U15.pin6, U15.pin8
  GND: U15.pin9, U15.pin11, U15.pin13, U15.pin15, U18.pin9, U18.pin11, U18.pin13, U18.pin15, U17.pin9, U17.pin11, U17.pin13, U17.pin15, U14.pin9, U14.pin11, U14.pin13, U14.pin15, U12.pin9, U12.pin11, U12.pin13, U12.pin15, U11.pin9, U11.pin11, U11.pin13, U11.pin15, U10.GND, U13.GND, U16.GND, A00.pin1, A01.pin1, A02.pin1, J64.pin1, J65.pin1, J66.pin1, J67.pin1, J68.pin1, J69.pin1, J82.pin1
  N47: U15.pin10, J21.pin1
  N48: U15.pin12, J20.pin1
  N49: U15.pin14, J22.pin1
  N50: U15.pin16, J23.pin1
  N51: U18.pin10, J25.pin1
  N52: U18.pin12, J24.pin1
  N53: U18.pin14, J26.pin1
  N54: U18.pin16, J27.pin1
  N55: U17.pin1, J46.pin1
  N56: U17.pin3, J45.pin1
  N57: U17.pin5, J48.pin1
  N58: U17.pin7, J47.pin1
  N59: U17.pin10, J55.pin1
  N60: U17.pin12, J56.pin1
  N61: U17.pin14, J53.pin1
  N62: U17.pin16, J54.pin1
  N63: U14.pin1, J42.pin1
  N64: U14.pin2, U14.pin4, U14.pin6, U14.pin8, J83.pin9
  N65: U14.pin3, J41.pin1
  N66: U14.pin5, J44.pin1
  N67: U14.pin7, J43.pin1
  N68: U14.pin10, J51.pin1
  N69: U14.pin12, J52.pin1
  N70: U14.pin14, J49.pin1
  N71: U14.pin16, J50.pin1
  AA02: J16.pin1, U12.pin12, U10.P2, J39.pin3
  AA03: J17.pin1, U12.pin10, U10.P3, J39.pin4
  AA01: J18.pin1, U12.pin14, U10.P1, J39.pin2
  AA00: J19.pin1, U12.pin16, U10.P0, J39.pin1
  N72: U11.pin10, J37.pin1
  N73: U11.pin12, J38.pin1
  N74: U11.pin14, J36.pin1
  N75: U11.pin16, J35.pin1
  N76: U10.A0, A00.pin2, R27.Pin_1
  N77: U10.A1, R26.Pin_1, A01.pin2
  N78: U10.A2, R25.Pin_1, A02.pin2
  N79: U10.P4, J40.pin4
  N80: U10.P5, J40.pin3
  N81: U10.P6, J40.pin2
  N82: U10.P7, J40.pin1
  I2C_SCL: U10.SCL, U13.SCL, U16.SCL, J82.pin3
  I2C_SDA: U10.SDA, U13.SDA, U16.SDA, J82.pin2
  3.3V: U10.VCC, U13.VCC, R25.Pin_0, R26.Pin_0, U16.VCC, R27.Pin_0, J82.pin4, R28.Pin_0, R29.Pin_0, R30.Pin_0, R31.Pin_0, R32.Pin_0, R33.Pin_0
  N83: U13.A0, J64.pin2, R29.Pin_1
  N84: U13.A1, J65.pin2, R28.Pin_1
  N85: U13.A2, J66.pin2, R30.Pin_1
  N86: U13.P0, J57.pin1
  N87: U13.P1, J57.pin2
  N88: U13.P2, J57.pin3
  N89: U13.P3, J57.pin4
  N90: U13.P4, J58.pin4
  N91: U13.P5, J58.pin3
  N92: U13.P6, J58.pin2
  N93: U13.P7, J58.pin1
  N94: U16.A0, J67.pin2, R32.Pin_1
  N95: U16.A1, J68.pin2, R33.Pin_1
  N96: U16.A2, J69.pin2, R31.Pin_1
  N97: U16.P0, J59.pin1
  N98: U16.P1, J59.pin2
  N99: U16.P2, J59.pin3
  N100: U16.P3, J59.pin4
  N101: U16.P4, J60.pin4
  N102: U16.P5, J60.pin3
  N103: U16.P6, J60.pin2
  N104: U16.P7, J60.pin1

custom parts:
  TLP620-4: Quad Photo-transistor optically coupled to two infrared emitting diodes connected in inverse parallel.
