# Fritzing sketch output_led (saved by Fritzing 0.9.6b)
stripboards: 1

parts:
  U1 = Sharp PC847X [package=THT]
  R1 = Resistor [tolerance=±5% power=0.25 resistance=330 package=THT]
  R2 = Resistor [tolerance=±5% power=0.25 resistance=330 package=THT]
  R3 = Resistor [tolerance=±5% power=0.25 resistance=330 package=THT]
  R4 = Resistor [tolerance=±5% power=0.25 resistance=330 package=THT]
  U2 = PCF8574 [package="DIP16 [THT]"]
  J1 = male pin header, 2 pins [form="♂ (male)"]
  J2 = male pin header, 2 pins [form="♂ (male)"]
  J3 = male pin header, 2 pins [form="♂ (male)"]
  J9 = male pin header, 1 pin [form="♂ (male)"]
  J10 = male pin header, 1 pin [form="♂ (male)"]
  J11 = male pin header, 1 pin [form="♂ (male)"]
  J12 = male pin header, 1 pin [form="♂ (male)"]
  J17 = male pin header, 1 pin [form="♂ (male)"]
  J18 = male pin header, 1 pin [form="♂ (male)"]
  J19 = male pin header, 1 pin [form="♂ (male)"]
  J20 = male pin header, 1 pin [form="♂ (male)"]
  J13 = male pin header, 4 pins [form="♂ (male)"]
  Rx1 = female pin header, 4 pins [form="♀ (female)"]
  J21 = male pin header, 4 pins [form="♂ (male)"]
  J22 = male pin header, 4 pins [form="♂ (male)"]
  J23 = male pin header, 4 pins [form="♂ (male)"]
  U3 = PCF8574 [package="DIP16 [THT]"]
  U4 = PCF8574 [package="DIP16 [THT]"]
  J24 = male pin header, 2 pins [form="♂ (male)"]
  J25 = male pin header, 2 pins [form="♂ (male)"]
  J26 = male pin header, 2 pins [form="♂ (male)"]
  J27 = male pin header, 2 pins [form="♂ (male)"]
  J28 = male pin header, 2 pins [form="♂ (male)"]
  J29 = male pin header, 2 pins [form="♂ (male)"]
  Rx2 = female pin header, 4 pins [form="♀ (female)"]
  Rx3 = female pin header, 4 pins [form="♀ (female)"]
  R5 = Resistor [tolerance=±5% power=0.25 resistance=330 package=THT]
  R6 = Resistor [tolerance=±5% power=0.25 resistance=330 package=THT]
  R7 = Resistor [tolerance=±5% power=0.25 resistance=330 package=THT]
  R8 = Resistor [tolerance=±5% power=0.25 resistance=330 package=THT]
  J30 = male pin header, 4 pins [form="♂ (male)"]
  R9 = Resistor [tolerance=±5% power=0.25 resistance=330 package=THT]
  R10 = Resistor [tolerance=±5% power=0.25 resistance=330 package=THT]
  R11 = Resistor [tolerance=±5% power=0.25 resistance=330 package=THT]
  R12 = Resistor [tolerance=±5% power=0.25 resistance=330 package=THT]
  J31 = male pin header, 4 pins [form="♂ (male)"]
  R13 = Resistor [tolerance=±5% power=0.25 resistance=330 package=THT]
  R14 = Resistor [tolerance=±5% power=0.25 resistance=330 package=THT]
  R15 = Resistor [tolerance=±5% power=0.25 resistance=330 package=THT]
  R16 = Resistor [tolerance=±5% power=0.25 resistance=330 package=THT]
  J32 = male pin header, 4 pins [form="♂ (male)"]
  R17 = Resistor [tolerance=±5% power=0.25 resistance=330 package=THT]
  R18 = Resistor [tolerance=±5% power=0.25 resistance=330 package=THT]
  R19 = Resistor [tolerance=±5% power=0.25 resistance=330 package=THT]
  R20 = Resistor [tolerance=±5% power=0.25 resistance=330 package=THT]
  J33 = male pin header, 4 pins [form="♂ (male)"]
  R21 = Resistor [tolerance=±5% power=0.25 resistance=330 package=THT]
  R22 = Resistor [tolerance=±5% power=0.25 resistance=330 package=THT]
  R23 = Resistor [tolerance=±5% power=0.25 resistance=330 package=THT]
  R24 = Resistor [tolerance=±5% power=0.25 resistance=330 package=THT]
  J34 = male pin header, 4 pins [form="♂ (male)"]
  R25 = Resistor [tolerance=±5% power=0.25 resistance=330 package=THT]
  R26 = Resistor [tolerance=±5% power=0.25 resistance=330 package=THT]
  R27 = Resistor [tolerance=±5% power=0.25 resistance=330 package=THT]
  R28 = Resistor [tolerance=±5% power=0.25 resistance=330 package=THT]
  U5 = Sharp PC847X [package=THT]
  R29 = Resistor [tolerance=±5% power=0.25 resistance=330 package=THT]
  R30 = Resistor [tolerance=±5% power=0.25 resistance=330 package=THT]
  R31 = Resistor [tolerance=±5% power=0.25 resistance=330 package=THT]
  R32 = Resistor [tolerance=±5% power=0.25 resistance=330 package=THT]
  J35 = male pin header, 1 pin [form="♂ (male)"]
  J36 = male pin header, 1 pin [form="♂ (male)"]
  J37 = male pin header, 1 pin [form="♂ (male)"]
  J38 = male pin header, 1 pin [form="♂ (male)"]
  J39 = male pin header, 1 pin [form="♂ (male)"]
  J40 = male pin header, 1 pin [form="♂ (male)"]
  J41 = male pin header, 1 pin [form="♂ (male)"]
  J42 = male pin header, 1 pin [form="♂ (male)"]
  J4 = male pin header, 9 pins [form="♂ (male)"]
  U6 = Sharp PC847X [package=THT]
  U7 = Sharp PC847X [package=THT]
  J43 = male pin header, 9 pins [form="♂ (male)"]
  J44 = male pin header, 9 pins [form="♂ (male)"]
  R33 = Resistor [tolerance=±5% power=0.25 resistance=330 package=THT]
  R34 = Resistor [tolerance=±5% power=0.25 resistance=330 package=THT]
  R35 = Resistor [tolerance=±5% power=0.25 resistance=330 package=THT]
  R36 = Resistor [tolerance=±5% power=0.25 resistance=330 package=THT]
  R37 = Resistor [tolerance=±5% power=0.25 resistance=330 package=THT]
  R38 = Resistor [tolerance=±5% power=0.25 resistance=330 package=THT]
  R39 = Resistor [tolerance=±5% power=0.25 resistance=330 package=THT]
  R40 = Resistor [tolerance=±5% power=0.25 resistance=330 package=THT]
  J45 = male pin header, 1 pin [form="♂ (male)"]
  J46 = male pin header, 1 pin [form="♂ (male)"]
  J47 = male pin header, 1 pin [form="♂ (male)"]
  J48 = male pin header, 1 pin [form="♂ (male)"]
  J49 = male pin header, 1 pin [form="♂ (male)"]
  J50 = male pin header, 1 pin [form="♂ (male)"]
  J51 = male pin header, 1 pin [form="♂ (male)"]
  J52 = male pin header, 1 pin [form="♂ (male)"]
  J53 = male pin header, 1 pin [form="♂ (male)"]
  J54 = male pin header, 1 pin [form="♂ (male)"]
  J55 = male pin header, 1 pin [form="♂ (male)"]
  J56 = male pin header, 1 pin [form="♂ (male)"]
  J57 = male pin header, 1 pin [form="♂ (male)"]
  J58 = male pin header, 1 pin [form="♂ (male)"]
  J59 = male pin header, 1 pin [form="♂ (male)"]
  J60 = male pin header, 1 pin [form="♂ (male)"]
  U8 = Sharp PC847X [package=THT]
  U9 = Sharp PC847X [package=THT]
  R41 = Resistor [tolerance=±5% power=0.25 resistance=330 package=THT]
  R42 = Resistor [tolerance=±5% power=0.25 resistance=330 package=THT]
  R43 = Resistor [tolerance=±5% power=0.25 resistance=330 package=THT]
  R44 = Resistor [tolerance=±5% power=0.25 resistance=330 package=THT]
  R45 = Resistor [tolerance=±5% power=0.25 resistance=330 package=THT]
  R46 = Resistor [tolerance=±5% power=0.25 resistance=330 package=THT]
  R47 = Resistor [tolerance=±5% power=0.25 resistance=330 package=THT]
  R48 = Resistor [tolerance=±5% power=0.25 resistance=330 package=THT]
  J61 = male pin header, 1 pin [form="♂ (male)"]
  J62 = male pin header, 1 pin [form="♂ (male)"]
  J63 = male pin header, 1 pin [form="♂ (male)"]
  J64 = male pin header, 1 pin [form="♂ (male)"]
  J65 = male pin header, 1 pin [form="♂ (male)"]
  J66 = male pin header, 1 pin [form="♂ (male)"]
  J67 = male pin header, 1 pin [form="♂ (male)"]
  J68 = male pin header, 1 pin [form="♂ (male)"]
  J69 = male pin header, 1 pin [form="♂ (male)"]
  J70 = male pin header, 1 pin [form="♂ (male)"]
  J71 = male pin header, 1 pin [form="♂ (male)"]
  J72 = male pin header, 1 pin [form="♂ (male)"]
  J73 = male pin header, 1 pin [form="♂ (male)"]
  J74 = male pin header, 1 pin [form="♂ (male)"]
  J75 = male pin header, 1 pin [form="♂ (male)"]
  J76 = male pin header, 1 pin [form="♂ (male)"]
  J77 = male pin header, 4 pins [form="♂ (male)"]
  J78 = male pin header, 4 pins [form="♂ (male)"]
  J79 = male pin header, 4 pins [form="♂ (male)"]
  J80 = male pin header, 4 pins [form="♂ (male)"]

nets:
  N1: U1.Pin_1, R25.Pin_0
  N2: U1.Pin_2, J11.pin1
  N3: U1.Pin_3, R26.Pin_0
  N4: U1.Pin_4, J10.pin1
  N5: U1.Pin_5, R27.Pin_0
  N6: U1.Pin_6, J12.pin1
  N7: U1.Pin_7, R28.Pin_0
  N8: U1.Pin_8, J9.pin1
  N9: U1.Pin_9, R4.Pin_1, J18.pin1, J13.pin1
  N10: U1.Pin_10, U1.Pin_12, U1.Pin_14, U1.Pin_16, U5.Pin_10, U5.Pin_12, U5.Pin_14, U5.Pin_16, J4.pin1
  N11: U1.Pin_11, R3.Pin_1, J17.pin1, J13.pin2
  N12: U1.Pin_13, R2.Pin_1, J20.pin1, J13.pin3
  N13: U1.Pin_15, R1.Pin_1, J19.pin1, J13.pin4
  N14: R1.Pin_0, J4.pin2
  N15: R2.Pin_0, J4.pin3
  N16: R3.Pin_0, J4.pin4
  N17: R4.Pin_0, J4.pin5
  N18: U2.A0, J1.pin2, Rx1.pin2
  N19: U2.A1, J2.pin2, Rx1.pin3
  N20: U2.A2, J3.pin2, Rx1.pin4
  N21: U2.P0, J21.pin1
  N22: U2.P1, J21.pin2
  N23: U2.P2, J21.pin3
  N24: U2.P3, J21.pin4
  GND: U2.GND, J1.pin1, J2.pin1, J3.pin1, J23.pin1, U3.GND, U4.GND, J24.pin1, J25.pin1, J26.pin1, J27.pin1, J28.pin1, J29.pin1
  N25: U2.P4, J22.pin4
  N26: U2.P5, J22.pin3
  N27: U2.P6, J22.pin2
  N28: U2.P7, J22.pin1
  I2C_SCL: U2.SCL, J23.pin3, U3.SCL, U4.SCL
  I2C_SDA: U2.SDA, J23.pin2, U3.SDA, U4.SDA
  3.3V: U2.VCC, Rx1.pin1, J23.pin4, U3.VCC, U4.VCC, Rx2.pin1, Rx3.pin1, R25.Pin_1, R26.Pin_1, R27.Pin_1, R28.Pin_1, R29.Pin_1, R30.Pin_1, R31.Pin_1, R32.Pin_1, R33.Pin_1, R34.Pin_1, R35.Pin_1, R36.Pin_1, R37.Pin_1, R38.Pin_1, R39.Pin_1, R40.Pin_1, R41.Pin_1, R42.Pin_1, R43.Pin_1, R44.Pin_1, R45.Pin_1, R46.Pin_1, R47.Pin_1, R48.Pin_1
  N29: U3.A0, J24.pin2, Rx2.pin2
  N30: U3.A1, J26.pin2, Rx2.pin3
  N31: U3.A2, J25.pin2, Rx2.pin4
  N32: U3.P0, J77.pin1
  N33: U3.P1, J77.pin2
  N34: U3.P2, J77.pin3
  N35: U3.P3, J77.pin4
  N36: U3.P4, J78.pin4
  N37: U3.P5, J78.pin3
  N38: U3.P6, J78.pin2
  N39: U3.P7, J78.pin1
  N40: U4.A0, J27.pin2, Rx3.pin2
  N41: U4.A1, J29.pin2, Rx3.pin3
  N42: U4.A2, J28.pin2, Rx3.pin4
  N43: U4.P0, J79.pin1
  N44: U4.P1, J79.pin2
  N45: U4.P2, J79.pin3
  N46: U4.P3, J79.pin4
  N47: U4.P4, J80.pin4
  N48: U4.P5, J80.pin3
  N49: U4.P6, J80.pin2
  N50: U4.P7, J80.pin1
  N51: R5.Pin_0, J4.pin6
  N52: R5.Pin_1, J30.pin4, U5.Pin_15, J37.pin1
  N53: R6.Pin_0, J4.pin7
  N54: R6.Pin_1, J30.pin3, U5.Pin_13, J35.pin1
  N55: R7.Pin_0, J4.pin8
  N56: R7.Pin_1, J30.pin2, U5.Pin_11, J36.pin1
  N57: R8.Pin_0, J4.pin9
  N58: R8.Pin_1, J30.pin1, U5.Pin_9, J38.pin1
  N59: R9.Pin_0, J43.pin2
  N60: R9.Pin_1, J31.pin4, U6.Pin_15, J50.pin1
  N61: R10.Pin_0, J43.pin3
  N62: R10.Pin_1, J31.pin3, U6.Pin_13, J52.pin1
  N63: R11.Pin_0, J43.pin4
  N64: R11.Pin_1, J31.pin2, U6.Pin_11, J51.pin1
  N65: R12.Pin_0, J43.pin5
  N66: R12.Pin_1, J31.pin1, U6.Pin_9, J49.pin1
  N67: R13.Pin_0, J43.pin6
  N68: R13.Pin_1, J32.pin4, U7.Pin_15, J58.pin1
  N69: R14.Pin_0, J43.pin7
  N70: R14.Pin_1, J32.pin3, U7.Pin_13, J60.pin1
  N71: R15.Pin_0, J43.pin8
  N72: R15.Pin_1, J32.pin2, U7.Pin_11, J59.pin1
  N73: R16.Pin_0, J43.pin9
  N74: R16.Pin_1, J32.pin1, U7.Pin_9, J57.pin1
  N75: R17.Pin_0, J44.pin2
  N76: R17.Pin_1, J33.pin4, U9.Pin_15, J70.pin1
  N77: R18.Pin_0, J44.pin3
  N78: R18.Pin_1, J33.pin3, U9.Pin_13, J72.pin1
  N79: R19.Pin_0, J44.pin4
  N80: R19.Pin_1, J33.pin2, U9.Pin_11, J71.pin1
  N81: R20.Pin_0, J44.pin5
  N82: R20.Pin_1, J33.pin1, U9.Pin_9, J69.pin1
  N83: R21.Pin_0, J44.pin6
  N84: R21.Pin_1, J34.pin4, U8.Pin_15, J62.pin1
  N85: R22.Pin_0, J44.pin7
  N86: R22.Pin_1, J34.pin3, U8.Pin_13, J64.pin1
  N87: R23.Pin_0, J44.pin8
  N88: R23.Pin_1, J34.pin2, U8.Pin_11, J63.pin1
  N89: R24.Pin_0, J44.pin9
  N90: R24.Pin_1, J34.pin1, U8.Pin_9, J61.pin1
  N91: U5.Pin_1, R29.Pin_0
  N92: U5.Pin_2, J41.pin1
  N93: U5.Pin_3, R32.Pin_0
  N94: U5.Pin_4, J39.pin1
  N95: U5.Pin_5, R31.Pin_0
  N96: U5.Pin_6, J40.pin1
  N97: U5.Pin_7, R30.Pin_0
  N98: U5.Pin_8, J42.pin1
  N99: U6.Pin_1, R38.Pin_0
  N100: U6.Pin_2, J46.pin1
  N101: U6.Pin_3, R37.Pin_0
  N102: U6.Pin_4, J48.pin1
  N103: U6.Pin_5, R40.Pin_0
  N104: U6.Pin_6, J47.pin1
  N105: U6.Pin_7, R39.Pin_0
  N106: U6.Pin_8, J45.pin1
  N107: U6.Pin_10, U6.Pin_12, U6.Pin_14, U6.Pin_16, U7.Pin_10, U7.Pin_12, U7.Pin_14, U7.Pin_16, J43.pin1
  N108: U7.Pin_1, R33.Pin_0
  N109: U7.Pin_2, J54.pin1
  N110: U7.Pin_3, R36.Pin_0
  N111: U7.Pin_4, J56.pin1
  N112: U7.Pin_5, R35.Pin_0
  N113: U7.Pin_6, J55.pin1
  N114: U7.Pin_7, R34.Pin_0
  N115: U7.Pin_8, J53.pin1
  N116: J44.pin1, U8.Pin_10, U8.Pin_12, U8.Pin_14, U8.Pin_16, U9.Pin_10, U9.Pin_12, U9.Pin_14, U9.Pin_16
  N117: U8.Pin_1, R47.Pin_0
  N118: U8.Pin_2, J66.pin1
  N119: U8.Pin_3, R48.Pin_0
  N120: U8.Pin_4, J68.pin1
  N121: U8.Pin_5, R45.Pin_0
  N122: U8.Pin_6, J67.pin1
  N123: U8.Pin_7, R46.Pin_0
  N124: U8.Pin_8, J65.pin1
  N125: U9.Pin_1, R43.Pin_0
  N126: U9.Pin_2, J74.pin1
  N127: U9.Pin_3, R44.Pin_0
  N128: U9.Pin_4, J76.pin1
  N129: U9.Pin_5, R41.Pin_0
  N130: U9.Pin_6, J75.pin1
  N131: U9.Pin_7, R42.Pin_0
  N132: U9.Pin_8, J73.pin1
