# Fritzing sketch pcb-002 (saved by Fritzing 0.9.6b)
stripboards: 1

parts:
  R1 = Resistor [tolerance=±5% power=0.25 resistance=100 package=THT]
  R2 = Resistor [tolerance=±5% power=0.25 resistance=100 package=THT]
  R3 = Resistor [tolerance=±5% power=0.25 resistance=100 package=THT]
  R4 = Resistor [tolerance=±5% power=0.25 resistance=100 package=THT]
  R5 = Resistor [tolerance=±5% power=0.25 resistance=100 package=THT]
  R6 = Resistor [tolerance=±5% power=0.25 resistance=100 package=THT]
  R7 = Resistor [tolerance=±5% power=0.25 resistance=100 package=THT]
  R8 = Resistor [tolerance=±5% power=0.25 resistance=100 package=THT]
  R9 = Resistor [tolerance=±5% power=0.25 resistance=100 package=THT]
  R10 = Resistor [tolerance=±5% power=0.25 resistance=100 package=THT]
  R11 = Resistor [tolerance=±5% power=0.25 resistance=100 package=THT]
  R12 = Resistor [tolerance=±5% power=0.25 resistance=100 package=THT]
  R13 = Resistor [tolerance=±5% power=0.25 resistance=100 package=THT]
  R14 = Resistor [tolerance=±5% power=0.25 resistance=100 package=THT]
  R15 = Resistor [tolerance=±5% power=0.25 resistance=100 package=THT]
  R16 = Resistor [tolerance=±5% power=0.25 resistance=100 package=THT]
  R17 = Resistor [tolerance=±5% power=0.25 resistance=100 package=THT]
  R18 = Resistor [tolerance=±5% power=0.25 resistance=100 package=THT]
  R19 = Resistor [tolerance=±5% power=0.25 resistance=100 package=THT]
  R20 = Resistor [tolerance=±5% power=0.25 resistance=100 package=THT]
  R21 = Resistor [tolerance=±5% power=0.25 resistance=100 package=THT]
  R22 = Resistor [tolerance=±5% power=0.25 resistance=100 package=THT]
  R23 = Resistor [tolerance=±5% power=0.25 resistance=100 package=THT]
  R24 = Resistor [tolerance=±5% power=0.25 resistance=100 package=THT]
  J1 = male pin header, 9 pins [form="♂ (male)"]
  J2 = male pin header, 9 pins [form="♂ (male)"]
  J3 = male pin header, 9 pins [form="♂ (male)"]
  U2 = TLP620-4 [package="DIP (Dual Inline) [THT]"]
  U3 = TLP620-4 [package="DIP (Dual Inline) [THT]"]
  U4 = TLP620-4 [package="DIP (Dual Inline) [THT]"]
  U5 = TLP620-4 [package="DIP (Dual Inline) [THT]"]
  J16 = male pin header, 1 pin [form="♂ (male)"]
  J17 = male pin header, 1 pin [form="♂ (male)"]
  J18 = male pin header, 1 pin [form="♂ (male)"]
  J19 = male pin header, 1 pin [form="♂ (male)"]
  J20 = male pin header, 1 pin [form="♂ (male)"]
  J21 = male pin header, 1 pin [form="♂ (male)"]
  J22 = male pin header, 1 pin [form="♂ (male)"]
  J23 = male pin header, 1 pin [form="♂ (male)"]
  J24 = male pin header, 1 pin [form="♂ (male)"]
  J25 = male pin header, 1 pin [form="♂ (male)"]
  J26 = male pin header, 1 pin [form="♂ (male)"]
  J27 = male pin header, 1 pin [form="♂ (male)"]
  U1 = TLP620-4 [package="DIP (Dual Inline) [THT]"]
  U6 = TLP620-4 [package="DIP (Dual Inline) [THT]"]
  J31 = male pin header, 1 pin [form="♂ (male)"]
  J32 = male pin header, 1 pin [form="♂ (male)"]
  J33 = male pin header, 1 pin [form="♂ (male)"]
  J34 = male pin header, 1 pin [form="♂ (male)"]
  J35 = male pin header, 1 pin [form="♂ (male)"]
  J36 = male pin header, 1 pin [form="♂ (male)"]
  J37 = male pin header, 1 pin [form="♂ (male)"]
  J38 = male pin header, 1 pin [form="♂ (male)"]
  U7 = PCF8574 [package="DIP16 [THT]"]
  U8 = PCF8574 [package="DIP16 [THT]"]
  J39 = male pin header, 4 pins [form="♂ (male)"]
  J40 = male pin header, 4 pins [form="♂ (male)"]
  R25 = Resistor [tolerance=±5% power=0.25 resistance=220 package=THT]
  R26 = Resistor [tolerance=±5% power=0.25 resistance=220 package=THT]
  U9 = PCF8574 [package="DIP16 [THT]"]
  J41 = male pin header, 1 pin [form="♂ (male)"]
  J42 = male pin header, 1 pin [form="♂ (male)"]
  J44 = male pin header, 1 pin [form="♂ (male)"]
  J45 = male pin header, 1 pin [form="♂ (male)"]
  J46 = male pin header, 1 pin [form="♂ (male)"]
  J47 = male pin header, 1 pin [form="♂ (male)"]
  J48 = male pin header, 1 pin [form="♂ (male)"]
  J49 = male pin header, 1 pin [form="♂ (male)"]
  J50 = male pin header, 1 pin [form="♂ (male)"]
  J51 = male pin header, 1 pin [form="♂ (male)"]
  J52 = male pin header, 1 pin [form="♂ (male)"]
  J53 = male pin header, 1 pin [form="♂ (male)"]
  J54 = male pin header, 1 pin [form="♂ (male)"]
  J55 = male pin header, 1 pin [form="♂ (male)"]
  J56 = male pin header, 1 pin [form="♂ (male)"]
  J57 = male pin header, 4 pins [form="♂ (male)"]
  J58 = male pin header, 4 pins [form="♂ (male)"]
  J59 = male pin header, 4 pins [form="♂ (male)"]
  J60 = male pin header, 4 pins [form="♂ (male)"]
  A00 = male pin header, 2 pins [form="♂ (male)"]
  A01 = male pin header, 2 pins [form="♂ (male)"]
  A02 = male pin header, 2 pins [form="♂ (male)"]
  J64 = male pin header, 2 pins [form="♂ (male)"]
  J65 = male pin header, 2 pins [form="♂ (male)"]
  J66 = male pin header, 2 pins [form="♂ (male)"]
  J67 = male pin header, 2 pins [form="♂ (male)"]
  J68 = male pin header, 2 pins [form="♂ (male)"]
  J69 = male pin header, 2 pins [form="♂ (male)"]
  R27 = Resistor [tolerance=±5% power=0.25 resistance=220 package=THT]
  J70 = male pin header, 1 pin [form="♂ (male)"]
  J71 = male pin header, 1 pin [form="♂ (male)"]
  J72 = male pin header, 1 pin [form="♂ (male)"]
  J73 = male pin header, 1 pin [form="♂ (male)"]
  J74 = male pin header, 1 pin [form="♂ (male)"]
  J75 = male pin header, 1 pin [form="♂ (male)"]
  J76 = male pin header, 1 pin [form="♂ (male)"]
  J77 = male pin header, 1 pin [form="♂ (male)"]
  J78 = male pin header, 1 pin [form="♂ (male)"]
  J79 = male pin header, 1 pin [form="♂ (male)"]
  J80 = male pin header, 1 pin [form="♂ (male)"]
  J81 = male pin header, 1 pin [form="♂ (male)"]
  J43 = male pin header, 1 pin [form="♂ (male)"]
  J82 = male pin header, 4 pins [form="♂ (male)"]

nets (from the breadboard view):
  N1: R1.Pin_0, J3.pin8
  N2: R1.Pin_1, J78.pin1
  N3: R2.Pin_0, J3.pin7
  N4: R2.Pin_1, U3.pin7
  N5: R3.Pin_0, J3.pin6
  N6: R3.Pin_1, J80.pin1
  N7: R4.Pin_0, J3.pin5
  N8: R4.Pin_1, U3.pin5
  N9: R5.Pin_0, J3.pin4
  N10: R5.Pin_1, J79.pin1
  N11: R6.Pin_0, J3.pin3
  N12: R6.Pin_1, U3.pin3
  N13: R7.Pin_0, J3.pin1
  N14: R7.Pin_1, U3.pin1
  N15: R8.Pin_0, J3.pin2
  N16: R8.Pin_1, J81.pin1
  N17: R9.Pin_0, J2.pin1
  N18: R9.Pin_1, U2.pin1
  N19: R10.Pin_0, J2.pin2
  N20: R10.Pin_1, J77.pin1
  N21: R11.Pin_0, J2.pin8
  N22: R11.Pin_1, J74.pin1
  N23: R12.Pin_0, J2.pin7
  N24: R12.Pin_1, U2.pin7
  N25: R13.Pin_0, J2.pin6
  N26: R13.Pin_1, J76.pin1
  N27: R14.Pin_0, J2.pin4
  N28: R14.Pin_1, J75.pin1
  N29: R15.Pin_0, J2.pin3
  N30: R15.Pin_1, U2.pin3
  N31: R16.Pin_0, J2.pin5
  N32: R16.Pin_1, U2.pin5
  N33: R17.Pin_0, J1.pin1
  N34: R17.Pin_1, U1.pin1
  N35: R18.Pin_0, J1.pin2
  N36: R18.Pin_1, J71.pin1
  N37: R19.Pin_0, J1.pin8
  N38: R19.Pin_1, J70.pin1
  N39: R20.Pin_0, J1.pin7
  N40: R20.Pin_1, U1.pin7
  N41: R21.Pin_0, J1.pin6
  N42: R21.Pin_1, J73.pin1
  N43: R22.Pin_0, J1.pin4
  N44: R22.Pin_1, J72.pin1
  N45: R23.Pin_0, J1.pin3
  N46: R23.Pin_1, U1.pin3
  N47: R24.Pin_0, J1.pin5
  N48: R24.Pin_1, U1.pin5
  N49: J1.pin9, J2.pin9, J3.pin9, U3.pin2, U3.pin4, U3.pin6, U3.pin8, U4.pin2, U4.pin4, U4.pin6, U4.pin8, U5.pin2, U5.pin4, U5.pin6, U5.pin8, U1.pin2, U1.pin4, U1.pin6, U1.pin8, U6.pin2, U6.pin4, U6.pin6, U6.pin8
  N50: U2.pin2, U2.pin4, U2.pin6, U2.pin8
  GND: U2.pin9, U2.pin11, U2.pin13, U2.pin15, U3.pin9, U3.pin11, U3.pin13, U3.pin15, U4.pin9, U4.pin11, U4.pin13, U4.pin15, U5.pin9, U5.pin11, U5.pin13, U5.pin15, U1.pin9, U1.pin11, U1.pin13, U1.pin15, U6.pin9, U6.pin11, U6.pin13, U6.pin15, U7.GND, U8.GND, U9.GND, A00.pin1, A01.pin1, A02.pin1, J64.pin1, J65.pin1, J66.pin1, J67.pin1, J68.pin1, J69.pin1, J82.pin1
  N51: U2.pin10, J21.pin1
  N52: U2.pin12, J20.pin1
  N53: U2.pin14, J22.pin1
  N54: U2.pin16, J23.pin1
  N55: U3.pin10, J25.pin1
  N56: U3.pin12, J24.pin1
  N57: U3.pin14, J26.pin1
  N58: U3.pin16, J27.pin1
  N59: U4.pin1, J46.pin1
  N60: U4.pin3, J45.pin1
  N61: U4.pin5, J48.pin1
  N62: U4.pin7, J47.pin1
  N63: U4.pin10, J55.pin1
  N64: U4.pin12, J56.pin1
  N65: U4.pin14, J53.pin1
  N66: U4.pin16, J54.pin1
  N67: U5.pin1, J42.pin1
  N68: U5.pin3, J41.pin1
  N69: U5.pin5, J44.pin1
  N70: U5.pin7, J43.pin1
  N71: U5.pin10, J51.pin1
  N72: U5.pin12, J52.pin1
  N73: U5.pin14, J49.pin1
  N74: U5.pin16, J50.pin1
  N75: J16.pin1, U1.pin12
  N76: J17.pin1, U1.pin10
  N77: J18.pin1, U1.pin14
  N78: J19.pin1, U1.pin16
  N79: U6.pin1, J31.pin1
  N80: U6.pin3, J32.pin1
  N81: U6.pin5, J33.pin1
  N82: U6.pin7, J34.pin1
  N83: U6.pin10, J37.pin1
  N84: U6.pin12, J38.pin1
  N85: U6.pin14, J36.pin1
  N86: U6.pin16, J35.pin1
  N87: U7.A0, A00.pin2
  N88: U7.A1, A01.pin2
  N89: U7.A2, A02.pin2
  N90: U7.P0, J39.pin1
  N91: U7.P1, J39.pin2
  N92: U7.P2, J39.pin3
  N93: U7.P3, J39.pin4
  N94: U7.P4, J40.pin4
  N95: U7.P5, J40.pin3
  N96: U7.P6, J40.pin2
  N97: U7.P7, J40.pin1
  N98: U7.SCL, U8.SCL, U9.SCL, J82.pin3
  N99: U7.SDA, U8.SDA, U9.SDA, J82.pin2
  VCC: U7.VCC, U8.VCC, R25.Pin_0, R26.Pin_0, U9.VCC, R27.Pin_0, J82.pin4
  N100: U8.A0, J64.pin2
  N101: U8.A1, J65.pin2
  N102: U8.A2, J66.pin2
  N103: U8.P0, J57.pin1
  N104: U8.P1, J57.pin2
  N105: U8.P2, J57.pin3
  N106: U8.P3, J57.pin4
  N107: U8.P4, J58.pin4
  N108: U8.P5, J58.pin3
  N109: U8.P6, J58.pin2
  N110: U8.P7, J58.pin1
  N111: U9.A0, J67.pin2
  N112: U9.A1, J68.pin2
  N113: U9.A2, J69.pin2
  N114: U9.P0, J59.pin1
  N115: U9.P1, J59.pin2
  N116: U9.P2, J59.pin3
  N117: U9.P3, J59.pin4
  N118: U9.P4, J60.pin4
  N119: U9.P5, J60.pin3
  N120: U9.P6, J60.pin2
  N121: U9.P7, J60.pin1

custom parts:
  TLP620-4: Quad Photo-transistor optically coupled to two infrared emitting diodes connected in inverse parallel.
