# Fritzing sketch Cpu (saved by Fritzing 0.9.6b)
stripboards: 1

parts:
  M1 = DOIT Esp32 DevKit v1 (30 pins long, 11 pins width) [part_number=ESP32S-PIN30]
  J1 = male pin header, 4 pins [form="♂ (male)"]
  J2 = male pin header, 4 pins [form="♂ (male)"]
  J3 = male pin header, 4 pins [form="♂ (male)"]
  J4 = male pin header, 4 pins [form="♂ (male)"]
  J5 = male pin header, 4 pins [form="♂ (male)"]
  J6 = male pin header, 4 pins [form="♂ (male)"]
  J7 = male pin header, 4 pins [form="♂ (male)"]
  J8 = male pin header, 4 pins [form="♂ (male)"]
  J9 = male pin header, 13 pins [form="♂ (male)"]
  J10 = male pin header, 13 pins [form="♂ (male)"]
  J11 = male pin header, 13 pins [form="♂ (male)"]
  J12 = male pin header, 13 pins [form="♂ (male)"]
  J13 = female pin header, 8 pins [form="♀ (female)"]
  J14 = female pin header, 8 pins [form="♀ (female)"]
  J15 = male pin header, 8 pins [form="♂ (male)"]
  J16 = male pin header, 8 pins [form="♂ (male)"]
  J17 = female pin header, 15 pins [form="♀ (female)"]
  J18 = female pin header, 15 pins [form="♀ (female)"]
  DFRobot_DFPlayer_Mini1 = DFRobot DFPlayer Mini [part_number=DFR0299]
  J22 = male pin header, 4 pins [form="♂ (male)"]
  J23 = male pin header, 4 pins [form="♂ (male)"]
  J24 = male pin header, 4 pins [form="♂ (male)"]
  U1 = PCF8574 [package="DIP16 [THT]"]
  J20 = female pin header, 8 pins [form="♀ (female)"]
  J19 = female pin header, 8 pins [form="♀ (female)"]
  J28 = female pin header, 8 pins [form="♀ (female)"]
  J29 = female pin header, 8 pins [form="♀ (female)"]
  U2 = PCF8574 [package="DIP16 [THT]"]
  SPKR1 = Loudspeaker
  J33 = male pin header, 2 pins [form="♂ (male)"]
  J26 = male pin header, 2 pins [form="♂ (male)"]

nets:
  3.3V: M1.3V3, J2.pin1, J2.pin2, J2.pin3, J2.pin4, J6.pin1, J6.pin2, J6.pin3, J6.pin4, J17.pin1, U1.VCC, J19.pin1, J28.pin1, J29.pin1, U2.A0, U2.VCC
  GND: M1.GND, J1.pin1, J1.pin2, J1.pin3, J1.pin4, J3.pin1, J3.pin2, J3.pin3, J3.pin4, J5.pin1, J5.pin2, J5.pin3, J5.pin4, J7.pin1, J7.pin2, J7.pin3, J7.pin4, J13.pin7, J14.pin7, J15.pin7, J16.pin7, J17.pin2, J18.pin2, DFRobot_DFPlayer_Mini1.GND-1, DFRobot_DFPlayer_Mini1.GND-2, U1.A0, U1.A1, U1.A2, U1.GND, J20.pin1, J20.pin2, J20.pin3, J20.pin8, J28.pin2, J28.pin3, J28.pin8, U2.A1, U2.A2, U2.GND, J33.pin1
  N1: M1.D15, J9.pin1, J10.pin1, J17.pin3
  N2: M1.D2, J9.pin2, J10.pin2, J17.pin4
  N3: M1.D4, J9.pin3, J10.pin3, J17.pin5
  N4: M1.RX2, J9.pin4, J10.pin4, J14.pin3, J16.pin3, J17.pin6, DFRobot_DFPlayer_Mini1.TX
  N5: M1.TX2, J9.pin5, J10.pin5, J14.pin2, J16.pin2, J17.pin7, DFRobot_DFPlayer_Mini1.RX
  N6: M1.D5, J9.pin6, J10.pin6, J17.pin8
  N7: M1.D18, J9.pin7, J10.pin7, J17.pin9
  N8: M1.D19, J9.pin8, J10.pin8, J17.pin10
  N9: M1.D21, J9.pin9, J10.pin9, J17.pin11, U1.SDA, J19.pin2, J29.pin2, U2.SDA, J26.pin1
  N10: M1.RX0, J9.pin10, J10.pin10, J17.pin12
  N11: M1.TX0, J9.pin11, J10.pin11, J17.pin13
  N12: M1.D22, J9.pin12, J10.pin12, J17.pin14, U1.SCL, J19.pin3, J29.pin3, U2.SCL, J26.pin2
  N13: M1.D23, J9.pin13, J10.pin13, J17.pin15
  N14: M1.EN, J11.pin13, J12.pin13, J18.pin15
  N15: M1.VP, J11.pin12, J12.pin12, J18.pin14
  N16: M1.VN, J11.pin11, J12.pin11, J18.pin13
  N17: M1.D34, J11.pin10, J12.pin10, J18.pin12
  N18: M1.D35, J11.pin9, J12.pin9, J18.pin11
  N19: M1.D32, J11.pin8, J12.pin8, J18.pin10
  N20: M1.D33, J11.pin7, J12.pin7, J18.pin9
  N21: M1.D25, J11.pin6, J12.pin6, J18.pin8
  N22: M1.D26, J11.pin5, J12.pin5, J18.pin7
  N23: M1.D27, J11.pin4, J12.pin4, J18.pin6
  N24: M1.D14, J11.pin3, J12.pin3, J18.pin5
  N25: M1.D12, J11.pin2, J12.pin2, J18.pin4
  N26: M1.D13, J11.pin1, J12.pin1, J18.pin3
  5V: M1.VIN, J4.pin1, J4.pin2, J4.pin3, J4.pin4, J8.pin1, J8.pin2, J8.pin3, J8.pin4, J18.pin1
  N27: J13.pin1, J15.pin1, DFRobot_DFPlayer_Mini1.BUSY
  N28: J13.pin2, J15.pin2, DFRobot_DFPlayer_Mini1.USB_NEG
  N29: J13.pin3, J15.pin3, DFRobot_DFPlayer_Mini1.USB_POS
  N30: J13.pin4, J15.pin4, DFRobot_DFPlayer_Mini1.ADKEY_2
  N31: J13.pin5, J15.pin5, DFRobot_DFPlayer_Mini1.ADKEY_1
  N32: J13.pin6, J15.pin6, DFRobot_DFPlayer_Mini1.IO_2
  N33: J13.pin8, J15.pin8, DFRobot_DFPlayer_Mini1.IO_1
  5.5V: J14.pin1, J16.pin1, DFRobot_DFPlayer_Mini1.VCC, J33.pin2
  N34: J14.pin4, J16.pin4, DFRobot_DFPlayer_Mini1.DAC_R
  N35: J14.pin5, J16.pin5, DFRobot_DFPlayer_Mini1.DAC_L
  N36: J14.pin6, J16.pin6, DFRobot_DFPlayer_Mini1.SPK_1, SPKR1.pin2
  N37: J14.pin8, J16.pin8, DFRobot_DFPlayer_Mini1.SPK_2, SPKR1.pin1
  N38: J22.pin1, U1.P0, J20.pin4
  N39: J22.pin2, U1.P1, J20.pin5
  N40: J22.pin3, U1.P2, J20.pin6
  N41: J22.pin4, U1.P3, J20.pin7
  N42: J23.pin1, J28.pin4, U2.P0
  N43: J23.pin2, J28.pin5, U2.P1
  N44: J23.pin3, J28.pin6, U2.P2
  N45: J23.pin4, J28.pin7, U2.P3
  N46: J24.pin1, J29.pin5, U2.P7
  N47: J24.pin2, J29.pin6, U2.P6
  N48: J24.pin3, J29.pin7, U2.P5
  N49: J24.pin4, J29.pin8, U2.P4
  N50: U1.P4, J19.pin8
  N51: U1.P5, J19.pin7
  N52: U1.P6, J19.pin6
  N53: U1.P7, J19.pin5
  N54: U1.INT, J19.pin4
  N55: J29.pin4, U2.INT

custom parts:
  DOIT Esp32 DevKit v1 (30 pins long, 11 pins width): The DOIT Esp32 DevKit v1 is one of the development board created by DOIT to evaluate the ESP-WROOM-32 module. It is based on the ESP32 microcontroller that boasts Wifi, Bluetooth, Ethernet and Low Power support all in a single chip. (vanepp) made breadboard work, adjusted pin numbering and labels and reduced size of schematic and cleaned up pcb. This chip is 30pins long (2 x15) and 11 pins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
