# Fritzing sketch Spor_Interface_Marklin (saved by Fritzing 0.9.6b)
circuit board: 7.0995cm x 9.88134cm
stripboards: 1

parts:
  U03 = Sharp PC817 [package=THT]
  U02 = Sharp PC817 [package=THT]
  U01 = Sharp PC817 [package=THT]
  U00 = Sharp PC817 [package=THT]
  U04 = Sharp PC817 [package=THT]
  U07 = Sharp PC817 [package=THT]
  U06 = Sharp PC817 [package=THT]
  U05 = Sharp PC817 [package=THT]
  LD8 = smd LED [color="Red (633nm)" current=0.030 package="0805 [SMD]"]
  U10 = Sharp PC817 [package=THT]
  U11 = Sharp PC817 [package=THT]
  U12 = Sharp PC817 [package=THT]
  U13 = Sharp PC817 [package=THT]
  U14 = Sharp PC817 [package=THT]
  U15 = Sharp PC817 [package=THT]
  U16 = Sharp PC817 [package=THT]
  U17 = Sharp PC817 [package=THT]
  R9 = Resistor [tolerance=±5% resistance=100 power=0.25 package="0805 [SMD]"]
  R10 = Resistor [tolerance=±5% resistance=100 power=0.25 package="0805 [SMD]"]
  R11 = Resistor [tolerance=±5% resistance=100 power=0.25 package="0805 [SMD]"]
  R12 = Resistor [tolerance=±5% resistance=100 power=0.25 package="0805 [SMD]"]
  R13 = Resistor [tolerance=±5% resistance=100 power=0.25 package="0805 [SMD]"]
  R14 = Resistor [tolerance=±5% resistance=100 power=0.25 package="0805 [SMD]"]
  R15 = Resistor [tolerance=±5% resistance=100 power=0.25 package="0805 [SMD]"]
  R16 = Resistor [tolerance=±5% resistance=100 power=0.25 package="0805 [SMD]"]
  U2 = PCF8574 [package="DIP16 [THT]"]
  R7 = Resistor [tolerance=±5% resistance=100 power=0.25 package="0805 [SMD]"]
  R8 = Resistor [tolerance=±5% resistance=100 power=0.25 package="0805 [SMD]"]
  R5 = Resistor [tolerance=±5% resistance=100 power=0.25 package="0805 [SMD]"]
  LD6 = smd LED [color="Blue (470nm)" current=0.030 package="0805 [SMD]"]
  LD5 = smd LED [color="Yellow (592nm)" current=0.030 package="0805 [SMD]"]
  LED7 = smd LED [color="Green (560nm)" current=0.030 package="0805 [SMD]"]
  M1 = DOIT Esp32 DevKit v1 (30 pins long, 11 pins width) [part_number=ESP32S-PIN30]
  R3 = Resistor [tolerance=±5% resistance=100 power=0.25 package="0805 [SMD]"]
  LED3 = smd LED [color="Red (633nm)" current=0.030 package="0805 [SMD]"]
  LED2 = smd LED [color="Blue (470nm)" current=0.030 package="0805 [SMD]"]
  LED1 = smd LED [color="Yellow (592nm)" current=0.030 package="0805 [SMD]"]
  LED0 = smd LED [color="Green (560nm)" current=0.030 package="0805 [SMD]"]
  R2 = Resistor [tolerance=±5% resistance=100 power=0.25 package="0805 [SMD]"]
  R1 = Resistor [tolerance=±5% resistance=100 power=0.25 package="0805 [SMD]"]
  R0 = Resistor [tolerance=±5% resistance=100 power=0.25 package="0805 [SMD]"]
  R6 = Resistor [tolerance=±5% resistance=100 power=0.25 package="0805 [SMD]"]
  LD9 = smd LED [color="Green (560nm)" current=0.030 package="0805 [SMD]"]
  LD10 = smd LED [color="Yellow (592nm)" current=0.030 package="0805 [SMD]"]
  LD11 = smd LED [color="Blue (470nm)" current=0.030 package="0805 [SMD]"]
  LD12 = smd LED [color="Red (633nm)" current=0.030 package="0805 [SMD]"]
  LED13 = smd LED [color="Green (560nm)" current=0.030 package="0805 [SMD]"]
  LED14 = smd LED [color="Yellow (592nm)" current=0.030 package="0805 [SMD]"]
  LED15 = smd LED [color="Blue (470nm)" current=0.030 package="0805 [SMD]"]
  LED16 = smd LED [color="Red (633nm)" current=0.030 package="0805 [SMD]"]
  U1 = PCF8574 [package="DIP16 [THT]"]
  J27 = male pin header, 3 pins [form="♂ (male)"]
  DFRobot_DFPlayer_Mini1 = DFRobot DFPlayer Mini [part_number=DFR0299]
  J28 = male pin header, 8 pins [form="♂ (male)"]
  J29 = male pin header, 8 pins [form="♂ (male)"]
  U18 = V_REG_LD1117VXX [package=78xxl]
  J30 = male pin header, 4 pins [form="♂ (male)"]
  J31 = male pin header, 4 pins [form="♂ (male)"]
  J32 = male pin header, 4 pins [form="♂ (male)"]
  J33 = male pin header, 4 pins [form="♂ (male)"]
  SPKR1 = Loudspeaker
  J34 = Camdenboss CTB0158-5 [part_number=CTB0158-5 package=THT]
  J35 = Camdenboss CTB0158-5 [part_number=CTB0158-5 package=THT]
  J36 = Camdenboss CTB0158-5 [part_number=CTB0158-5 package=THT]
  J37 = Camdenboss CTB0158-5 [part_number=CTB0158-5 package=THT]

nets:
  N1: U03.Pin_1, LED3.cathode
  N2: U03.Pin_2, R3.Pin_0
  P00: U03.Pin_4, U1.P0, J31.pin1
  GND: U03.Pin_3, U02.Pin_3, U01.Pin_3, U00.Pin_3, U04.Pin_3, U07.Pin_3, U06.Pin_3, U05.Pin_3, U10.Pin_3, U11.Pin_3, U12.Pin_3, U13.Pin_3, U14.Pin_3, U15.Pin_3, U16.Pin_3, U17.Pin_3, U2.A1, U2.A2, U2.GND, M1.GND, U1.A0, U1.A1, U1.A2, U1.GND, J27.pin2, DFRobot_DFPlayer_Mini1.GND-1, DFRobot_DFPlayer_Mini1.GND-2, J28.pin7, J29.pin7, U18.GND
  N3: U02.Pin_1, LED2.cathode
  N4: U02.Pin_2, R2.Pin_0
  P01: U02.Pin_4, U1.P1, J31.pin2
  N5: U01.Pin_1, LED1.cathode
  N6: U01.Pin_2, R1.Pin_0
  P02: U01.Pin_4, U1.P2, J31.pin3
  N7: U00.Pin_1, LED0.cathode
  N8: U00.Pin_2, R0.Pin_0
  P03: U00.Pin_4, U1.P3, J31.pin4
  N9: U04.Pin_1, LED7.cathode
  N10: U04.Pin_2, R5.Pin_0
  P13: U04.Pin_4, U2.P3, J33.pin4
  N11: U07.Pin_1, LD8.cathode
  N12: U07.Pin_2, R6.Pin_0
  P10: U07.Pin_4, U2.P0, J33.pin1
  N13: U06.Pin_1, LD6.cathode
  N14: U06.Pin_2, R7.Pin_0
  P11: U06.Pin_4, U2.P1, J33.pin2
  N15: U05.Pin_1, LD5.cathode
  N16: U05.Pin_2, R8.Pin_0
  P12: U05.Pin_4, U2.P2, J33.pin3
  N17: LD8.anode, LD6.anode, LD5.anode, LED7.anode, J35.pin5
  N18: U10.Pin_1, LD9.cathode
  N19: U10.Pin_2, R13.Pin_0
  P04: U10.Pin_4, U1.P4, J30.pin4
  N20: U11.Pin_1, LD10.cathode
  N21: U11.Pin_2, R14.Pin_0
  P05: U11.Pin_4, U1.P5, J30.pin3
  N22: U12.Pin_1, LD11.cathode
  N23: U12.Pin_2, R15.Pin_0
  P06: U12.Pin_4, U1.P6, J30.pin2
  N24: U13.Pin_1, LD12.cathode
  N25: U13.Pin_2, R16.Pin_0
  P07: U13.Pin_4, U1.P7, J30.pin1
  N26: U14.Pin_1, LED16.cathode
  N27: U14.Pin_2, R9.Pin_0
  P14: U14.Pin_4, U2.P4, J32.pin4
  N28: U15.Pin_1, LED15.cathode
  N29: U15.Pin_2, R10.Pin_0
  P15: U15.Pin_4, U2.P5, J32.pin3
  N30: U16.Pin_1, LED14.cathode
  N31: U16.Pin_2, R11.Pin_0
  P16: U16.Pin_4, U2.P6, J32.pin2
  N32: U17.Pin_1, LED13.cathode
  N33: U17.Pin_2, R12.Pin_0
  P17: U17.Pin_4, U2.P7, J32.pin1
  N34: R9.Pin_1, J37.pin4
  N35: R10.Pin_1, J37.pin3
  N36: R11.Pin_1, J37.pin2
  N37: R12.Pin_1, J37.pin1
  N38: R13.Pin_1, J34.pin1
  N39: R14.Pin_1, J34.pin2
  N40: R15.Pin_1, J34.pin3
  N41: R16.Pin_1, J34.pin4
  3.3V: U2.A0, U2.VCC, M1.3V3, U1.VCC, J27.pin3
  I2C-SCL: U2.SCL, M1.D22, U1.SCL
  I2C-SDA: U2.SDA, M1.D21, U1.SDA
  N42: R7.Pin_1, J35.pin3
  N43: R8.Pin_1, J35.pin2
  N44: R5.Pin_1, J35.pin1
  cpu-tx: M1.RX2, DFRobot_DFPlayer_Mini1.RX, J28.pin2
  cpu-rx: M1.TX2, DFRobot_DFPlayer_Mini1.TX, J28.pin3
  5V: M1.VIN, J27.pin1, U18.IN
  N45: R3.Pin_1, J36.pin4
  N46: LED3.anode, LED2.anode, LED1.anode, LED0.anode, J36.pin5
  N47: R2.Pin_1, J36.pin3
  N48: R1.Pin_1, J36.pin2
  N49: R0.Pin_1, J36.pin1
  N50: R6.Pin_1, J35.pin4
  N51: LD9.anode, LD10.anode, LD11.anode, LD12.anode, J34.pin5
  N52: LED13.anode, LED14.anode, LED15.anode, LED16.anode, J37.pin5
  N53: DFRobot_DFPlayer_Mini1.VCC, J28.pin1, U18.OUT
  N54: DFRobot_DFPlayer_Mini1.DAC_R, J28.pin4
  N55: DFRobot_DFPlayer_Mini1.DAC_L, J28.pin5
  N56: DFRobot_DFPlayer_Mini1.SPK_1, J28.pin6, SPKR1.pin1
  N57: DFRobot_DFPlayer_Mini1.SPK_2, J28.pin8, SPKR1.pin2
  N58: DFRobot_DFPlayer_Mini1.IO_1, J29.pin8
  N59: DFRobot_DFPlayer_Mini1.IO_2, J29.pin6
  N60: DFRobot_DFPlayer_Mini1.ADKEY_1, J29.pin5
  N61: DFRobot_DFPlayer_Mini1.ADKEY_2, J29.pin4
  N62: DFRobot_DFPlayer_Mini1.USB_POS, J29.pin3
  N63: DFRobot_DFPlayer_Mini1.USB_NEG, J29.pin2
  N64: DFRobot_DFPlayer_Mini1.BUSY, J29.pin1

notes:
  Ext. Power

custom parts:
  DOIT Esp32 DevKit v1 (30 pins long, 11 pins width): The DOIT Esp32 DevKit v1 is one of the development board created by DOIT to evaluate the ESP-WROOM-32 module. It is based on the ESP32 microcontroller that boasts Wifi, Bluetooth, Ethernet and Low Power support all in a single chip. (vanepp) made breadboard work, adjusted pin numbering and labels and reduced size of schematic and cleaned up pcb. This chip is 30pins long (2 x15) and 11 pins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
