# Fritzing sketch PCB-LedDriver-V6.1 (saved by Fritzing 0.9.6b)
circuit board: 22.3cm x 5.86cm

parts:
  IC1 = PCF8574 [package="DIP16 [THT]"]
  IC2 = PCF8574 [package="DIP16 [THT]"]
  IC3 = PCF8574 [package="DIP16 [THT]"]
  IC4 = PCF8574 [package="DIP16 [THT]"]
  U1 = Sharp PC847X [package=THT]
  R3 = Resistor [tolerance=±5% power=0.25 resistance=330 package=THT]
  R1 = Resistor [tolerance=±5% power=0.25 resistance=330 package=THT]
  R36 = Resistor [tolerance=±5% power=0.25 resistance=100 package=THT]
  R34 = Resistor [tolerance=±5% power=0.25 resistance=100 package=THT]
  R35 = Resistor [tolerance=±5% power=0.25 resistance=100 package=THT]
  R33 = Resistor [tolerance=±5% power=0.25 resistance=100 package=THT]
  U2 = Sharp PC847X [package=THT]
  R68 = Resistor [tolerance=±5% power=0.25 resistance=100 package=THT]
  R67 = Resistor [tolerance=±5% power=0.25 resistance=100 package=THT]
  R66 = Resistor [tolerance=±5% power=0.25 resistance=100 package=THT]
  R65 = Resistor [tolerance=±5% power=0.25 resistance=100 package=THT]
  R100 = Resistor [tolerance=±5% power=0.25 resistance=330 package=THT]
  R99 = Resistor [tolerance=±5% power=0.25 resistance=330 package=THT]
  R98 = Resistor [tolerance=±5% power=0.25 resistance=330 package=THT]
  R97 = Resistor [tolerance=±5% power=0.25 resistance=330 package=THT]
  U4 = Sharp PC847X [package=THT]
  R104 = Resistor [tolerance=±5% power=0.25 resistance=330 package=THT]
  R103 = Resistor [tolerance=±5% power=0.25 resistance=330 package=THT]
  R102 = Resistor [tolerance=±5% power=0.25 resistance=330 package=THT]
  R101 = Resistor [tolerance=±5% power=0.25 resistance=330 package=THT]
  U3 = Sharp PC847X [package=THT]
  R8 = Resistor [tolerance=±5% power=0.25 resistance=330 package=THT]
  R7 = Resistor [tolerance=±5% power=0.25 resistance=330 package=THT]
  R6 = Resistor [tolerance=±5% power=0.25 resistance=330 package=THT]
  R5 = Resistor [tolerance=±5% power=0.25 resistance=330 package=THT]
  R40 = Resistor [tolerance=±5% power=0.25 resistance=100 package=THT]
  R39 = Resistor [tolerance=±5% power=0.25 resistance=100 package=THT]
  R38 = Resistor [tolerance=±5% power=0.25 resistance=100 package=THT]
  R37 = Resistor [tolerance=±5% power=0.25 resistance=100 package=THT]
  R69 = Resistor [tolerance=±5% power=0.25 resistance=100 package=THT]
  R70 = Resistor [tolerance=±5% power=0.25 resistance=100 package=THT]
  R71 = Resistor [tolerance=±5% power=0.25 resistance=100 package=THT]
  R72 = Resistor [tolerance=±5% power=0.25 resistance=100 package=THT]
  U7 = Sharp PC847X [package=THT]
  U5 = Sharp PC847X [package=THT]
  R9 = Resistor [tolerance=±5% power=0.25 resistance=330 package=THT]
  R10 = Resistor [tolerance=±5% power=0.25 resistance=330 package=THT]
  R11 = Resistor [tolerance=±5% power=0.25 resistance=330 package=THT]
  R12 = Resistor [tolerance=±5% power=0.25 resistance=330 package=THT]
  R41 = Resistor [tolerance=±5% power=0.25 resistance=100 package=THT]
  R42 = Resistor [tolerance=±5% power=0.25 resistance=100 package=THT]
  R43 = Resistor [tolerance=±5% power=0.25 resistance=100 package=THT]
  R44 = Resistor [tolerance=±5% power=0.25 resistance=100 package=THT]
  R45 = Resistor [tolerance=±5% power=0.25 resistance=100 package=THT]
  R46 = Resistor [tolerance=±5% power=0.25 resistance=100 package=THT]
  R48 = Resistor [tolerance=±5% power=0.25 resistance=100 package=THT]
  R76 = Resistor [tolerance=±5% power=0.25 resistance=100 package=THT]
  R75 = Resistor [tolerance=±5% power=0.25 resistance=100 package=THT]
  R74 = Resistor [tolerance=±5% power=0.25 resistance=100 package=THT]
  R73 = Resistor [tolerance=±5% power=0.25 resistance=100 package=THT]
  R80 = Resistor [tolerance=±5% power=0.25 resistance=100 package=THT]
  R79 = Resistor [tolerance=±5% power=0.25 resistance=100 package=THT]
  R78 = Resistor [tolerance=±5% power=0.25 resistance=100 package=THT]
  R77 = Resistor [tolerance=±5% power=0.25 resistance=100 package=THT]
  U6 = Sharp PC847X [package=THT]
  U8 = Sharp PC847X [package=THT]
  R105 = Resistor [tolerance=±5% power=0.25 resistance=330 package=THT]
  R106 = Resistor [tolerance=±5% power=0.25 resistance=330 package=THT]
  R107 = Resistor [tolerance=±5% power=0.25 resistance=330 package=THT]
  R108 = Resistor [tolerance=±5% power=0.25 resistance=330 package=THT]
  R109 = Resistor [tolerance=±5% power=0.25 resistance=330 package=THT]
  R110 = Resistor [tolerance=±5% power=0.25 resistance=330 package=THT]
  R111 = Resistor [tolerance=±5% power=0.25 resistance=330 package=THT]
  R112 = Resistor [tolerance=±5% power=0.25 resistance=330 package=THT]
  J1 = male pin header, 8 pins [form="♂ (male)"]
  J5 = male pin header, 8 pins [form="♂ (male)"]
  J7 = male pin header, 8 pins [form="♂ (male)"]
  R13 = Resistor [tolerance=±5% power=0.25 resistance=330 package=THT]
  R14 = Resistor [tolerance=±5% power=0.25 resistance=330 package=THT]
  R16 = Resistor [tolerance=±5% power=0.25 resistance=330 package=THT]
  R15 = Resistor [tolerance=±5% power=0.25 resistance=330 package=THT]
  J8 = male pin header, 8 pins [form="♂ (male)"]
  J6 = male pin header, 8 pins [form="♂ (male)"]
  J4 = male pin header, 8 pins [form="♂ (male)"]
  J2 = male pin header, 8 pins [form="♂ (male)"]
  J3 = male pin header, 8 pins [form="♂ (male)"]
  R4 = Resistor [tolerance=±5% power=0.25 resistance=330 package=THT]
  R2 = Resistor [tolerance=±5% power=0.25 resistance=330 package=THT]
  R47 = Resistor [tolerance=±5% power=0.25 resistance=100 package=THT]
  Pad1 = Pad [width=3 height=2 connect=center]
  Pad2 = Pad [width=3 height=2 connect=center]
  Pad3 = Pad [width=3 height=2 connect=center]
  Pad4 = Pad [width=3 height=2 connect=center]
  Pad5 = Pad [width=3 height=2 connect=center]
  Pad6 = Pad [width=3 height=2 connect=center]
  Pad7 = Pad [width=3 height=2 connect=center]
  Pad8 = Pad [width=3 height=2 connect=center]
  Pad9 = Pad [width=3 height=2 connect=center]
  Pad10 = Pad [width=3 height=2 connect=center]
  Pad11 = Pad [width=3 height=2 connect=center]
  Pad12 = Pad [width=3 height=2 connect=center]
  Pad13 = Pad [width=3 height=2 connect=center]
  Pad14 = Pad [width=3 height=2 connect=center]
  Pad15 = Pad [width=3 height=2 connect=center]
  Pad16 = Pad [width=3 height=2 connect=center]
  Pad17 = Pad [width=3 height=2 connect=center]
  Pad18 = Pad [width=3 height=2 connect=center]
  Pad19 = Pad [width=3 height=2 connect=center]
  Pad20 = Pad [width=3 height=2 connect=center]
  Pad21 = Pad [width=3 height=2 connect=center]
  Pad22 = Pad [width=3 height=2 connect=center]
  Pad23 = Pad [width=3 height=2 connect=center]
  Pad24 = Pad [width=3 height=2 connect=center]
  Pad25 = Pad [width=3 height=2 connect=center]
  Pad26 = Pad [width=3 height=2 connect=center]
  Pad27 = Pad [width=3 height=2 connect=center]
  Pad28 = Pad [width=3 height=2 connect=center]
  Pad29 = Pad [width=3 height=2 connect=center]
  Pad30 = Pad [width=3 height=2 connect=center]
  Pad31 = Pad [width=3 height=2 connect=center]
  Pad32 = Pad [width=3 height=2 connect=center]
  Pad33 = Pad [width=3 height=2 connect=center]
  Pad34 = Pad [width=3 height=2 connect=center]
  Pad35 = Pad [width=3 height=2 connect=center]
  Pad36 = Pad [width=3 height=2 connect=center]
  Pad37 = Pad [width=3 height=2 connect=center]
  Pad38 = Pad [width=3 height=2 connect=center]
  Pad39 = Pad [width=3 height=2 connect=center]
  Pad40 = Pad [width=3 height=2 connect=center]
  Pad41 = Pad [width=3 height=2 connect=center]
  Pad42 = Pad [width=3 height=2 connect=center]
  Pad43 = Pad [width=3 height=2 connect=center]
  Pad44 = Pad [width=3 height=2 connect=center]
  Pad45 = Pad [width=3 height=2 connect=center]
  Pad46 = Pad [width=3 height=2 connect=center]
  Pad47 = Pad [width=3 height=2 connect=center]
  Pad48 = Pad [width=3 height=2 connect=center]
  Pad49 = Pad [width=3 height=2 connect=center]
  Pad50 = Pad [width=3 height=2 connect=center]
  Pad51 = Pad [width=3 height=2 connect=center]
  Pad52 = Pad [width=3 height=2 connect=center]
  Pad53 = Pad [width=3 height=2 connect=center]
  Pad54 = Pad [width=3 height=2 connect=center]
  Pad55 = Pad [width=3 height=2 connect=center]
  Pad56 = Pad [width=3 height=2 connect=center]
  Pad57 = Pad [width=3 height=2 connect=center]
  Pad58 = Pad [width=3 height=2 connect=center]
  Pad59 = Pad [width=3 height=2 connect=center]
  Pad60 = Pad [width=3 height=2 connect=center]
  Pad61 = Pad [width=3 height=2 connect=center]
  Pad62 = Pad [width=3 height=2 connect=center]
  Pad63 = Pad [width=3 height=2 connect=center]
  Pad64 = Pad [width=3 height=2 connect=center]
  IC5 = PCF8574 [package="DIP16 [THT]"]
  IC6 = PCF8574 [package="DIP16 [THT]"]
  IC7 = PCF8574 [package="DIP16 [THT]"]
  IC8 = PCF8574 [package="DIP16 [THT]"]
  U10 = Sharp PC847X [package=THT]
  U12 = Sharp PC847X [package=THT]
  U14 = Sharp PC847X [package=THT]
  U16 = Sharp PC847X [package=THT]
  U9 = Sharp PC847X [package=THT]
  U11 = Sharp PC847X [package=THT]
  U13 = Sharp PC847X [package=THT]
  U15 = Sharp PC847X [package=THT]
  J9 = male pin header, 8 pins [form="♂ (male)"]
  J11 = male pin header, 8 pins [form="♂ (male)"]
  J13 = male pin header, 8 pins [form="♂ (male)"]
  J15 = male pin header, 8 pins [form="♂ (male)"]
  R17 = Resistor [tolerance=±5% power=0.25 resistance=330 package=THT]
  R18 = Resistor [tolerance=±5% power=0.25 resistance=330 package=THT]
  R19 = Resistor [tolerance=±5% power=0.25 resistance=330 package=THT]
  R20 = Resistor [tolerance=±5% power=0.25 resistance=330 package=THT]
  R24 = Resistor [tolerance=±5% power=0.25 resistance=330 package=THT]
  R22 = Resistor [tolerance=±5% power=0.25 resistance=330 package=THT]
  R23 = Resistor [tolerance=±5% power=0.25 resistance=330 package=THT]
  R21 = Resistor [tolerance=±5% power=0.25 resistance=330 package=THT]
  R28 = Resistor [tolerance=±5% power=0.25 resistance=330 package=THT]
  R26 = Resistor [tolerance=±5% power=0.25 resistance=330 package=THT]
  R27 = Resistor [tolerance=±5% power=0.25 resistance=330 package=THT]
  R25 = Resistor [tolerance=±5% power=0.25 resistance=330 package=THT]
  R32 = Resistor [tolerance=±5% power=0.25 resistance=330 package=THT]
  R30 = Resistor [tolerance=±5% power=0.25 resistance=330 package=THT]
  R31 = Resistor [tolerance=±5% power=0.25 resistance=330 package=THT]
  R29 = Resistor [tolerance=±5% power=0.25 resistance=330 package=THT]
  R49 = Resistor [tolerance=±5% power=0.25 resistance=100 package=THT]
  R50 = Resistor [tolerance=±5% power=0.25 resistance=100 package=THT]
  R52 = Resistor [tolerance=±5% power=0.25 resistance=100 package=THT]
  R53 = Resistor [tolerance=±5% power=0.25 resistance=100 package=THT]
  R54 = Resistor [tolerance=±5% power=0.25 resistance=100 package=THT]
  R54_2 = Resistor [tolerance=±5% power=0.25 resistance=100 package=THT]
  R55 = Resistor [tolerance=±5% power=0.25 resistance=100 package=THT]
  R56 = Resistor [tolerance=±5% power=0.25 resistance=100 package=THT]
  R57 = Resistor [tolerance=±5% power=0.25 resistance=100 package=THT]
  R58 = Resistor [tolerance=±5% power=0.25 resistance=100 package=THT]
  R59 = Resistor [tolerance=±5% power=0.25 resistance=100 package=THT]
  R60 = Resistor [tolerance=±5% power=0.25 resistance=100 package=THT]
  R61 = Resistor [tolerance=±5% power=0.25 resistance=100 package=THT]
  R62 = Resistor [tolerance=±5% power=0.25 resistance=100 package=THT]
  R63 = Resistor [tolerance=±5% power=0.25 resistance=100 package=THT]
  R64 = Resistor [tolerance=±5% power=0.25 resistance=100 package=THT]
  R84 = Resistor [tolerance=±5% power=0.25 resistance=100 package=THT]
  R83 = Resistor [tolerance=±5% power=0.25 resistance=100 package=THT]
  R82 = Resistor [tolerance=±5% power=0.25 resistance=100 package=THT]
  R81 = Resistor [tolerance=±5% power=0.25 resistance=100 package=THT]
  R88 = Resistor [tolerance=±5% power=0.25 resistance=100 package=THT]
  R87 = Resistor [tolerance=±5% power=0.25 resistance=100 package=THT]
  R86 = Resistor [tolerance=±5% power=0.25 resistance=100 package=THT]
  R85 = Resistor [tolerance=±5% power=0.25 resistance=100 package=THT]
  R92 = Resistor [tolerance=±5% power=0.25 resistance=100 package=THT]
  R91 = Resistor [tolerance=±5% power=0.25 resistance=100 package=THT]
  R90 = Resistor [tolerance=±5% power=0.25 resistance=100 package=THT]
  R89 = Resistor [tolerance=±5% power=0.25 resistance=100 package=THT]
  R96 = Resistor [tolerance=±5% power=0.25 resistance=100 package=THT]
  R95 = Resistor [tolerance=±5% power=0.25 resistance=100 package=THT]
  R94 = Resistor [tolerance=±5% power=0.25 resistance=100 package=THT]
  R93 = Resistor [tolerance=±5% power=0.25 resistance=100 package=THT]
  J10 = male pin header, 8 pins [form="♂ (male)"]
  J12 = male pin header, 8 pins [form="♂ (male)"]
  J14 = male pin header, 8 pins [form="♂ (male)"]
  J16 = male pin header, 8 pins [form="♂ (male)"]
  R113 = Resistor [tolerance=±5% power=0.25 resistance=330 package=THT]
  R114 = Resistor [tolerance=±5% power=0.25 resistance=330 package=THT]
  R115 = Resistor [tolerance=±5% power=0.25 resistance=330 package=THT]
  R116 = Resistor [tolerance=±5% power=0.25 resistance=330 package=THT]
  R117 = Resistor [tolerance=±5% power=0.25 resistance=330 package=THT]
  R118 = Resistor [tolerance=±5% power=0.25 resistance=330 package=THT]
  R119 = Resistor [tolerance=±5% power=0.25 resistance=330 package=THT]
  R120 = Resistor [tolerance=±5% power=0.25 resistance=330 package=THT]
  R121 = Resistor [tolerance=±5% power=0.25 resistance=330 package=THT]
  R122 = Resistor [tolerance=±5% power=0.25 resistance=330 package=THT]
  R123 = Resistor [tolerance=±5% power=0.25 resistance=330 package=THT]
  R124 = Resistor [tolerance=±5% power=0.25 resistance=330 package=THT]
  R125 = Resistor [tolerance=±5% power=0.25 resistance=330 package=THT]
  R126 = Resistor [tolerance=±5% power=0.25 resistance=330 package=THT]
  R127 = Resistor [tolerance=±5% power=0.25 resistance=330 package=THT]
  R128 = Resistor [tolerance=±5% power=0.25 resistance=330 package=THT]
  Pad65 = Pad [width=3 height=2 connect=center]
  Pad66 = Pad [width=3 height=2 connect=center]
  Pad67 = Pad [width=3 height=2 connect=center]
  Pad68 = Pad [width=3 height=2 connect=center]
  Pad69 = Pad [width=3 height=2 connect=center]
  Pad70 = Pad [width=3 height=2 connect=center]
  Pad71 = Pad [width=3 height=2 connect=center]
  Pad72 = Pad [width=3 height=2 connect=center]
  Pad73 = Pad [width=3 height=2 connect=center]
  Pad74 = Pad [width=3 height=2 connect=center]
  Pad75 = Pad [width=3 height=2 connect=center]
  Pad76 = Pad [width=3 height=2 connect=center]
  Pad77 = Pad [width=3 height=2 connect=center]
  Pad78 = Pad [width=3 height=2 connect=center]
  Pad79 = Pad [width=3 height=2 connect=center]
  Pad80 = Pad [width=3 height=2 connect=center]
  Pad81 = Pad [width=3 height=2 connect=center]
  Pad82 = Pad [width=3 height=2 connect=center]
  Pad83 = Pad [width=3 height=2 connect=center]
  Pad84 = Pad [width=3 height=2 connect=center]
  Pad85 = Pad [width=3 height=2 connect=center]
  Pad86 = Pad [width=3 height=2 connect=center]
  Pad87 = Pad [width=3 height=2 connect=center]
  Pad88 = Pad [width=3 height=2 connect=center]
  Pad89 = Pad [width=3 height=2 connect=center]
  Pad90 = Pad [width=3 height=2 connect=center]
  Pad91 = Pad [width=3 height=2 connect=center]
  Pad92 = Pad [width=3 height=2 connect=center]
  Pad93 = Pad [width=3 height=2 connect=center]
  Pad94 = Pad [width=3 height=2 connect=center]
  Pad95 = Pad [width=3 height=2 connect=center]
  Pad96 = Pad [width=3 height=2 connect=center]
  Pad97 = Pad [width=3 height=2 connect=center]
  Pad98 = Pad [width=3 height=2 connect=center]
  Pad99 = Pad [width=3 height=2 connect=center]
  Pad100 = Pad [width=3 height=2 connect=center]
  Pad101 = Pad [width=3 height=2 connect=center]
  Pad102 = Pad [width=3 height=2 connect=center]
  Pad103 = Pad [width=3 height=2 connect=center]
  Pad104 = Pad [width=3 height=2 connect=center]
  Pad105 = Pad [width=3 height=2 connect=center]
  Pad106 = Pad [width=3 height=2 connect=center]
  Pad107 = Pad [width=3 height=2 connect=center]
  Pad108 = Pad [width=3 height=2 connect=center]
  Pad109 = Pad [width=3 height=2 connect=center]
  Pad110 = Pad [width=3 height=2 connect=center]
  Pad111 = Pad [width=3 height=2 connect=center]
  Pad112 = Pad [width=3 height=2 connect=center]
  Pad113 = Pad [width=3 height=2 connect=center]
  Pad114 = Pad [width=3 height=2 connect=center]
  Pad115 = Pad [width=3 height=2 connect=center]
  Pad116 = Pad [width=3 height=2 connect=center]
  Pad117 = Pad [width=3 height=2 connect=center]
  Pad118 = Pad [width=3 height=2 connect=center]
  Pad119 = Pad [width=3 height=2 connect=center]
  Pad120 = Pad [width=3 height=2 connect=center]
  Pad121 = Pad [width=3 height=2 connect=center]
  Pad122 = Pad [width=3 height=2 connect=center]
  Pad123 = Pad [width=3 height=2 connect=center]
  Pad124 = Pad [width=3 height=2 connect=center]
  Pad125 = Pad [width=3 height=2 connect=center]
  Pad126 = Pad [width=3 height=2 connect=center]
  Pad127 = Pad [width=3 height=2 connect=center]
  Pad128 = Pad [width=3 height=2 connect=center]
  LED1 = LED - 5mm [color="Red (633nm)" current=0.030 package="5 mm [THT]"]
  R129 = Resistor [tolerance=±5% power=0.25 resistance=330 package=THT]
  LED2 = LED - 5mm [color="Red (633nm)" current=0.030 package="5 mm [THT]"]
  R130 = Resistor [tolerance=±5% power=0.25 resistance=330 package=THT]
  TEST = male pin header, 3 pins [form="♂ (male)"]
  C2 = Ceramic Capacitor [capacitance=100nF voltage=16V package="200 mil [THT, multilayer]"]
  C3 = Ceramic Capacitor [capacitance=100nF voltage=16V package="200 mil [THT, multilayer]"]
  C4 = Ceramic Capacitor [capacitance=100nF voltage=16V package="200 mil [THT, multilayer]"]
  C5 = Ceramic Capacitor [capacitance=100nF voltage=16V package="200 mil [THT, multilayer]"]
  C6 = Ceramic Capacitor [capacitance=100nF voltage=16V package="200 mil [THT, multilayer]"]
  C7 = Ceramic Capacitor [capacitance=100nF voltage=16V package="200 mil [THT, multilayer]"]
  C8 = Ceramic Capacitor [capacitance=100nF voltage=16V package="200 mil [THT, multilayer]"]
  C1 = Ceramic Capacitor [capacitance=100nF voltage=16V package="200 mil [THT, multilayer]"]
  ESP32 = DOIT Esp32 DevKit v1 (30 pins long, 11 pins width) [part_number=ESP32S-PIN30]
  HW-613 = male pin header, 4 pins [form="♂ (male)"]
  C9 = Electrolytic Capacitor [capacitance=100µF voltage=10V package="100 mil [THT, electrolytic]"]
  Power = male pin header, 3 pins [form="♂ (male)"]

nets:
  GND: IC1.A0, IC1.A1, IC1.A2, IC1.GND, IC2.A1, IC2.A2, IC2.GND, IC3.A0, IC3.A2, IC3.GND, IC4.A2, IC4.GND, IC5.A0, IC5.A1, IC5.GND, IC6.A1, IC6.GND, IC7.A0, IC7.GND, IC8.GND, LED1.cathode, LED2.cathode, C2.0, C3.0, C4.0, C5.0, C6.0, C7.0, C8.0, C1.0, ESP32.GND, HW-613.pin3, C9.-, Power.pin3
  L01-04: IC1.P0, R33.Pin_0
  L01-05: IC1.P1, R34.Pin_1
  L01-06: IC1.P2, R35.Pin_0
  L01-07: IC1.P3, R36.Pin_1
  L01-09: IC1.P4, R68.Pin_0
  L01-10: IC1.P5, R67.Pin_0
  L01-11: IC1.P6, R66.Pin_0
  L01-12: IC1.P7, R65.Pin_0
  I2C-SCL: IC1.SCL, IC2.SCL, IC3.SCL, IC4.SCL, IC5.SCL, IC6.SCL, IC7.SCL, IC8.SCL, ESP32.D22
  I2C_SDA: IC1.SDA, IC2.SDA, IC3.SDA, IC4.SDA, IC5.SDA, IC6.SDA, IC7.SDA, IC8.SDA, ESP32.D21
  3.3V: IC1.VCC, IC2.A0, IC2.VCC, IC3.A1, IC3.VCC, IC4.A0, IC4.A1, IC4.VCC, U1.Pin_1, U1.Pin_3, U1.Pin_5, U1.Pin_7, U2.Pin_1, U2.Pin_3, U2.Pin_5, U2.Pin_7, U4.Pin_1, U4.Pin_3, U4.Pin_5, U4.Pin_7, U3.Pin_1, U3.Pin_3, U3.Pin_5, U3.Pin_7, U7.Pin_1, U7.Pin_3, U7.Pin_5, U7.Pin_7, U5.Pin_1, U5.Pin_3, U5.Pin_5, U5.Pin_7, U6.Pin_1, U6.Pin_3, U6.Pin_5, U6.Pin_7, U8.Pin_1, U8.Pin_3, U8.Pin_5, U8.Pin_7, IC5.A2, IC5.VCC, IC6.A0, IC6.A2, IC6.VCC, IC7.A1, IC7.A2, IC7.VCC, IC8.A0, IC8.A1, IC8.A2, IC8.VCC, U10.Pin_1, U10.Pin_3, U10.Pin_5, U10.Pin_7, U12.Pin_1, U12.Pin_3, U12.Pin_5, U12.Pin_7, U14.Pin_1, U14.Pin_3, U14.Pin_5, U14.Pin_7, U16.Pin_1, U16.Pin_3, U16.Pin_5, U16.Pin_7, U9.Pin_1, U9.Pin_3, U9.Pin_5, U9.Pin_7, U11.Pin_1, U11.Pin_3, U11.Pin_5, U11.Pin_7, U13.Pin_1, U13.Pin_3, U13.Pin_5, U13.Pin_7, U15.Pin_1, U15.Pin_3, U15.Pin_5, U15.Pin_7, C2.1, C3.1, C4.1, C5.1, C6.1, C7.1, C8.1, C1.1, ESP32.3V3, HW-613.pin4, C9.+
  L02-04: IC2.P0, R37.Pin_0
  L02-05: IC2.P1, R38.Pin_1
  L02-06: IC2.P2, R39.Pin_0
  L02-07: IC2.P3, R40.Pin_1
  L02-09: IC2.P4, R72.Pin_0
  L02-10: IC2.P5, R71.Pin_0
  L02-11: IC2.P6, R70.Pin_0
  L02-12: IC2.P7, R69.Pin_0
  L03-04: IC3.P0, R41.Pin_0
  L03-05: IC3.P1, R42.Pin_1
  L03-06: IC3.P2, R43.Pin_0
  L03-07: IC3.P3, R44.Pin_1
  L03-09: IC3.P4, R76.Pin_0
  L03-10: IC3.P5, R75.Pin_0
  L03-11: IC3.P6, R74.Pin_0
  L03-12: IC3.P7, R73.Pin_0
  L04-04: IC4.P0, R45.Pin_0
  L04-05: IC4.P1, R46.Pin_1
  L04-06: IC4.P2, R47.Pin_0
  L04-07: IC4.P3, R48.Pin_1
  L04-09: IC4.P4, R80.Pin_0
  L04-10: IC4.P5, R79.Pin_0
  L04-11: IC4.P6, R78.Pin_0
  L04-12: IC4.P7, R77.Pin_0
  N1: U1.Pin_2, R36.Pin_0
  N2: U1.Pin_4, R35.Pin_1
  N3: U1.Pin_6, R34.Pin_0
  N4: U1.Pin_8, R33.Pin_1
  N5: U1.Pin_9, R1.Pin_0
  12V: U1.Pin_10, U1.Pin_12, U1.Pin_14, U1.Pin_16, U2.Pin_10, U2.Pin_12, U2.Pin_14, U2.Pin_16, U4.Pin_10, U4.Pin_12, U4.Pin_14, U4.Pin_16, U3.Pin_10, U3.Pin_12, U3.Pin_14, U3.Pin_16, U7.Pin_10, U7.Pin_12, U7.Pin_14, U7.Pin_16, U5.Pin_10, U5.Pin_12, U5.Pin_14, U5.Pin_16, U6.Pin_10, U6.Pin_12, U6.Pin_14, U6.Pin_16, U8.Pin_10, U8.Pin_12, U8.Pin_14, U8.Pin_16, J1.pin2, J1.pin4, J1.pin6, J1.pin8, J5.pin2, J5.pin4, J5.pin6, J5.pin8, J7.pin2, J7.pin4, J7.pin6, J7.pin8, J8.pin2, J8.pin4, J8.pin6, J8.pin8, J6.pin2, J6.pin4, J6.pin6, J6.pin8, J4.pin2, J4.pin4, J4.pin6, J4.pin8, J2.pin2, J2.pin4, J2.pin6, J2.pin8, J3.pin2, J3.pin4, J3.pin6, J3.pin8, Pad1.pad, Pad2.pad, Pad3.pad, Pad4.pad, Pad5.pad, Pad6.pad, Pad7.pad, Pad8.pad, Pad9.pad, Pad10.pad, Pad11.pad, Pad12.pad, Pad13.pad, Pad14.pad, Pad15.pad, Pad16.pad, Pad17.pad, Pad18.pad, Pad19.pad, Pad20.pad, Pad21.pad, Pad22.pad, Pad23.pad, Pad24.pad, Pad25.pad, Pad26.pad, Pad27.pad, Pad28.pad, Pad29.pad, Pad30.pad, Pad31.pad, Pad32.pad, Pad33.pad, Pad34.pad, Pad35.pad, Pad36.pad, Pad37.pad, Pad38.pad, Pad39.pad, Pad40.pad, Pad41.pad, Pad42.pad, Pad43.pad, Pad44.pad, Pad45.pad, Pad46.pad, Pad47.pad, Pad48.pad, Pad49.pad, Pad50.pad, Pad51.pad, Pad52.pad, Pad53.pad, Pad54.pad, Pad55.pad, Pad56.pad, Pad57.pad, Pad58.pad, Pad59.pad, Pad60.pad, Pad61.pad, Pad62.pad, Pad63.pad, Pad64.pad, U10.Pin_10, U10.Pin_12, U10.Pin_14, U10.Pin_16, U12.Pin_10, U12.Pin_12, U12.Pin_14, U12.Pin_16, U14.Pin_10, U14.Pin_12, U14.Pin_14, U14.Pin_16, U16.Pin_10, U16.Pin_12, U16.Pin_14, U16.Pin_16, U9.Pin_10, U9.Pin_12, U9.Pin_14, U9.Pin_16, U11.Pin_10, U11.Pin_12, U11.Pin_14, U11.Pin_16, U13.Pin_10, U13.Pin_12, U13.Pin_14, U13.Pin_16, U15.Pin_10, U15.Pin_12, U15.Pin_14, U15.Pin_16, J9.pin2, J9.pin4, J9.pin6, J9.pin8, J11.pin2, J11.pin4, J11.pin6, J11.pin8, J13.pin2, J13.pin4, J13.pin6, J13.pin8, J15.pin2, J15.pin4, J15.pin6, J15.pin8, J10.pin2, J10.pin4, J10.pin6, J10.pin8, J12.pin2, J12.pin4, J12.pin6, J12.pin8, J14.pin2, J14.pin4, J14.pin6, J14.pin8, J16.pin2, J16.pin4, J16.pin6, J16.pin8, Pad65.pad, Pad66.pad, Pad67.pad, Pad68.pad, Pad69.pad, Pad70.pad, Pad71.pad, Pad72.pad, Pad73.pad, Pad74.pad, Pad75.pad, Pad76.pad, Pad77.pad, Pad78.pad, Pad79.pad, Pad80.pad, Pad81.pad, Pad82.pad, Pad83.pad, Pad84.pad, Pad85.pad, Pad86.pad, Pad87.pad, Pad88.pad, Pad89.pad, Pad90.pad, Pad91.pad, Pad92.pad, Pad93.pad, Pad94.pad, Pad95.pad, Pad96.pad, Pad97.pad, Pad98.pad, Pad99.pad, Pad100.pad, Pad101.pad, Pad102.pad, Pad103.pad, Pad104.pad, Pad105.pad, Pad106.pad, Pad107.pad, Pad108.pad, Pad109.pad, Pad110.pad, Pad111.pad, Pad112.pad, Pad113.pad, Pad114.pad, Pad115.pad, Pad116.pad, Pad117.pad, Pad118.pad, Pad119.pad, Pad120.pad, Pad121.pad, Pad122.pad, Pad123.pad, Pad124.pad, Pad125.pad, Pad126.pad, Pad127.pad, Pad128.pad, TEST.pin2, HW-613.pin2, Power.pin2
  N6: U1.Pin_11, R2.Pin_0
  N7: U1.Pin_13, R3.Pin_1
  N8: U1.Pin_15, R4.Pin_1
  N9: R3.Pin_0, J1.pin5
  N10: R1.Pin_1, J1.pin1
  N11: U2.Pin_2, R65.Pin_1
  N12: U2.Pin_4, R66.Pin_1
  N13: U2.Pin_6, R67.Pin_1
  N14: U2.Pin_8, R68.Pin_1
  N15: U2.Pin_9, R100.Pin_0
  N16: U2.Pin_11, R99.Pin_0
  N17: U2.Pin_13, R98.Pin_0
  N18: U2.Pin_15, R97.Pin_0
  N19: R100.Pin_1, J2.pin1
  N20: R99.Pin_1, J2.pin3
  N21: R98.Pin_1, J2.pin5
  N22: R97.Pin_1, J2.pin7
  N23: U4.Pin_2, R69.Pin_1
  N24: U4.Pin_4, R70.Pin_1
  N25: U4.Pin_6, R71.Pin_1
  N26: U4.Pin_8, R72.Pin_1
  N27: U4.Pin_9, R104.Pin_0
  N28: U4.Pin_11, R103.Pin_0
  N29: U4.Pin_13, R102.Pin_0
  N30: U4.Pin_15, R101.Pin_0
  N31: R104.Pin_1, J4.pin1
  N32: R103.Pin_1, J4.pin3
  N33: R102.Pin_1, J4.pin5
  N34: R101.Pin_1, J4.pin7
  N35: U3.Pin_2, R40.Pin_0
  N36: U3.Pin_4, R39.Pin_1
  N37: U3.Pin_6, R38.Pin_0
  N38: U3.Pin_8, R37.Pin_1
  N39: U3.Pin_9, R5.Pin_1
  N40: U3.Pin_11, R6.Pin_1
  N41: U3.Pin_13, R7.Pin_1
  N42: U3.Pin_15, R8.Pin_1
  N43: R8.Pin_0, J3.pin7
  N44: R7.Pin_0, J3.pin5
  N45: R6.Pin_0, J3.pin3
  N46: R5.Pin_0, J3.pin1
  N47: U7.Pin_2, R48.Pin_0
  N48: U7.Pin_4, R47.Pin_1
  N49: U7.Pin_6, R46.Pin_0
  N50: U7.Pin_8, R45.Pin_1
  N51: U7.Pin_9, R13.Pin_1
  N52: U7.Pin_11, R14.Pin_1
  N53: U7.Pin_13, R15.Pin_1
  N54: U7.Pin_15, R16.Pin_1
  N55: U5.Pin_2, R44.Pin_0
  N56: U5.Pin_4, R43.Pin_1
  N57: U5.Pin_6, R42.Pin_0
  N58: U5.Pin_8, R41.Pin_1
  N59: U5.Pin_9, R9.Pin_1
  N60: U5.Pin_11, R10.Pin_1
  N61: U5.Pin_13, R11.Pin_1
  N62: U5.Pin_15, R12.Pin_1
  N63: R9.Pin_0, J5.pin1
  N64: R10.Pin_0, J5.pin3
  N65: R11.Pin_0, J5.pin5
  N66: R12.Pin_0, J5.pin7
  N67: R76.Pin_1, U6.Pin_8
  N68: R75.Pin_1, U6.Pin_6
  N69: R74.Pin_1, U6.Pin_4
  N70: R73.Pin_1, U6.Pin_2
  N71: R80.Pin_1, U8.Pin_8
  N72: R79.Pin_1, U8.Pin_6
  N73: R78.Pin_1, U8.Pin_4
  N74: R77.Pin_1, U8.Pin_2
  N75: U6.Pin_9, R108.Pin_0
  N76: U6.Pin_11, R107.Pin_0
  N77: U6.Pin_13, R106.Pin_0
  N78: U6.Pin_15, R105.Pin_0
  N79: U8.Pin_9, R112.Pin_0
  N80: U8.Pin_11, R111.Pin_0
  N81: U8.Pin_13, R110.Pin_0
  N82: U8.Pin_15, R109.Pin_0
  N83: R105.Pin_1, J6.pin7
  N84: R106.Pin_1, J6.pin5
  N85: R107.Pin_1, J6.pin3
  N86: R108.Pin_1, J6.pin1
  N87: R109.Pin_1, J8.pin7
  N88: R110.Pin_1, J8.pin5
  N89: R111.Pin_1, J8.pin3
  N90: R112.Pin_1, J8.pin1
  N91: J1.pin3, R2.Pin_1
  N92: J1.pin7, R4.Pin_0
  N93: J7.pin1, R13.Pin_0
  N94: J7.pin3, R14.Pin_0
  N95: J7.pin5, R15.Pin_0
  N96: J7.pin7, R16.Pin_0
  N97: IC5.P0, R49.Pin_0
  N98: IC5.P1, R50.Pin_1
  N99: IC5.P2, R52.Pin_0
  N100: IC5.P3, R53.Pin_1
  N101: IC5.P4, R84.Pin_0
  N102: IC5.P5, R83.Pin_0
  N103: IC5.P6, R82.Pin_0
  N104: IC5.P7, R81.Pin_0
  N105: IC6.P0, R54.Pin_0
  N106: IC6.P1, R54_2.Pin_1
  N107: IC6.P2, R55.Pin_0
  N108: IC6.P3, R56.Pin_1
  N109: IC6.P4, R88.Pin_0
  N110: IC6.P5, R87.Pin_0
  N111: IC6.P6, R86.Pin_0
  N112: IC6.P7, R85.Pin_0
  N113: IC7.P0, R57.Pin_0
  N114: IC7.P1, R58.Pin_1
  N115: IC7.P2, R59.Pin_0
  N116: IC7.P3, R60.Pin_1
  N117: IC7.P4, R92.Pin_0
  N118: IC7.P5, R91.Pin_0
  N119: IC7.P6, R90.Pin_0
  N120: IC7.P7, R89.Pin_0
  N121: IC8.P0, R61.Pin_0
  N122: IC8.P1, R62.Pin_1
  N123: IC8.P2, R63.Pin_0
  N124: IC8.P3, R64.Pin_1
  N125: IC8.P4, R96.Pin_0
  N126: IC8.P5, R95.Pin_0
  N127: IC8.P6, R94.Pin_0
  N128: IC8.P7, R93.Pin_0
  N129: U10.Pin_2, R81.Pin_1
  N130: U10.Pin_4, R82.Pin_1
  N131: U10.Pin_6, R83.Pin_1
  N132: U10.Pin_8, R84.Pin_1
  N133: U10.Pin_9, R116.Pin_0
  N134: U10.Pin_11, R115.Pin_0
  N135: U10.Pin_13, R114.Pin_0
  N136: U10.Pin_15, R113.Pin_0
  N137: U12.Pin_2, R85.Pin_1
  N138: U12.Pin_4, R86.Pin_1
  N139: U12.Pin_6, R87.Pin_1
  N140: U12.Pin_8, R88.Pin_1
  N141: U12.Pin_9, R120.Pin_0
  N142: U12.Pin_11, R119.Pin_0
  N143: U12.Pin_13, R118.Pin_0
  N144: U12.Pin_15, R117.Pin_0
  N145: U14.Pin_2, R89.Pin_1
  N146: U14.Pin_4, R90.Pin_1
  N147: U14.Pin_6, R91.Pin_1
  N148: U14.Pin_8, R92.Pin_1
  N149: U14.Pin_9, R124.Pin_0
  N150: U14.Pin_11, R123.Pin_0
  N151: U14.Pin_13, R122.Pin_0
  N152: U14.Pin_15, R121.Pin_0
  N153: U16.Pin_2, R93.Pin_1
  N154: U16.Pin_4, R94.Pin_1
  N155: U16.Pin_6, R95.Pin_1
  N156: U16.Pin_8, R96.Pin_1
  N157: U16.Pin_9, R128.Pin_0
  N158: U16.Pin_11, R127.Pin_0
  N159: U16.Pin_13, R126.Pin_0
  N160: U16.Pin_15, R125.Pin_0
  N161: U9.Pin_2, R53.Pin_0
  N162: U9.Pin_4, R52.Pin_1
  N163: U9.Pin_6, R50.Pin_0
  N164: U9.Pin_8, R49.Pin_1
  N165: U9.Pin_9, R17.Pin_1
  N166: U9.Pin_11, R18.Pin_1
  N167: U9.Pin_13, R19.Pin_1
  N168: U9.Pin_15, R20.Pin_1
  N169: U11.Pin_2, R56.Pin_0
  N170: U11.Pin_4, R55.Pin_1
  N171: U11.Pin_6, R54_2.Pin_0
  N172: U11.Pin_8, R54.Pin_1
  N173: U11.Pin_9, R21.Pin_1
  N174: U11.Pin_11, R22.Pin_1
  N175: U11.Pin_13, R23.Pin_1
  N176: U11.Pin_15, R24.Pin_1
  N177: U13.Pin_2, R60.Pin_0
  N178: U13.Pin_4, R59.Pin_1
  N179: U13.Pin_6, R58.Pin_0
  N180: U13.Pin_8, R57.Pin_1
  N181: U13.Pin_9, R25.Pin_1
  N182: U13.Pin_11, R26.Pin_1
  N183: U13.Pin_13, R27.Pin_1
  N184: U13.Pin_15, R28.Pin_1
  N185: U15.Pin_2, R64.Pin_0
  N186: U15.Pin_4, R63.Pin_1
  N187: U15.Pin_6, R62.Pin_0
  N188: U15.Pin_8, R61.Pin_1
  N189: U15.Pin_9, R29.Pin_1
  N190: U15.Pin_11, R30.Pin_1
  N191: U15.Pin_13, R31.Pin_1
  N192: U15.Pin_15, R32.Pin_1
  N193: J9.pin1, R17.Pin_0
  N194: J9.pin3, R18.Pin_0
  N195: J9.pin5, R19.Pin_0
  N196: J9.pin7, R20.Pin_0
  N197: J11.pin1, R21.Pin_0
  N198: J11.pin3, R22.Pin_0
  N199: J11.pin5, R23.Pin_0
  N200: J11.pin7, R24.Pin_0
  N201: J13.pin1, R25.Pin_0
  N202: J13.pin3, R26.Pin_0
  N203: J13.pin5, R27.Pin_0
  N204: J13.pin7, R28.Pin_0
  N205: J15.pin1, R29.Pin_0
  N206: J15.pin3, R30.Pin_0
  N207: J15.pin5, R31.Pin_0
  N208: J15.pin7, R32.Pin_0
  N209: J10.pin1, R116.Pin_1
  N210: J10.pin3, R115.Pin_1
  N211: J10.pin5, R114.Pin_1
  N212: J10.pin7, R113.Pin_1
  N213: J12.pin1, R120.Pin_1
  N214: J12.pin3, R119.Pin_1
  N215: J12.pin5, R118.Pin_1
  N216: J12.pin7, R117.Pin_1
  N217: J14.pin1, R124.Pin_1
  N218: J14.pin3, R123.Pin_1
  N219: J14.pin5, R122.Pin_1
  N220: J14.pin7, R121.Pin_1
  N221: J16.pin1, R128.Pin_1
  N222: J16.pin3, R127.Pin_1
  N223: J16.pin5, R126.Pin_1
  N224: J16.pin7, R125.Pin_1
  N225: LED1.anode, R129.Pin_1
  N226: R129.Pin_0, TEST.pin1
  N227: LED2.anode, R130.Pin_1
  N228: R130.Pin_0, TEST.pin3
  N229: HW-613.pin1, Power.pin1

notes:
  LedDriver
  v6,1
  - +
  +3V3
  GND
  +12V
  EN
  Svenn-Erik K. Thomsen
  sekt1953@gmail.com

custom parts:
  DOIT Esp32 DevKit v1 (30 pins long, 11 pins width): The DOIT Esp32 DevKit v1 is one of the development board created by DOIT to evaluate the ESP-WROOM-32 module. It is based on the ESP32 microcontroller that boasts Wifi, Bluetooth, Ethernet and Low Power support all in a single chip. (vanepp) made breadboard work, adjusted pin numbering and labels and reduced size of schematic and cleaned up pcb. This chip is 30pins long (2 x15) and 11 pins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
