# Fritzing sketch PCB-TrackSensor_V3.3 (saved by Fritzing 0.9.6b)
circuit board: 10cm x 6.9cm

parts:
  U01 = PCF8574 [package="DIP16 [THT]"]
  U02 = TLP620-4 [package="DIP (Dual Inline) [THT]"]
  J10 = male pin header, 4 pins [form="♂ (male)"]
  U05 = TLP620-4 [package="DIP (Dual Inline) [THT]"]
  U04 = PCF8574 [package="DIP16 [THT]"]
  U06 = TLP620-4 [package="DIP (Dual Inline) [THT]"]
  U08 = TLP620-4 [package="DIP (Dual Inline) [THT]"]
  U11 = TLP620-4 [package="DIP (Dual Inline) [THT]"]
  U10 = PCF8574 [package="DIP16 [THT]"]
  U09 = TLP620-4 [package="DIP (Dual Inline) [THT]"]
  J1 = male pin header, 5 pins [form="♂ (male)"]
  J2 = male pin header, 5 pins [form="♂ (male)"]
  J3 = male pin header, 5 pins [form="♂ (male)"]
  J5 = male pin header, 5 pins [form="♂ (male)"]
  R11 = Resistor [tolerance=±5% power=0.25 resistance=22 package=THT]
  R12 = Resistor [tolerance=±5% power=0.25 resistance=22 package=THT]
  R13 = Resistor [tolerance=±5% power=0.25 resistance=22 package=THT]
  R14 = Resistor [tolerance=±5% power=0.25 resistance=22 package=THT]
  R9 = Resistor [tolerance=±5% power=0.25 resistance=22 package=THT]
  R8 = Resistor [tolerance=±5% power=0.25 resistance=22 package=THT]
  R7 = Resistor [tolerance=±5% power=0.25 resistance=22 package=THT]
  R6 = Resistor [tolerance=±5% power=0.25 resistance=22 package=THT]
  R4 = Resistor [tolerance=±5% power=0.25 resistance=22 package=THT]
  R3 = Resistor [tolerance=±5% power=0.25 resistance=22 package=THT]
  R2 = Resistor [tolerance=±5% power=0.25 resistance=22 package=THT]
  R1 = Resistor [tolerance=±5% power=0.25 resistance=22 package=THT]
  R19 = Resistor [tolerance=±5% power=0.25 resistance=22 package=THT]
  R18 = Resistor [tolerance=±5% power=0.25 resistance=22 package=THT]
  R17 = Resistor [tolerance=±5% power=0.25 resistance=22 package=THT]
  R16 = Resistor [tolerance=±5% power=0.25 resistance=22 package=THT]
  J12 = male pin header, 5 pins [form="♂ (male)"]
  J13 = male pin header, 5 pins [form="♂ (male)"]
  J14 = male pin header, 5 pins [form="♂ (male)"]
  J16 = male pin header, 5 pins [form="♂ (male)"]
  R29 = Resistor [tolerance=±5% power=0.25 resistance=22 package=THT]
  R30 = Resistor [tolerance=±5% power=0.25 resistance=22 package=THT]
  R31 = Resistor [tolerance=±5% power=0.25 resistance=22 package=THT]
  R32 = Resistor [tolerance=±5% power=0.25 resistance=22 package=THT]
  R34 = Resistor [tolerance=±5% power=0.25 resistance=22 package=THT]
  R35 = Resistor [tolerance=±5% power=0.25 resistance=22 package=THT]
  R36 = Resistor [tolerance=±5% power=0.25 resistance=22 package=THT]
  R37 = Resistor [tolerance=±5% power=0.25 resistance=22 package=THT]
  R39 = Resistor [tolerance=±5% power=0.25 resistance=22 package=THT]
  R40 = Resistor [tolerance=±5% power=0.25 resistance=22 package=THT]
  R41 = Resistor [tolerance=±5% power=0.25 resistance=22 package=THT]
  R42 = Resistor [tolerance=±5% power=0.25 resistance=22 package=THT]
  R44 = Resistor [tolerance=±5% power=0.25 resistance=22 package=THT]
  R45 = Resistor [tolerance=±5% power=0.25 resistance=22 package=THT]
  R46 = Resistor [tolerance=±5% power=0.25 resistance=22 package=THT]
  R47 = Resistor [tolerance=±5% power=0.25 resistance=22 package=THT]
  J11 = male pin header, 4 pins [form="♂ (male)"]
  U12 = TLP620-4 [package="DIP (Dual Inline) [THT]"]
  U03 = TLP620-4 [package="DIP (Dual Inline) [THT]"]
  J4 = male pin header, 2 pins [form="♂ (male)"]
  R5 = IC, SIP package, 5 pins [chip_label=R part_number=4x470ohm]
  R33 = IC, SIP package, 5 pins [chip_label=R part_number=4x470ohm]
  R10 = IC, SIP package, 5 pins [chip_label=R part_number=4x470ohm]
  R38 = IC, SIP package, 5 pins [chip_label=R part_number=4x470ohm]
  R15 = IC, SIP package, 5 pins [chip_label=R part_number=4x470ohm]
  R43 = IC, SIP package, 5 pins [chip_label=R part_number=4x470ohm]
  R48 = IC, SIP package, 5 pins [chip_label=R part_number=4x470ohm]
  J15 = male pin header, 2 pins [form="♂ (male)"]
  J8 = male pin header, 2 pins [form="♂ (male)"]
  J7 = male pin header, 2 pins [form="♂ (male)"]
  J9 = male pin header, 2 pins [form="♂ (male)"]
  J6 = male pin header, 2 pins [form="♂ (male)"]
  R20 = IC, SIP package, 5 pins [chip_label=R part_number=4x470ohm]
  R25 = IC, SIP package, 6 pins [chip_label=R part_number=5x2K2]
  R21 = IC, SIP package, 6 pins [chip_label=R part_number=5x2K2]
  R22 = IC, SIP package, 6 pins [chip_label=R part_number=5x2K2]
  R23 = IC, SIP package, 6 pins [chip_label=R part_number=5x2K2]
  R24 = IC, SIP package, 6 pins [chip_label=R part_number=5x2K2]
  U07 = PCF8574 [package="DIP16 [THT]"]
  R26 = IC, SIP package, 6 pins [chip_label=R part_number=5x2K2]
  R27 = IC, SIP package, 6 pins [chip_label=R part_number=5x2K2]
  R28 = IC, SIP package, 6 pins [chip_label=R part_number=5x2K2]

nets:
  GND: U01.A0, U01.A1, U01.GND, U02.pin9, U02.pin11, U02.pin13, U02.pin15, J10.pin4, U05.pin9, U05.pin11, U05.pin13, U05.pin15, U04.A1, U04.GND, U06.pin9, U06.pin11, U06.pin13, U06.pin15, U08.pin9, U08.pin11, U08.pin13, U08.pin15, U11.pin9, U11.pin11, U11.pin13, U11.pin15, U10.GND, U09.pin9, U09.pin11, U09.pin13, U09.pin15, J11.pin4, U12.pin9, U12.pin11, U12.pin13, U12.pin15, U03.pin9, U03.pin11, U03.pin13, U03.pin15, J8.pin2, J7.pin2, J9.pin2, J6.pin2, U07.A0, U07.GND
  N1: U01.A2, J9.pin1, R24.pin2
  L02-16: U01.P0, U02.pin16, R24.pin3
  L02-14: U01.P1, U02.pin14, R24.pin4
  L02-12: U01.P2, U02.pin12, R24.pin5
  L02-10: U01.P3, U02.pin10, R24.pin6
  L03-16: U01.P4, U03.pin16, R28.pin6
  L03-14: U01.P5, U03.pin14, R28.pin5
  L03-12: U01.P6, U03.pin12, R28.pin4
  L03-10: U01.P7, U03.pin10, R28.pin3
  N2: U01.INT, R28.pin2
  I2C-SCL: U01.SCL, J10.pin3, U04.SCL, U10.SCL, J11.pin3, U07.SCL
  I2C-SDA: U01.SDA, J10.pin2, U04.SDA, U10.SDA, J11.pin2, U07.SDA
  3.3V: U01.VCC, J10.pin1, U04.A0, U04.VCC, U10.A0, U10.A1, U10.VCC, J11.pin1, R25.pin1, R21.pin1, R22.pin1, R23.pin1, R24.pin1, U07.A1, U07.VCC, R26.pin1, R27.pin1, R28.pin1
  N3: U02.pin1, R19.Pin_1
  L27-2: U02.pin2, U02.pin4, U02.pin6, U02.pin8, U05.pin2, U05.pin4, U05.pin6, U05.pin8, U08.pin2, U08.pin4, U08.pin6, U08.pin8, U11.pin2, U11.pin4, U11.pin6, U11.pin8, J1.pin1, J2.pin1, J3.pin1, J5.pin1, J4.pin1, J4.pin2, R5.pin1, R10.pin1, R15.pin1, R20.pin1
  N4: U02.pin3, R18.Pin_1
  N5: U02.pin5, R17.Pin_1
  N6: U02.pin7, R16.Pin_1
  N7: U05.pin1, R14.Pin_1
  N8: U05.pin3, R13.Pin_1
  N9: U05.pin5, R12.Pin_1
  N10: U05.pin7, R11.Pin_1
  L05-10: U05.pin10, U04.P3, R23.pin6
  L05-12: U05.pin12, U04.P2, R23.pin5
  L05-14: U05.pin14, U04.P1, R23.pin4
  L05-16: U05.pin16, U04.P0, R23.pin3
  N11: U04.A2, J8.pin1, R23.pin2
  L06-16: U04.P4, U06.pin16, R27.pin6
  L06-14: U04.P5, U06.pin14, R27.pin5
  L06-12: U04.P6, U06.pin12, R27.pin4
  L06-10: U04.P7, U06.pin10, R27.pin3
  N12: U04.INT, R27.pin2
  N13: U06.pin1, R39.Pin_1
  L28-2: U06.pin2, U06.pin4, U06.pin6, U06.pin8, U09.pin2, U09.pin4, U09.pin6, U09.pin8, J12.pin1, J13.pin1, J14.pin1, J16.pin1, U12.pin2, U12.pin4, U12.pin6, U12.pin8, U03.pin2, U03.pin4, U03.pin6, U03.pin8, R33.pin1, R38.pin1, R43.pin1, R48.pin1, J15.pin1, J15.pin2
  N14: U06.pin3, R40.Pin_1
  N15: U06.pin5, R41.Pin_1
  N16: U06.pin7, R42.Pin_1
  N17: U08.pin1, R9.Pin_1
  N18: U08.pin3, R8.Pin_1
  N19: U08.pin5, R7.Pin_1
  N20: U08.pin7, R6.Pin_1
  L08-10: U08.pin10, R22.pin6, U07.P3
  L08-12: U08.pin12, R22.pin5, U07.P2
  L08-14: U08.pin14, R22.pin4, U07.P1
  L08-16: U08.pin16, R22.pin3, U07.P0
  N21: U11.pin1, R4.Pin_1
  N22: U11.pin3, R3.Pin_1
  N23: U11.pin5, R2.Pin_1
  N24: U11.pin7, R1.Pin_1
  L107-10: U11.pin10, U10.P3, R21.pin6
  L107-12: U11.pin12, U10.P2, R21.pin5
  L107-14: U11.pin14, U10.P1, R21.pin4
  L107-16: U11.pin16, U10.P0, R21.pin3
  N25: U10.A2, J6.pin1, R21.pin2
  L17-16: U10.P4, U12.pin16, R25.pin6
  L17-14: U10.P5, U12.pin14, R25.pin5
  L17-12: U10.P6, U12.pin12, R25.pin4
  L17-10: U10.P7, U12.pin10, R25.pin3
  N26: U10.INT, R25.pin2
  N27: U09.pin1, R34.Pin_1
  N28: U09.pin3, R35.Pin_1
  N29: U09.pin5, R36.Pin_1
  N30: U09.pin7, R37.Pin_1
  L09-10: U09.pin10, U07.P7, R26.pin3
  L09-12: U09.pin12, U07.P6, R26.pin4
  L09-14: U09.pin14, U07.P5, R26.pin5
  L09-16: U09.pin16, U07.P4, R26.pin6
  N31: J1.pin2, R4.Pin_0, R5.pin2
  N32: J1.pin3, R3.Pin_0, R5.pin3
  N33: J1.pin4, R2.Pin_0, R5.pin4
  N34: J1.pin5, R1.Pin_0, R5.pin5
  N35: J2.pin2, R9.Pin_0, R10.pin2
  N36: J2.pin3, R8.Pin_0, R10.pin3
  N37: J2.pin4, R7.Pin_0, R10.pin4
  N38: J2.pin5, R6.Pin_0, R10.pin5
  N39: J3.pin2, R14.Pin_0, R15.pin2
  N40: J3.pin3, R13.Pin_0, R15.pin3
  N41: J3.pin4, R12.Pin_0, R15.pin4
  N42: J3.pin5, R11.Pin_0, R15.pin5
  N43: J5.pin2, R19.Pin_0, R20.pin2
  N44: J5.pin3, R18.Pin_0, R20.pin3
  N45: J5.pin4, R17.Pin_0, R20.pin4
  N46: J5.pin5, R16.Pin_0, R20.pin5
  N47: J12.pin2, R29.Pin_0, R33.pin2
  N48: J12.pin3, R30.Pin_0, R33.pin3
  N49: J12.pin4, R31.Pin_0, R33.pin4
  N50: J12.pin5, R32.Pin_0, R33.pin5
  N51: J13.pin2, R34.Pin_0, R38.pin2
  N52: J13.pin3, R35.Pin_0, R38.pin3
  N53: J13.pin4, R36.Pin_0, R38.pin4
  N54: J13.pin5, R37.Pin_0, R38.pin5
  N55: J14.pin2, R39.Pin_0, R43.pin2
  N56: J14.pin3, R40.Pin_0, R43.pin3
  N57: J14.pin4, R41.Pin_0, R43.pin4
  N58: J14.pin5, R42.Pin_0, R43.pin5
  N59: J16.pin2, R44.Pin_0, R48.pin2
  N60: J16.pin3, R45.Pin_0, R48.pin3
  N61: J16.pin4, R46.Pin_0, R48.pin4
  N62: J16.pin5, R47.Pin_0, R48.pin5
  N63: R29.Pin_1, U12.pin1
  N64: R30.Pin_1, U12.pin3
  N65: R31.Pin_1, U12.pin5
  N66: R32.Pin_1, U12.pin7
  N67: R44.Pin_1, U03.pin1
  N68: R45.Pin_1, U03.pin3
  N69: R46.Pin_1, U03.pin5
  N70: R47.Pin_1, U03.pin7
  N71: J7.pin1, R22.pin2, U07.A2
  N72: U07.INT, R26.pin2

notes:
  Svenn-Erik K. Thomsen
  sekt1953@gmail.com
  3V3
  SDA
  SCL
  GND
  TrackSensor
  TrackSensor v3.3
  https://github.com/sekt1953/Modeltog-med-Home-Assistant

custom parts:
  TLP620-4: Quad Photo-transistor optically coupled to two infrared emitting diodes connected in inverse parallel.
