# Fritzing sketch ESP32_PCF8574 (saved by Fritzing 0.9.6b)
circuit board: 7.0995cm x 9.88134cm
stripboards: 1

parts:
  U2 = PCF8574 [package="DIP16 [THT]"]
  M1 = DOIT Esp32 DevKit v1 (30 pins long, 11 pins width) [part_number=ESP32S-PIN30]
  J27 = male pin header, 3 pins [form="♂ (male)"]
  U1 = PCF8574 [package="DIP16 [THT]"]
  J23 = male pin header, 5 pins [form="♂ (male)"]
  J24 = male pin header, 5 pins [form="♂ (male)"]
  J25 = male pin header, 5 pins [form="♂ (male)"]
  J26 = male pin header, 5 pins [form="♂ (male)"]
  J34 = male pin header, 5 pins [form="♂ (male)"]
  J36 = male pin header, 5 pins [form="♂ (male)"]
  U3 = PCF8574 [package="DIP16 [THT]"]
  U4 = PCF8574 [package="DIP16 [THT]"]
  U5 = PCF8574 [package="DIP16 [THT]"]
  U6 = PCF8574 [package="DIP16 [THT]"]
  J29 = male pin header, 2 pins [form="♂ (male)"]
  J38 = male pin header, 2 pins [form="♂ (male)"]
  J41 = male pin header, 5 pins [form="♂ (male)"]
  J42 = male pin header, 5 pins [form="♂ (male)"]
  J43 = male pin header, 5 pins [form="♂ (male)"]
  J44 = male pin header, 5 pins [form="♂ (male)"]
  J45 = male pin header, 5 pins [form="♂ (male)"]
  J46 = male pin header, 5 pins [form="♂ (male)"]
  J47 = male pin header, 2 pins [form="♂ (male)"]

nets:
  3.3V: U2.A0, U2.VCC, M1.3V3, J27.pin3, U1.VCC, U3.A1, U3.VCC, U4.A0, U4.A1, U4.VCC, U5.A2, U5.VCC, U6.A0, U6.A2, U6.VCC
  GND: U2.A1, U2.A2, U2.GND, M1.GND, J27.pin2, U1.A0, U1.A1, U1.A2, U1.GND, J23.pin5, J24.pin5, J25.pin5, J26.pin5, J34.pin5, J36.pin5, U3.A0, U3.A2, U3.GND, U4.A2, U4.GND, U5.A0, U5.A1, U5.GND, U6.A1, U6.GND, J41.pin5, J42.pin5, J43.pin5, J44.pin5, J45.pin5, J46.pin5
  N1: U2.P0, J23.pin1
  N2: U2.P1, J23.pin2
  N3: U2.P2, J23.pin3
  N4: U2.P3, J23.pin4
  N5: U2.P4, J26.pin4
  N6: U2.P5, J26.pin3
  N7: U2.P6, J26.pin2
  N8: U2.P7, J26.pin1
  I2C-SCL: U2.SCL, M1.D22, U1.SCL, U3.SCL, U4.SCL, U5.SCL, U6.SCL, J29.pin2, J38.pin2, J47.pin2
  I2C-SDA: U2.SDA, M1.D21, U1.SDA, U3.SDA, U4.SDA, U5.SDA, U6.SDA, J29.pin1, J38.pin1, J47.pin1
  5V: M1.VIN, J27.pin1
  N9: U1.P0, J24.pin1
  N10: U1.P1, J24.pin2
  N11: U1.P2, J24.pin3
  N12: U1.P3, J24.pin4
  N13: U1.P4, J25.pin4
  N14: U1.P5, J25.pin3
  N15: U1.P6, J25.pin2
  N16: U1.P7, J25.pin1
  N17: J34.pin1, U3.P0
  N18: J34.pin2, U3.P1
  N19: J34.pin3, U3.P2
  N20: J34.pin4, U3.P3
  N21: J36.pin1, U3.P7
  N22: J36.pin2, U3.P6
  N23: J36.pin3, U3.P5
  N24: J36.pin4, U3.P4
  N25: U4.P0, J46.pin1
  N26: U4.P1, J46.pin2
  N27: U4.P2, J46.pin3
  N28: U4.P3, J46.pin4
  N29: U4.P4, J45.pin4
  N30: U4.P5, J45.pin3
  N31: U4.P6, J45.pin2
  N32: U4.P7, J45.pin1
  N33: U5.P0, J44.pin1
  N34: U5.P1, J44.pin2
  N35: U5.P2, J44.pin3
  N36: U5.P3, J44.pin4
  N37: U5.P4, J43.pin4
  N38: U5.P5, J43.pin3
  N39: U5.P6, J43.pin2
  N40: U5.P7, J43.pin1
  N41: U6.P0, J42.pin1
  N42: U6.P1, J42.pin2
  N43: U6.P2, J42.pin3
  N44: U6.P3, J42.pin4
  N45: U6.P4, J41.pin4
  N46: U6.P5, J41.pin3
  N47: U6.P6, J41.pin2
  N48: U6.P7, J41.pin1

notes:
  Ext. Power

custom parts:
  DOIT Esp32 DevKit v1 (30 pins long, 11 pins width): The DOIT Esp32 DevKit v1 is one of the development board created by DOIT to evaluate the ESP-WROOM-32 module. It is based on the ESP32 microcontroller that boasts Wifi, Bluetooth, Ethernet and Low Power support all in a single chip. (vanepp) made breadboard work, adjusted pin numbering and labels and reduced size of schematic and cleaned up pcb. This chip is 30pins long (2 x15) and 11 pins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
