# Fritzing sketch LED_Controler (saved by Fritzing 0.9.6b)
breadboards: 1

parts:
  R1 = Resistor [tolerance=±5% power=0.25 resistance=220 package=THT]
  LED1 = LED - 5mm [color="Red (633nm)" current=0.030 package="5 mm [THT]"]
  Q3 = PNP-Transistor [part_number=BC557 package="TO92 [THT]"]
  R3 = Resistor [tolerance=±5% power=0.25 resistance=220 package=THT]
  R4 = Resistor [tolerance=±5% power=0.25 resistance=220 package=THT]
  U2 = PCF8575C [package=so-24dw]
  R5 = Resistor [tolerance=±5% power=0.25 resistance=220 package=THT]
  LED2 = LED - 5mm [color="Red (633nm)" current=0.030 package="5 mm [THT]"]
  Q4 = PNP-Transistor [part_number=BC557 package="TO92 [THT]"]
  R6 = Resistor [tolerance=±5% power=0.25 resistance=220 package=THT]
  R7 = Resistor [tolerance=±5% power=0.25 resistance=220 package=THT]
  R8 = Resistor [tolerance=±5% power=0.25 resistance=220 package=THT]
  LED3 = LED - 5mm [color="Red (633nm)" current=0.030 package="5 mm [THT]"]
  Q5 = PNP-Transistor [part_number=BC557 package="TO92 [THT]"]
  R9 = Resistor [tolerance=±5% power=0.25 resistance=220 package=THT]
  R10 = Resistor [tolerance=±5% power=0.25 resistance=220 package=THT]
  Part1 = I2C level shifter bidirectional
  M1 = DOIT Esp32 DevKit v1 (30 pins long, 11 pins width) [part_number=ESP32S-PIN30]

nets:
  N1: R1.Pin_0, Q3.C
  N2: R1.Pin_1, LED1.anode
  GND: LED1.cathode, U2.GND, LED2.cathode, LED3.cathode, Part1.GND, M1.GND
  5V: Q3.E, R3.Pin_0, U2.VCC, R6.Pin_0, Q5.E, R9.Pin_0, Part1.HV, M1.VIN
  N3: Q3.B, R3.Pin_1, R4.Pin_0
  N4: R4.Pin_1, U2.P17
  N5: U2.P15, R10.Pin_1
  N6: U2.P16, R7.Pin_1
  scl_h: U2.SCL, Part1.HV4
  sda_h: U2.SDA, Part1.HV1
  N7: R5.Pin_0, Q4.C
  N8: R5.Pin_1, LED2.anode
  N9: Q4.B, R6.Pin_1, R7.Pin_0
  N10: R8.Pin_0, Q5.C
  N11: R8.Pin_1, LED3.anode
  N12: Q5.B, R9.Pin_1, R10.Pin_0
  sda_l: Part1.LV4, Part1.LV1, M1.D21, M1.D22
  3.3V: Part1.LV

custom parts:
  DOIT Esp32 DevKit v1 (30 pins long, 11 pins width): The DOIT Esp32 DevKit v1 is one of the development board created by DOIT to evaluate the ESP-WROOM-32 module. It is based on the ESP32 microcontroller that boasts Wifi, Bluetooth, Ethernet and Low Power support all in a single chip. (vanepp) made breadboard work, adjusted pin numbering and labels and reduced size of schematic and cleaned up pcb. This chip is 30pins long (2 x15) and 11 pins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
