# Fritzing sketch LED_Print (saved by Fritzing 0.9.6b)
stripboards: 1

parts:
  R1 = Resistor [tolerance=±5% power=0.25 resistance=220 package=THT]
  LED1 = LED - 5mm [color="Red (633nm)" current=0.030 package="5 mm [THT]"]
  R5 = Resistor [tolerance=±5% power=0.25 resistance=220 package=THT]
  LED2 = LED - 5mm [color="Red (633nm)" current=0.030 package="5 mm [THT]"]
  R8 = Resistor [tolerance=±5% power=0.25 resistance=220 package=THT]
  LED3 = LED - 5mm [color="Red (633nm)" current=0.030 package="5 mm [THT]"]
  J2 = male pin header, 1 pin [form="♂ (male)"]
  J11 = male pin header, 1 pin [form="♂ (male)"]
  J1 = male pin header, 1 pin [form="♂ (male)"]
  J12 = male pin header, 1 pin [form="♂ (male)"]
  J14 = male pin header, 1 pin [form="♂ (male)"]
  J13 = male pin header, 1 pin [form="♂ (male)"]
  Q1 = PNP-Transistor [package="TO92 [THT]"]
  Q2 = PNP-Transistor [package="TO92 [THT]"]
  Q3 = PNP-Transistor [package="TO92 [THT]"]
  Q4 = PNP-Transistor [package="TO92 [THT]"]
  J3 = male pin header, 1 pin [form="♂ (male)"]
  J4 = male pin header, 1 pin [form="♂ (male)"]
  J9 = male pin header, 1 pin [form="♂ (male)"]
  R9 = Resistor [tolerance=±5% power=0.25 resistance=22k package=THT]
  R10 = Resistor [tolerance=±5% power=0.25 resistance=22k package=THT]
  R11 = Resistor [tolerance=±5% power=0.25 resistance=22k package=THT]
  R12 = Resistor [tolerance=±5% power=0.25 resistance=22k package=THT]
  R13 = Resistor [tolerance=±5% power=0.25 resistance=10k package=THT]
  R14 = Resistor [tolerance=±5% power=0.25 resistance=10k package=THT]
  R15 = Resistor [tolerance=±5% power=0.25 resistance=10k package=THT]
  R16 = Resistor [tolerance=±5% power=0.25 resistance=10k package=THT]
  R17 = Resistor [tolerance=±5% power=0.25 resistance=220 package=THT]
  LED4 = LED - 5mm [color="Red (633nm)" current=0.030 package="5 mm [THT]"]

nets:
  N1: R1.Pin_0, J14.pin1, Q4.C
  N2: R1.Pin_1, LED1.anode
  GND: LED1.cathode, LED2.cathode, LED3.cathode, LED4.cathode
  N3: R5.Pin_0, J13.pin1, Q3.C
  N4: R5.Pin_1, LED2.anode
  N5: R8.Pin_0, J12.pin1, Q2.C
  N6: R8.Pin_1, LED3.anode
  N7: J2.pin1, R10.Pin_0
  N8: J11.pin1, Q1.C, R17.Pin_0
  N9: J1.pin1, R9.Pin_0
  3.3V: Q1.E, Q2.E, Q3.E, Q4.E, J9.pin1, R13.Pin_0, R14.Pin_0, R15.Pin_0, R16.Pin_0
  N10: Q1.B, R9.Pin_1, R13.Pin_1
  N11: Q2.B, R10.Pin_1, R14.Pin_1
  N12: Q3.B, R11.Pin_1, R15.Pin_1
  N13: Q4.B, R12.Pin_1, R16.Pin_1
  N14: J3.pin1, R11.Pin_0
  N15: J4.pin1, R12.Pin_0
  N16: R17.Pin_1, LED4.anode
