# Fritzing sketch PCB-CPU_and_Power (saved by Fritzing 0.9.6b)
stripboards: 1

parts:
  U1 = Adafruit TCA9548A
  M1 = DOIT Esp32 DevKit v1 (30 pins long, 11 pins width) [part_number=ESP32S-PIN30]
  J7 = male pin header, 4 pins [form="♂ (male)" part_number=5556-04A]
  J8 = male pin header, 4 pins [form="♂ (male)" part_number=5556-04A]
  J9 = male pin header, 4 pins [form="♂ (male)" part_number=5556-04A]
  J10 = male pin header, 4 pins [form="♂ (male)" part_number=5556-04A]
  J11 = male pin header, 4 pins [form="♂ (male)" part_number=5556-04A]
  J12 = male pin header, 4 pins [form="♂ (male)" part_number=5556-04A]
  J13 = male pin header, 2 pins [form="♂ (male)" part_number=5556-02A]
  M2 = IC, SIP package, 4 pins [chip_label=OE-SD part_number=OE-SD28V]
  J14 = male pin header, 2 pins [form="♂ (male)" part_number=5501]
  J15 = male pin header, 2 pins [form="♂ (male)" part_number=5501]
  J16 = male pin header, 2 pins [form="♂ (male)" part_number=5501]
  J17 = male pin header, 2 pins [form="♂ (male)" part_number=5501]
  J18 = male pin header, 2 pins [form="♂ (male)" part_number=5501]
  J19 = male pin header, 2 pins [form="♂ (male)" part_number=5501]
  J20 = male pin header, 12 pins [form="♂ (male)" part_number=5501]
  J21 = male pin header, 2 pins [form="♂ (male)" part_number=5501]
  J22 = male pin header, 1 pin [form="♂ (male)" part_number=5501]
  J23 = male pin header, 1 pin [form="♂ (male)" part_number=5501]
  R1 = Resistor [tolerance=±5% power=0.25 resistance=10k package=THT]

nets:
  I2C_02SDA: U1.2SDA, J12.pin2, J19.pin1, J20.pin12
  I2C_02SCL: U1.2SCL, J12.pin3, J19.pin2, J20.pin11
  I2C_03SDA: U1.3SDA, J11.pin2, J18.pin1, J20.pin10
  I2C_03SCL: U1.3SCL, J11.pin3, J18.pin2, J20.pin9
  I2C_04SDA: U1.4SDA, J10.pin2, J17.pin1, J20.pin8
  I2C_04SCL: U1.4SCL, J10.pin3, J17.pin2, J20.pin7
  I2C_05SDA: U1.5SDA, J9.pin2, J16.pin1, J20.pin6
  I2C_05SCL: U1.5SCL, J9.pin3, J16.pin2, J20.pin5
  I2C_06SDA: U1.6SDA, J8.pin2, J15.pin1, J20.pin4
  I2C_06SCL: U1.6SCL, J8.pin3, J15.pin2, J20.pin3
  I2C_07SDA: U1.7SDA, J7.pin2, J14.pin1, J20.pin2
  I2C_07SCL: U1.7SCL, J7.pin3, J14.pin2, J20.pin1
  3.3V: U1.VCC, M1.3V3, J7.pin1, J8.pin1, J9.pin1, J10.pin1, J11.pin1, J12.pin1, M2.pin4, R1.Pin_0
  GND: U1.GND, U1.A0, U1.A1, U1.A2, M1.GND, J7.pin4, J8.pin4, J9.pin4, J10.pin4, J11.pin4, J12.pin4, J13.pin2, M2.pin3
  I2C_SDA: U1.INPUTSDA, M1.D21, J21.pin2, J23.pin1
  I2C_SCL: U1.INPUTSCL, M1.D22, J21.pin1, J22.pin1
  N1: U1.RESET, R1.Pin_1
  5V: M1.VIN
  12V: J13.pin1, M2.pin2

custom parts:
  Adafruit TCA9548A: You just found the perfect I2C sensor, and you want to wire up two or three or more of them to your Arduino when you realize "Uh oh, this chip has a fixed I2C address, and from what I know about I2C, you cannot have two devices with the same address on the same SDA/SCL pins!" Are you out of luck? You would be, if you didn't have this ultra-cool TCA9548A 1-to-8 I2C multiplexer! Finally, a way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
  DOIT Esp32 DevKit v1 (30 pins long, 11 pins width): The DOIT Esp32 DevKit v1 is one of the development board created by DOIT to evaluate the ESP-WROOM-32 module. It is based on the ESP32 microcontroller that boasts Wifi, Bluetooth, Ethernet and Low Power support all in a single chip. (vanepp) made breadboard work, adjusted pin numbering and labels and reduced size of schematic and cleaned up pcb. This chip is 30pins long (2 x15) and 11 pins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
