# Fritzing sketch PCB-CPU_and_Power_002 (saved by Fritzing 0.9.6b)
circuit board: 6.9cm x 10cm
breadboards: 1

parts:
  J1 = male pin header, 15 pins [form="♂ (male)"]
  J2 = male pin header, 15 pins [form="♂ (male)"]
  J3 = male pin header, 15 pins [form="♂ (male)"]
  J4 = male pin header, 15 pins [form="♂ (male)"]
  J5 = male pin header, 15 pins [form="♂ (male)"]
  J6 = male pin header, 15 pins [form="♂ (male)"]
  I2C = male pin header, 4 pins [form="♂ (male)"]
  ESP32_30Pin = DOIT Esp32 DevKit v1 (30 pins long, 11 pins width) [part_number=ESP32S-PIN30]
  J11 = female pin header, 15 pins [form="♀ (female)"]
  J12 = female pin header, 15 pins [form="♀ (female)"]
  LED1 = LED - 5mm [color="Red (633nm)" current=0.030 package="5 mm [THT]"]
  R1 = Resistor [tolerance=±5% power=0.25 resistance=220 package=THT]
  LED2 = LED - 5mm [color="Red (633nm)" current=0.030 package="5 mm [THT]"]
  LED3 = LED - 5mm [color="Red (633nm)" current=0.030 package="5 mm [THT]"]
  LED4 = LED - 5mm [color="Red (633nm)" current=0.030 package="5 mm [THT]"]
  R2 = Resistor [tolerance=±5% power=0.25 resistance=220 package=THT]
  R3 = Resistor [tolerance=±5% power=0.25 resistance=220 package=THT]
  R4 = Resistor [tolerance=±5% power=0.25 resistance=220 package=THT]
  S1 = Pushbutton [package=THT]
  S2 = Pushbutton [package=THT]
  S3 = Pushbutton [package=THT]
  S4 = Pushbutton [package=THT]
  J13 = male pin header, 2 pins [form="♂ (male)"]
  J14 = male pin header, 2 pins [form="♂ (male)"]
  J15 = male pin header, 2 pins [form="♂ (male)"]
  J16 = male pin header, 2 pins [form="♂ (male)"]
  J17 = male pin header, 2 pins [form="♂ (male)"]
  J18 = male pin header, 2 pins [form="♂ (male)"]
  J19 = male pin header, 2 pins [form="♂ (male)"]
  J20 = male pin header, 2 pins [form="♂ (male)"]
  HW-613 = male pin header, 4 pins [form="♂ (male)"]
  Power = male pin header, 3 pins [form="♂ (male)"]
  D1 = Rectifier Diode [part_number=1N4001 package="300 mil [THT]"]
  J22 = female pin header, 3 pins [form="♀ (female)"]

nets:
  3.3V: J1.pin1, J2.pin1, J3.pin1, I2C.pin1, ESP32_30Pin.3V3, J11.pin1, R1.Pin_1, R2.Pin_1, R3.Pin_1, R4.Pin_1, HW-613.pin4, J22.pin1, J22.pin2
  GND: J1.pin2, J2.pin2, J3.pin2, J4.pin2, J5.pin2, J6.pin2, I2C.pin4, ESP32_30Pin.GND, J11.pin2, J12.pin2, S1.leg0, S2.leg0, S3.leg0, S4.leg0, HW-613.pin3, Power.pin3
  N1: J1.pin3, J2.pin3, J3.pin3, ESP32_30Pin.D15, J11.pin3
  N2: J1.pin4, J2.pin4, J3.pin4, ESP32_30Pin.D2, J11.pin4
  N3: J1.pin5, J2.pin5, J3.pin5, ESP32_30Pin.D4, J11.pin5
  N4: J1.pin6, J2.pin6, J3.pin6, ESP32_30Pin.RX2, J11.pin6
  N5: J1.pin7, J2.pin7, J3.pin7, ESP32_30Pin.TX2, J11.pin7
  N6: J1.pin8, J2.pin8, J3.pin8, ESP32_30Pin.D5, J11.pin8
  N7: J1.pin9, J2.pin9, J3.pin9, ESP32_30Pin.D18, J11.pin9
  N8: J1.pin10, J2.pin10, J3.pin10, ESP32_30Pin.D19, J11.pin10
  N9: J1.pin11, J2.pin11, J3.pin11, I2C.pin2, ESP32_30Pin.D21, J11.pin11
  N10: J1.pin12, J2.pin12, J3.pin12, ESP32_30Pin.RX0, J11.pin12
  N11: J1.pin13, J2.pin13, J3.pin13, ESP32_30Pin.TX0, J11.pin13
  N12: J1.pin14, J2.pin14, J3.pin14, I2C.pin3, ESP32_30Pin.D22, J11.pin14
  N13: J1.pin15, J2.pin15, J3.pin15, ESP32_30Pin.D23, J11.pin15
  5V: J4.pin1, J5.pin1, J6.pin1, ESP32_30Pin.VIN, J12.pin1, J22.pin3
  N14: J4.pin3, J5.pin3, J6.pin3, ESP32_30Pin.D13, J12.pin3
  N15: J4.pin4, J5.pin4, J6.pin4, ESP32_30Pin.D12, J12.pin4
  N16: J4.pin5, J5.pin5, J6.pin5, ESP32_30Pin.D14, J12.pin5
  N17: J4.pin6, J5.pin6, J6.pin6, ESP32_30Pin.D27, J12.pin6
  N18: J4.pin7, J5.pin7, J6.pin7, ESP32_30Pin.D26, J12.pin7
  N19: J4.pin8, J5.pin8, J6.pin8, ESP32_30Pin.D25, J12.pin8
  N20: J4.pin9, J5.pin9, J6.pin9, ESP32_30Pin.D33, J12.pin9
  N21: J4.pin10, J5.pin10, J6.pin10, ESP32_30Pin.D32, J12.pin10
  N22: J4.pin11, J5.pin11, J6.pin11, ESP32_30Pin.D35, J12.pin11
  N23: J4.pin12, J5.pin12, J6.pin12, ESP32_30Pin.D34, J12.pin12
  N24: J4.pin13, J5.pin13, J6.pin13, ESP32_30Pin.VN, J12.pin13
  N25: J4.pin14, J5.pin14, J6.pin14, ESP32_30Pin.VP, J12.pin14
  N26: J4.pin15, J5.pin15, J6.pin15, ESP32_30Pin.EN, J12.pin15
  N27: LED1.cathode, J13.pin1, J13.pin2
  N28: LED1.anode, R1.Pin_0
  N29: LED2.cathode, J14.pin1, J14.pin2
  N30: LED2.anode, R2.Pin_0
  N31: LED3.cathode, J15.pin1, J15.pin2
  N32: LED3.anode, R3.Pin_0
  N33: LED4.cathode, J16.pin1, J16.pin2
  N34: LED4.anode, R4.Pin_0
  N35: S1.leg1, J17.pin1, J17.pin2
  N36: S2.leg1, J18.pin1, J18.pin2
  N37: S3.leg1, J19.pin1, J19.pin2
  N38: S4.leg1, J20.pin1, J20.pin2
  N39: HW-613.pin2, D1.cathode
  N40: Power.pin2, D1.anode

notes:
  GND
  +24V
  +3,3V
  Vin
  EN
  HW-613

custom parts:
  DOIT Esp32 DevKit v1 (30 pins long, 11 pins width): The DOIT Esp32 DevKit v1 is one of the development board created by DOIT to evaluate the ESP-WROOM-32 module. It is based on the ESP32 microcontroller that boasts Wifi, Bluetooth, Ethernet and Low Power support all in a single chip. (vanepp) made breadboard work, adjusted pin numbering and labels and reduced size of schematic and cleaned up pcb. This chip is 30pins long (2 x15) and 11 pins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
