# Fritzing sketch PCB-CPU_and_Power_2xI2C (saved by Fritzing 0.9.6b)
circuit board: 5.87332cm x 5.47394cm
stripboards: 1

parts:
  M1 = DOIT Esp32 DevKit v1 (30 pins long, 11 pins width) [part_number=ESP32S-PIN30]
  J1 = male pin header, 3 pins [form="♂ (male)"]
  J2 = male pin header, 4 pins [form="♂ (male)"]
  J3 = male pin header, 4 pins [form="♂ (male)"]
  HW613 = female pin header, 4 pins [form="♀ (female)"]
  J8 = female pin header, 15 pins [form="♀ (female)"]
  J9 = female pin header, 15 pins [form="♀ (female)"]
  J10 = male pin header, 15 pins [form="♂ (male)"]
  J11 = male pin header, 15 pins [form="♂ (male)"]
  J12 = male pin header, 15 pins [form="♂ (male)"]
  J13 = male pin header, 15 pins [form="♂ (male)"]

nets:
  3.3V: M1.3V3, J2.pin1, J3.pin1, HW613.pin4, J9.pin1, J10.pin1, J11.pin1
  GND: M1.GND, J1.pin3, J2.pin4, J3.pin4, HW613.pin3, J8.pin2, J9.pin2, J10.pin2, J11.pin2, J12.pin2, J13.pin2
  N1: M1.D15, J9.pin3, J10.pin3, J11.pin3
  N2: M1.D2, J9.pin4, J10.pin4, J11.pin4
  N3: M1.D4, J9.pin5, J10.pin5, J11.pin5
  I2C_SCL2: M1.RX2, J3.pin3, J9.pin6, J10.pin6, J11.pin6
  I2C_SDA2: M1.TX2, J3.pin2, J9.pin7, J10.pin7, J11.pin7
  N4: M1.D5, J9.pin8, J10.pin8, J11.pin8
  N5: M1.D18, J9.pin9, J10.pin9, J11.pin9
  N6: M1.D19, J9.pin10, J10.pin10, J11.pin10
  I2C_SDA1: M1.D21, J2.pin2, J9.pin11, J10.pin11, J11.pin11
  N7: M1.RX0, J9.pin12, J10.pin12, J11.pin12
  N8: M1.TX0, J9.pin13, J10.pin13, J11.pin13
  I2C_SCL1: M1.D22, J2.pin3, J9.pin14, J10.pin14, J11.pin14
  N9: M1.D23, J9.pin15, J10.pin15, J11.pin15
  N10: M1.EN, J8.pin15, J12.pin15, J13.pin15
  N11: M1.VP, J8.pin14, J12.pin14, J13.pin14
  N12: M1.VN, J8.pin13, J12.pin13, J13.pin13
  N13: M1.D34, J8.pin12, J12.pin12, J13.pin12
  N14: M1.D35, J8.pin11, J12.pin11, J13.pin11
  N15: M1.D32, J8.pin10, J12.pin10, J13.pin10
  N16: M1.D33, J8.pin9, J12.pin9, J13.pin9
  N17: M1.D25, J8.pin8, J12.pin8, J13.pin8
  N18: M1.D26, J8.pin7, J12.pin7, J13.pin7
  N19: M1.D27, J8.pin6, J12.pin6, J13.pin6
  N20: M1.D14, J8.pin5, J12.pin5, J13.pin5
  N21: M1.D12, J8.pin4, J12.pin4, J13.pin4
  N22: M1.D13, J8.pin3, J12.pin3, J13.pin3
  N23: M1.VIN, J8.pin1, J12.pin1, J13.pin1
  N24: J1.pin1, HW613.pin1
  N25: J1.pin2, HW613.pin2

notes:
  Extern power
  GND
  12-24V
  SDA1
  SCL1
  SDA2
  SCL2
  3V3
  I2C Bus A
  I2C Bus B

custom parts:
  DOIT Esp32 DevKit v1 (30 pins long, 11 pins width): The DOIT Esp32 DevKit v1 is one of the development board created by DOIT to evaluate the ESP-WROOM-32 module. It is based on the ESP32 microcontroller that boasts Wifi, Bluetooth, Ethernet and Low Power support all in a single chip. (vanepp) made breadboard work, adjusted pin numbering and labels and reduced size of schematic and cleaned up pcb. This chip is 30pins long (2 x15) and 11 pins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
