# Fritzing sketch PCB-CPU_and_Power_2xI2C_002 (saved by Fritzing 0.9.6b)
circuit board: 5.12849cm x 5.47394cm
stripboards: 1

parts:
  J1 = male pin header, 3 pins [form="♂ (male)"]
  I2C = male pin header, 4 pins [form="♂ (male)"]
  HW613 = female pin header, 4 pins [form="♀ (female)"]
  J8 = female pin header, 15 pins [form="♀ (female)"]
  J9 = female pin header, 15 pins [form="♀ (female)"]
  J10 = male pin header, 15 pins [form="♂ (male)"]
  J11 = male pin header, 15 pins [form="♂ (male)"]
  J12 = male pin header, 15 pins [form="♂ (male)"]
  J13 = male pin header, 15 pins [form="♂ (male)"]
  D1 = Rectifier Diode [part_number=1N4001 package="300 mil [THT]"]

nets:
  N1: J1.pin2, D1.anode
  GND: J1.pin3, I2C.pin4, HW613.pin3, J9.pin2, J10.pin2, J11.pin2
  3.3V: I2C.pin1, HW613.pin4, J9.pin1, J10.pin1, J11.pin1
  I2C_SDA1: I2C.pin2, J9.pin11, J10.pin11, J11.pin11
  I2C_SCL1: I2C.pin3, J9.pin14, J10.pin14, J11.pin14
  N2: HW613.pin2, D1.cathode
  N3: J8.pin1, J12.pin1, J13.pin1
  N4: J8.pin2, J12.pin2, J13.pin2
  N5: J8.pin3, J12.pin3, J13.pin3
  N6: J8.pin4, J12.pin4, J13.pin4
  N7: J8.pin5, J12.pin5, J13.pin5
  N8: J8.pin6, J12.pin6, J13.pin6
  N9: J8.pin7, J12.pin7, J13.pin7
  N10: J8.pin8, J12.pin8, J13.pin8
  N11: J8.pin9, J12.pin9, J13.pin9
  N12: J8.pin10, J12.pin10, J13.pin10
  N13: J8.pin11, J12.pin11, J13.pin11
  N14: J8.pin12, J12.pin12, J13.pin12
  N15: J8.pin13, J12.pin13, J13.pin13
  N16: J8.pin14, J12.pin14, J13.pin14
  N17: J8.pin15, J12.pin15, J13.pin15
  N18: J9.pin3, J10.pin3, J11.pin3
  N19: J9.pin4, J10.pin4, J11.pin4
  N20: J9.pin5, J10.pin5, J11.pin5
  N21: J9.pin6, J10.pin6, J11.pin6
  N22: J9.pin7, J10.pin7, J11.pin7
  N23: J9.pin8, J10.pin8, J11.pin8
  N24: J9.pin9, J10.pin9, J11.pin9
  N25: J9.pin10, J10.pin10, J11.pin10
  N26: J9.pin12, J10.pin12, J11.pin12
  N27: J9.pin13, J10.pin13, J11.pin13
  N28: J9.pin15, J10.pin15, J11.pin15

notes:
  Extern power
  GND
  12-24V
  SDA1
  SCL1
  SDA2
  SCL2
  3V3
  I2C Bus A
  I2C Bus B
  sekt1953@gmail.com
  https://github.com/sekt1953
  ESP32 30Pin
