# Fritzing sketch PCB-LedDriver (saved by Fritzing 0.9.6b)
stripboards: 1

parts:
  U1 = PCF8574 [package="DIP16 [THT]"]
  U2 = Sharp PC847X [package=THT]
  U3 = Sharp PC847X [package=THT]
  R1 = Resistor [tolerance=±5% power=0.25 resistance=330 package=THT]
  J1 = male pin header, 2 pins [form="♂ (male)"]
  J2 = male pin header, 2 pins [form="♂ (male)"]
  J3 = male pin header, 2 pins [form="♂ (male)"]
  R2 = Resistor [tolerance=±5% power=0.25 resistance=100 package=THT]
  R3 = Resistor [tolerance=±5% power=0.25 resistance=100 package=THT]
  J4 = male pin header, 1 pin [form="♂ (male)"]
  J5 = male pin header, 1 pin [form="♂ (male)"]
  J6 = male pin header, 1 pin [form="♂ (male)"]
  J7 = male pin header, 1 pin [form="♂ (male)"]
  J8 = male pin header, 1 pin [form="♂ (male)"]
  J9 = male pin header, 1 pin [form="♂ (male)"]
  J10 = male pin header, 1 pin [form="♂ (male)"]
  J11 = male pin header, 1 pin [form="♂ (male)"]
  J12 = male pin header, 1 pin [form="♂ (male)"]
  J13 = male pin header, 1 pin [form="♂ (male)"]
  J14 = male pin header, 1 pin [form="♂ (male)"]
  J15 = male pin header, 1 pin [form="♂ (male)"]
  J16 = male pin header, 1 pin [form="♂ (male)"]
  J17 = male pin header, 1 pin [form="♂ (male)"]
  J18 = male pin header, 1 pin [form="♂ (male)"]
  J19 = male pin header, 1 pin [form="♂ (male)"]
  R4 = Resistor [tolerance=±5% power=0.25 resistance=100 package=THT]
  R5 = Resistor [tolerance=±5% power=0.25 resistance=100 package=THT]
  R6 = Resistor [tolerance=±5% power=0.25 resistance=100 package=THT]
  R7 = Resistor [tolerance=±5% power=0.25 resistance=100 package=THT]
  R8 = Resistor [tolerance=±5% power=0.25 resistance=100 package=THT]
  R9 = Resistor [tolerance=±5% power=0.25 resistance=100 package=THT]
  J20 = male pin header, 4 pins [form="♂ (male)"]
  R10 = Resistor [tolerance=±5% power=0.25 resistance=330 package=THT]
  J21 = male pin header, 4 pins [form="♂ (male)"]
  R11 = Resistor [tolerance=±5% power=0.25 resistance=330 package=THT]
  R12 = Resistor [tolerance=±5% power=0.25 resistance=330 package=THT]
  R13 = Resistor [tolerance=±5% power=0.25 resistance=330 package=THT]
  R14 = Resistor [tolerance=±5% power=0.25 resistance=330 package=THT]
  R15 = Resistor [tolerance=±5% power=0.25 resistance=330 package=THT]
  R16 = Resistor [tolerance=±5% power=0.25 resistance=330 package=THT]
  J22 = male pin header, 9 pins [form="♂ (male)"]
  J23 = male pin header, 4 pins [form="♂ (male)"]
  U4 = Sharp PC847X [package=THT]
  U5 = PCF8574 [package="DIP16 [THT]"]
  U6 = Sharp PC847X [package=THT]
  R17 = Resistor [tolerance=±5% power=0.25 resistance=330 package=THT]
  R18 = Resistor [tolerance=±5% power=0.25 resistance=330 package=THT]
  R19 = Resistor [tolerance=±5% power=0.25 resistance=100 package=THT]
  R20 = Resistor [tolerance=±5% power=0.25 resistance=330 package=THT]
  R21 = Resistor [tolerance=±5% power=0.25 resistance=330 package=THT]
  R22 = Resistor [tolerance=±5% power=0.25 resistance=330 package=THT]
  R23 = Resistor [tolerance=±5% power=0.25 resistance=100 package=THT]
  R24 = Resistor [tolerance=±5% power=0.25 resistance=100 package=THT]
  R25 = Resistor [tolerance=±5% power=0.25 resistance=330 package=THT]
  R26 = Resistor [tolerance=±5% power=0.25 resistance=330 package=THT]
  R27 = Resistor [tolerance=±5% power=0.25 resistance=100 package=THT]
  R28 = Resistor [tolerance=±5% power=0.25 resistance=100 package=THT]
  R29 = Resistor [tolerance=±5% power=0.25 resistance=100 package=THT]
  R30 = Resistor [tolerance=±5% power=0.25 resistance=100 package=THT]
  R31 = Resistor [tolerance=±5% power=0.25 resistance=330 package=THT]
  R32 = Resistor [tolerance=±5% power=0.25 resistance=100 package=THT]
  J24 = male pin header, 2 pins [form="♂ (male)"]
  J25 = male pin header, 2 pins [form="♂ (male)"]
  J26 = male pin header, 2 pins [form="♂ (male)"]
  J27 = male pin header, 1 pin [form="♂ (male)"]
  J28 = male pin header, 1 pin [form="♂ (male)"]
  J29 = male pin header, 1 pin [form="♂ (male)"]
  J30 = male pin header, 1 pin [form="♂ (male)"]
  J31 = male pin header, 1 pin [form="♂ (male)"]
  J32 = male pin header, 1 pin [form="♂ (male)"]
  J33 = male pin header, 1 pin [form="♂ (male)"]
  J34 = male pin header, 1 pin [form="♂ (male)"]
  J35 = male pin header, 1 pin [form="♂ (male)"]
  J36 = male pin header, 1 pin [form="♂ (male)"]
  J37 = male pin header, 1 pin [form="♂ (male)"]
  J38 = male pin header, 1 pin [form="♂ (male)"]
  J39 = male pin header, 1 pin [form="♂ (male)"]
  J40 = male pin header, 1 pin [form="♂ (male)"]
  J41 = male pin header, 1 pin [form="♂ (male)"]
  J42 = male pin header, 1 pin [form="♂ (male)"]
  J43 = male pin header, 4 pins [form="♂ (male)"]
  J44 = male pin header, 4 pins [form="♂ (male)"]
  J45 = male pin header, 9 pins [form="♂ (male)"]
  U7 = PCF8574 [package="DIP16 [THT]"]
  U8 = Sharp PC847X [package=THT]
  U9 = Sharp PC847X [package=THT]
  R33 = Resistor [tolerance=±5% power=0.25 resistance=330 package=THT]
  R34 = Resistor [tolerance=±5% power=0.25 resistance=100 package=THT]
  R35 = Resistor [tolerance=±5% power=0.25 resistance=330 package=THT]
  R36 = Resistor [tolerance=±5% power=0.25 resistance=100 package=THT]
  R37 = Resistor [tolerance=±5% power=0.25 resistance=100 package=THT]
  R38 = Resistor [tolerance=±5% power=0.25 resistance=330 package=THT]
  R39 = Resistor [tolerance=±5% power=0.25 resistance=330 package=THT]
  R40 = Resistor [tolerance=±5% power=0.25 resistance=100 package=THT]
  R41 = Resistor [tolerance=±5% power=0.25 resistance=330 package=THT]
  R42 = Resistor [tolerance=±5% power=0.25 resistance=330 package=THT]
  R43 = Resistor [tolerance=±5% power=0.25 resistance=330 package=THT]
  R44 = Resistor [tolerance=±5% power=0.25 resistance=100 package=THT]
  R45 = Resistor [tolerance=±5% power=0.25 resistance=100 package=THT]
  R46 = Resistor [tolerance=±5% power=0.25 resistance=100 package=THT]
  R47 = Resistor [tolerance=±5% power=0.25 resistance=330 package=THT]
  R48 = Resistor [tolerance=±5% power=0.25 resistance=330 package=THT]
  J46 = male pin header, 2 pins [form="♂ (male)"]
  J47 = male pin header, 2 pins [form="♂ (male)"]
  J48 = male pin header, 2 pins [form="♂ (male)"]
  J49 = male pin header, 1 pin [form="♂ (male)"]
  J50 = male pin header, 1 pin [form="♂ (male)"]
  J51 = male pin header, 1 pin [form="♂ (male)"]
  J52 = male pin header, 1 pin [form="♂ (male)"]
  J53 = male pin header, 1 pin [form="♂ (male)"]
  J54 = male pin header, 1 pin [form="♂ (male)"]
  J55 = male pin header, 1 pin [form="♂ (male)"]
  J56 = male pin header, 1 pin [form="♂ (male)"]
  J57 = male pin header, 1 pin [form="♂ (male)"]
  J58 = male pin header, 1 pin [form="♂ (male)"]
  J59 = male pin header, 1 pin [form="♂ (male)"]
  J60 = male pin header, 1 pin [form="♂ (male)"]
  J61 = male pin header, 1 pin [form="♂ (male)"]
  J62 = male pin header, 1 pin [form="♂ (male)"]
  J63 = male pin header, 1 pin [form="♂ (male)"]
  J64 = male pin header, 1 pin [form="♂ (male)"]
  J65 = male pin header, 4 pins [form="♂ (male)"]
  J66 = male pin header, 4 pins [form="♂ (male)"]
  J67 = male pin header, 9 pins [form="♂ (male)"]
  LED1 = RGB LED (com. cathode, rgb) [package="5 mm [THT]"]
  Power_12V = Power plug
  J68 = male pin header, 8 pins [form="♂ (male)"]
  J69 = male pin header, 8 pins [form="♂ (male)"]
  J70 = male pin header, 8 pins [form="♂ (male)"]
  R49 = Resistor [tolerance=±5% power=0.25 resistance=2.2k package=THT]
  R50 = Resistor [tolerance=±5% power=0.25 resistance=2.2k package=THT]
  R51 = Resistor [tolerance=±5% power=0.25 resistance=2.2k package=THT]
  R52 = Resistor [tolerance=±5% power=0.25 resistance=2.2k package=THT]
  R53 = Resistor [tolerance=±5% power=0.25 resistance=2.2k package=THT]
  R54 = Resistor [tolerance=±5% power=0.25 resistance=2.2k package=THT]
  R55 = Resistor [tolerance=±5% power=0.25 resistance=2.2k package=THT]
  R56 = Resistor [tolerance=±5% power=0.25 resistance=2.2k package=THT]
  R57 = Resistor [tolerance=±5% power=0.25 resistance=2.2k package=THT]
  J71 = male pin header, 4 pins [form="♂ (male)"]

nets:
  N1: U1.A0, J1.pin2, R49.Pin_1
  N2: U1.A1, J2.pin2, R50.Pin_1
  N3: U1.A2, J26.pin2, R51.Pin_1
  net JP00: U1.P0, U3.Pin_8, J8.pin1, J20.pin1
  net JP01: U1.P1, U3.Pin_6, J9.pin1, J20.pin2
  net JP02: U1.P2, U3.Pin_4, J11.pin1, J20.pin3
  net JP03: U1.P3, U3.Pin_2, J10.pin1, J20.pin4
  GND: U1.GND, J1.pin1, J2.pin1, J3.pin1, J23.pin4, U5.GND, J24.pin1, J25.pin1, J26.pin1, U7.GND, J46.pin1, J47.pin1, J48.pin1, J71.pin4
  net JP04: U1.P4, U2.Pin_8, J16.pin1, J21.pin4
  net JP05: U1.P5, U2.Pin_6, J17.pin1, J21.pin3
  net JP06: U1.P6, U2.Pin_4, J19.pin1, J21.pin2
  net JP07: U1.P7, U2.Pin_2, J18.pin1, J21.pin1
  I2C_SCL: U1.SCL, J23.pin3, U5.SCL, U7.SCL, J71.pin3
  I2C_SDA: U1.SDA, J23.pin2, U5.SDA, U7.SDA, J71.pin2
  3.3V: U1.VCC, R2.Pin_1, R3.Pin_1, R4.Pin_1, R5.Pin_1, R6.Pin_1, R7.Pin_1, R8.Pin_1, R9.Pin_1, J23.pin1, U5.VCC, R19.Pin_1, R23.Pin_1, R24.Pin_1, R27.Pin_1, R28.Pin_1, R29.Pin_1, R30.Pin_1, R32.Pin_1, U7.VCC, R34.Pin_1, R36.Pin_1, R37.Pin_1, R40.Pin_1, R42.Pin_1, R44.Pin_1, R45.Pin_1, R46.Pin_1, R49.Pin_0, R50.Pin_0, R51.Pin_0, R52.Pin_0, R53.Pin_0, R54.Pin_0, R55.Pin_0, R56.Pin_0, R57.Pin_0, J71.pin1
  N4: U2.Pin_1, R9.Pin_0
  N5: U2.Pin_3, R8.Pin_0
  N6: U2.Pin_5, R7.Pin_0
  N7: U2.Pin_7, R3.Pin_0
  N8: U2.Pin_9, J12.pin1, R13.Pin_1, J68.pin5
  N9: U2.Pin_10, U2.Pin_12, U2.Pin_14, U2.Pin_16, U3.Pin_10, U3.Pin_12, U3.Pin_14, U3.Pin_16, J22.pin9, Power_12V.VCC
  N10: U2.Pin_11, J13.pin1, R14.Pin_1, J68.pin6
  N11: U2.Pin_13, J15.pin1, R15.Pin_1, J68.pin7
  N12: U2.Pin_15, J14.pin1, R16.Pin_1, J68.pin8
  N13: U3.Pin_1, R6.Pin_0
  N14: U3.Pin_3, R5.Pin_0
  N15: U3.Pin_5, R4.Pin_0
  N16: U3.Pin_7, R2.Pin_0
  N17: U3.Pin_9, R1.Pin_1, J4.pin1, J68.pin1
  N18: U3.Pin_11, J5.pin1, R10.Pin_1, J68.pin2
  N19: U3.Pin_13, J6.pin1, R11.Pin_1, J68.pin3
  N20: U3.Pin_15, J7.pin1, R12.Pin_1, J68.pin4
  N21: R1.Pin_0, J22.pin1, LED1.blue_anode
  N22: J3.pin2, U5.A1, R53.Pin_1
  N23: R10.Pin_0, J22.pin2, LED1.green_anode
  N24: R11.Pin_0, J22.pin3, LED1.red_anode
  N25: R12.Pin_0, J22.pin4
  N26: R13.Pin_0, J22.pin5
  N27: R14.Pin_0, J22.pin6
  N28: R15.Pin_0, J22.pin7
  N29: R16.Pin_0, J22.pin8
  N30: U4.Pin_1, R24.Pin_0
  net JP17: U4.Pin_2, U5.P7, J42.pin1, J44.pin1
  N31: U4.Pin_3, R28.Pin_0
  N32: U4.Pin_4, J36.pin1
  N33: U4.Pin_5, R23.Pin_0
  N34: U4.Pin_6, J34.pin1
  N35: U4.Pin_7, R29.Pin_0
  N36: U4.Pin_8, J37.pin1
  N37: U4.Pin_9, R26.Pin_1, J32.pin1, J69.pin5
  N38: U4.Pin_10, U4.Pin_12, U4.Pin_14, U4.Pin_16, U6.Pin_10, U6.Pin_12, U6.Pin_14, U6.Pin_16, J45.pin9
  N39: U4.Pin_11, R31.Pin_1, J27.pin1, J69.pin6
  N40: U4.Pin_13, R18.Pin_1, J39.pin1, J69.pin7
  N41: U4.Pin_15, R20.Pin_1, J30.pin1, J69.pin8
  N42: U5.A0, J25.pin2, R52.Pin_1
  N43: U5.A2, J24.pin2, R54.Pin_1
  N44: U5.P0, J43.pin1
  N45: U5.P1, J43.pin2
  N46: U5.P2, J43.pin3
  N47: U5.P3, J43.pin4
  N48: U5.P4, J44.pin4
  N49: U5.P5, J44.pin3
  N50: U5.P6, J44.pin2
  N51: U6.Pin_1, R19.Pin_0
  N52: U6.Pin_2, J35.pin1
  N53: U6.Pin_3, R32.Pin_0
  N54: U6.Pin_4, J28.pin1
  N55: U6.Pin_5, R30.Pin_0
  N56: U6.Pin_6, J38.pin1
  N57: U6.Pin_7, R27.Pin_0
  N58: U6.Pin_8, J41.pin1
  N59: U6.Pin_9, R17.Pin_1, J29.pin1, J69.pin1
  N60: U6.Pin_11, R21.Pin_1, J33.pin1, J69.pin2
  N61: U6.Pin_13, R22.Pin_1, J31.pin1, J69.pin3
  N62: U6.Pin_15, R25.Pin_1, J40.pin1, J69.pin4
  N63: R17.Pin_0, J45.pin1
  N64: R18.Pin_0, J45.pin7
  N65: R20.Pin_0, J45.pin8
  N66: R21.Pin_0, J45.pin2
  N67: R22.Pin_0, J45.pin3
  N68: R25.Pin_0, J45.pin4
  N69: R26.Pin_0, J45.pin5
  N70: R31.Pin_0, J45.pin6
  N71: U7.A0, J47.pin2, R55.Pin_1
  N72: U7.A1, J48.pin2, R56.Pin_1
  N73: U7.A2, J46.pin2, R57.Pin_1
  N74: U7.P0, J65.pin1
  N75: U7.P1, J65.pin2
  N76: U7.P2, J65.pin3
  N77: U7.P3, J65.pin4
  N78: U7.P4, J66.pin4
  N79: U7.P5, J66.pin3
  N80: U7.P6, J66.pin2
  N81: U7.P7, J66.pin1
  N82: U8.Pin_1, R44.Pin_0
  N83: U8.Pin_2, J64.pin1
  N84: U8.Pin_3, R45.Pin_0
  N85: U8.Pin_4, J61.pin1
  N86: U8.Pin_5, R40.Pin_0
  N87: U8.Pin_6, J49.pin1
  N88: U8.Pin_7, R36.Pin_0
  N89: U8.Pin_8, J55.pin1
  N90: U8.Pin_9, R43.Pin_1, J56.pin1, J70.pin5
  N91: U8.Pin_10, U8.Pin_12, U8.Pin_14, U8.Pin_16, U9.Pin_10, U9.Pin_12, U9.Pin_14, U9.Pin_16, J67.pin9
  N92: U8.Pin_11, R35.Pin_1, J62.pin1, J70.pin6
  N93: U8.Pin_13, R47.Pin_1, J51.pin1, J70.pin7
  N94: U8.Pin_15, R48.Pin_1, J58.pin1, J70.pin8
  N95: U9.Pin_1, R34.Pin_0
  N96: U9.Pin_2, J60.pin1
  N97: U9.Pin_3, R37.Pin_0
  N98: U9.Pin_4, J53.pin1
  N99: U9.Pin_5, R42.Pin_0
  N100: U9.Pin_6, J57.pin1
  N101: U9.Pin_7, R46.Pin_0
  N102: U9.Pin_8, J63.pin1
  N103: U9.Pin_9, R33.Pin_1, J54.pin1, J70.pin1
  N104: U9.Pin_11, R41.Pin_1, J50.pin1, J70.pin2
  N105: U9.Pin_13, R39.Pin_1, J52.pin1, J70.pin3
  N106: U9.Pin_15, R38.Pin_1, J59.pin1, J70.pin4
  N107: R33.Pin_0, J67.pin1
  N108: R35.Pin_0, J67.pin6
  N109: R38.Pin_0, J67.pin4
  N110: R39.Pin_0, J67.pin3
  N111: R41.Pin_0, J67.pin2
  N112: R43.Pin_0, J67.pin5
  N113: R47.Pin_0, J67.pin7
  N114: R48.Pin_0, J67.pin8
  N115: LED1.common_cathode, Power_12V.GND

notes:
  I2C & Power
