# Fritzing sketch TrackInterface (saved by Fritzing 0.9.6b)
perfboards: 1

parts:
  D1 = Rectifier Diode [part_number=1N5400 package="300 mil [THT]"]
  D2 = Rectifier Diode [part_number=1N5400 package="300 mil [THT]"]
  D3 = Rectifier Diode [part_number=1N5400 package="300 mil [THT]"]
  D4 = Rectifier Diode [part_number=1N5400 package="300 mil [THT]"]
  D5 = Rectifier Diode [part_number=1N5400 package="300 mil [THT]"]
  D6 = Rectifier Diode [part_number=1N5400 package="300 mil [THT]"]
  D7 = Rectifier Diode [part_number=1N5400 package="300 mil [THT]"]
  D8 = Rectifier Diode [part_number=1N5400 package="300 mil [THT]"]
  D9 = Rectifier Diode [part_number=1N5400 package="300 mil [THT]"]
  D10 = Rectifier Diode [part_number=1N5400 package="300 mil [THT]"]
  D11 = Rectifier Diode [part_number=1N5400 package="300 mil [THT]"]
  D12 = Rectifier Diode [part_number=1N5400 package="300 mil [THT]"]
  D13 = Rectifier Diode [part_number=1N5400 package="300 mil [THT]"]
  D14 = Rectifier Diode [part_number=1N5400 package="300 mil [THT]"]
  D15 = Rectifier Diode [part_number=1N5400 package="300 mil [THT]"]
  D16 = Rectifier Diode [part_number=1N5400 package="300 mil [THT]"]
  D17 = Rectifier Diode [part_number=1N5400 package="300 mil [THT]"]
  D18 = Rectifier Diode [part_number=1N5400 package="300 mil [THT]"]
  D19 = Rectifier Diode [part_number=1N5400 package="300 mil [THT]"]
  D20 = Rectifier Diode [part_number=1N5400 package="300 mil [THT]"]
  D21 = Rectifier Diode [part_number=1N5400 package="300 mil [THT]"]
  D22 = Rectifier Diode [part_number=1N5400 package="300 mil [THT]"]
  D23 = Rectifier Diode [part_number=1N5400 package="300 mil [THT]"]
  D24 = Rectifier Diode [part_number=1N5400 package="300 mil [THT]"]
  D25 = Rectifier Diode [part_number=1N5400 package="300 mil [THT]"]
  D26 = Rectifier Diode [part_number=1N5400 package="300 mil [THT]"]
  D27 = Rectifier Diode [part_number=1N5400 package="300 mil [THT]"]
  D28 = Rectifier Diode [part_number=1N5400 package="300 mil [THT]"]
  D29 = Rectifier Diode [part_number=1N5400 package="300 mil [THT]"]
  D30 = Rectifier Diode [part_number=1N5400 package="300 mil [THT]"]
  D31 = Rectifier Diode [part_number=1N5400 package="300 mil [THT]"]
  D32 = Rectifier Diode [part_number=1N5400 package="300 mil [THT]"]
  D33 = Rectifier Diode [part_number=1N5400 package="300 mil [THT]"]
  D34 = Rectifier Diode [part_number=1N5400 package="300 mil [THT]"]
  D35 = Rectifier Diode [part_number=1N5400 package="300 mil [THT]"]
  D36 = Rectifier Diode [part_number=1N5400 package="300 mil [THT]"]
  D37 = Rectifier Diode [part_number=1N5400 package="300 mil [THT]"]
  D38 = Rectifier Diode [part_number=1N5400 package="300 mil [THT]"]
  D39 = Rectifier Diode [part_number=1N5400 package="300 mil [THT]"]
  D40 = Rectifier Diode [part_number=1N5400 package="300 mil [THT]"]
  D41 = Rectifier Diode [part_number=1N5400 package="300 mil [THT]"]
  D42 = Rectifier Diode [part_number=1N5400 package="300 mil [THT]"]
  D43 = Rectifier Diode [part_number=1N5400 package="300 mil [THT]"]
  D44 = Rectifier Diode [part_number=1N5400 package="300 mil [THT]"]
  D45 = Rectifier Diode [part_number=1N5400 package="300 mil [THT]"]
  D46 = Rectifier Diode [part_number=1N5400 package="300 mil [THT]"]
  D47 = Rectifier Diode [part_number=1N5400 package="300 mil [THT]"]
  D48 = Rectifier Diode [part_number=1N5400 package="300 mil [THT]"]
  J3 = Camdenboss CTB0158-9 [part_number=CTB0158-9 package=THT]
  J2 = Camdenboss CTB0158-9 [part_number=CTB0158-9 package=THT]

nets (from the schematic view):
  N1: D1.cathode, D2.anode
  N2: D1.anode, D4.cathode, D11.cathode, D12.anode, D15.cathode, D18.anode, D21.cathode, D24.anode, D26.anode, D28.cathode, D32.cathode, D36.anode, D38.anode, D41.cathode, D44.anode, D47.cathode, J2.pin8, J2.pin9
  N3: D2.cathode, D3.anode
  N4: D3.cathode, D6.anode, J2.pin6, J2.pin7
  N5: D4.anode, D5.cathode
  N6: D5.anode, D6.cathode
  N7: D7.cathode, D9.anode, J2.pin4, J2.pin5
  N8: D7.anode, D8.cathode
  N9: D8.anode, D12.cathode
  N10: D9.cathode, D10.anode
  N11: D10.cathode, D11.anode
  N12: D13.cathode, D16.anode, J2.pin2, J2.pin3
  N13: D13.anode, D14.cathode
  N14: D14.anode, D18.cathode
  N15: D15.anode, D17.cathode
  N16: D16.cathode, D17.anode
  N17: D19.cathode, D22.anode, J3.pin9, J2.pin1
  N18: D19.anode, D20.cathode
  N19: D20.anode, D24.cathode
  N20: D21.anode, D23.cathode
  N21: D22.cathode, D23.anode
  N22: D25.cathode, D32.anode
  N23: D25.anode, D34.cathode
  N24: D26.cathode, D35.anode
  N25: D27.cathode, D31.anode
  N26: D27.anode, D33.cathode, J3.pin5, J3.pin6
  N27: D28.anode, D31.cathode
  N28: D29.cathode, D34.anode, J3.pin7, J3.pin8
  N29: D29.anode, D30.cathode
  N30: D30.anode, D36.cathode
  N31: D33.anode, D35.cathode
  N32: D37.cathode, D45.anode
  N33: D37.anode, D38.cathode
  N34: D39.cathode, D46.anode
  N35: D39.anode, D40.cathode, J3.pin3, J3.pin4
  N36: D40.anode, D42.cathode
  N37: D41.anode, D43.cathode
  N38: D42.anode, D44.cathode
  N39: D43.anode, D48.cathode
  N40: D45.cathode, D48.anode, J3.pin1, J3.pin2
  N41: D46.cathode, D47.anode
  Track_07: J3.terminal_1
  Tracksensor_07: J3.terminal_2
  Track_06: J3.terminal_3
  Tracksensor_06: J3.terminal_4
  Tracksensor_05: J3.terminal_5
  Track_05: J3.terminal_6
  Tracksensor_04: J3.terminal_7
  Track_04: J3.terminal_8
  Tracksensor_03: J3.terminal_9
  Track_03: J2.terminal_1
  Tracksensor_02: J2.terminal_2
  Track_02: J2.terminal_3
  Tracksensor_01: J2.terminal_4
  Track_01: J2.terminal_5
  Tracksensor_00: J2.terminal_6
  Track_00: J2.terminal_7
  TrackSensor Line: J2.terminal_8
  Track Power: J2.terminal_9
