# Fritzing sketch PCB-TrackSensor_V2 (saved by Fritzing 0.9.6b)
stripboards: 1

parts:
  U1 = TLP620-4 [package="DIP (Dual Inline) [THT]"]
  U2 = TLP620-4 [package="DIP (Dual Inline) [THT]"]
  U3 = PCF8574 [package="DIP16 [THT]"]
  R1 = Resistor [tolerance=±5% power=0.25 resistance=39 package=THT]
  J1 = male pin header, 2 pins [form="♂ (male)"]
  J2 = male pin header, 2 pins [form="♂ (male)"]
  J3 = male pin header, 2 pins [form="♂ (male)"]
  J4 = male pin header, 4 pins [form="♂ (male)"]
  J5 = male pin header, 4 pins [form="♂ (male)"]
  R2 = Resistor [tolerance=±5% power=0.25 resistance=2.2k package=THT]
  R3 = Resistor [tolerance=±5% power=0.25 resistance=2.2k package=THT]
  R4 = Resistor [tolerance=±5% power=0.25 resistance=2.2k package=THT]
  J6 = male pin header, 1 pin [form="♂ (male)"]
  J7 = male pin header, 1 pin [form="♂ (male)"]
  J8 = male pin header, 1 pin [form="♂ (male)"]
  J9 = male pin header, 1 pin [form="♂ (male)"]
  J10 = male pin header, 1 pin [form="♂ (male)"]
  J11 = male pin header, 1 pin [form="♂ (male)"]
  J12 = male pin header, 1 pin [form="♂ (male)"]
  J13 = male pin header, 1 pin [form="♂ (male)"]
  J14 = male pin header, 1 pin [form="♂ (male)"]
  J15 = male pin header, 1 pin [form="♂ (male)"]
  J16 = male pin header, 1 pin [form="♂ (male)"]
  J17 = male pin header, 1 pin [form="♂ (male)"]
  J18 = male pin header, 1 pin [form="♂ (male)"]
  J19 = male pin header, 1 pin [form="♂ (male)"]
  J20 = male pin header, 1 pin [form="♂ (male)"]
  J21 = male pin header, 1 pin [form="♂ (male)"]
  R5 = Resistor [tolerance=±5% power=0.25 resistance=39 package=THT]
  R6 = Resistor [tolerance=±5% power=0.25 resistance=39 package=THT]
  R7 = Resistor [tolerance=±5% power=0.25 resistance=39 package=THT]
  R8 = Resistor [tolerance=±5% power=0.25 resistance=39 package=THT]
  R9 = Resistor [tolerance=±5% power=0.25 resistance=39 package=THT]
  R10 = Resistor [tolerance=±5% power=0.25 resistance=39 package=THT]
  R11 = Resistor [tolerance=±5% power=0.25 resistance=39 package=THT]
  J22 = male pin header, 8 pins [form="♂ (male)"]
  J23 = male pin header, 9 pins [form="♂ (male)"]
  U4 = TLP620-4 [package="DIP (Dual Inline) [THT]"]
  U5 = TLP620-4 [package="DIP (Dual Inline) [THT]"]
  U6 = PCF8574 [package="DIP16 [THT]"]
  R12 = Resistor [tolerance=±5% power=0.25 resistance=39 package=THT]
  R13 = Resistor [tolerance=±5% power=0.25 resistance=39 package=THT]
  R14 = Resistor [tolerance=±5% power=0.25 resistance=39 package=THT]
  R15 = Resistor [tolerance=±5% power=0.25 resistance=39 package=THT]
  R16 = Resistor [tolerance=±5% power=0.25 resistance=39 package=THT]
  R17 = Resistor [tolerance=±5% power=0.25 resistance=39 package=THT]
  R18 = Resistor [tolerance=±5% power=0.25 resistance=39 package=THT]
  R19 = Resistor [tolerance=±5% power=0.25 resistance=39 package=THT]
  J24 = male pin header, 2 pins [form="♂ (male)"]
  J25 = male pin header, 2 pins [form="♂ (male)"]
  J26 = male pin header, 2 pins [form="♂ (male)"]
  J27 = male pin header, 4 pins [form="♂ (male)"]
  J28 = male pin header, 4 pins [form="♂ (male)"]
  R20 = Resistor [tolerance=±5% power=0.25 resistance=2.2k package=THT]
  J29 = male pin header, 1 pin [form="♂ (male)"]
  J30 = male pin header, 1 pin [form="♂ (male)"]
  J31 = male pin header, 1 pin [form="♂ (male)"]
  J32 = male pin header, 1 pin [form="♂ (male)"]
  J33 = male pin header, 1 pin [form="♂ (male)"]
  J34 = male pin header, 1 pin [form="♂ (male)"]
  J35 = male pin header, 1 pin [form="♂ (male)"]
  J36 = male pin header, 1 pin [form="♂ (male)"]
  J37 = male pin header, 1 pin [form="♂ (male)"]
  J38 = male pin header, 1 pin [form="♂ (male)"]
  J39 = male pin header, 1 pin [form="♂ (male)"]
  J40 = male pin header, 1 pin [form="♂ (male)"]
  J41 = male pin header, 1 pin [form="♂ (male)"]
  J42 = male pin header, 1 pin [form="♂ (male)"]
  J43 = male pin header, 1 pin [form="♂ (male)"]
  J44 = male pin header, 1 pin [form="♂ (male)"]
  R21 = Resistor [tolerance=±5% power=0.25 resistance=2.2k package=THT]
  J45 = male pin header, 8 pins [form="♂ (male)"]
  R22 = Resistor [tolerance=±5% power=0.25 resistance=2.2k package=THT]
  J46 = male pin header, 9 pins [form="♂ (male)"]
  U7 = TLP620-4 [package="DIP (Dual Inline) [THT]"]
  U8 = TLP620-4 [package="DIP (Dual Inline) [THT]"]
  U9 = PCF8574 [package="DIP16 [THT]"]
  R23 = Resistor [tolerance=±5% power=0.25 resistance=39 package=THT]
  R24 = Resistor [tolerance=±5% power=0.25 resistance=39 package=THT]
  R25 = Resistor [tolerance=±5% power=0.25 resistance=39 package=THT]
  R26 = Resistor [tolerance=±5% power=0.25 resistance=39 package=THT]
  R27 = Resistor [tolerance=±5% power=0.25 resistance=39 package=THT]
  R28 = Resistor [tolerance=±5% power=0.25 resistance=39 package=THT]
  R29 = Resistor [tolerance=±5% power=0.25 resistance=39 package=THT]
  R30 = Resistor [tolerance=±5% power=0.25 resistance=39 package=THT]
  J47 = male pin header, 2 pins [form="♂ (male)"]
  J48 = male pin header, 2 pins [form="♂ (male)"]
  J49 = male pin header, 2 pins [form="♂ (male)"]
  J50 = male pin header, 4 pins [form="♂ (male)"]
  J51 = male pin header, 4 pins [form="♂ (male)"]
  R31 = Resistor [tolerance=±5% power=0.25 resistance=2.2k package=THT]
  J52 = male pin header, 1 pin [form="♂ (male)"]
  J53 = male pin header, 1 pin [form="♂ (male)"]
  J54 = male pin header, 1 pin [form="♂ (male)"]
  J55 = male pin header, 1 pin [form="♂ (male)"]
  J56 = male pin header, 1 pin [form="♂ (male)"]
  J57 = male pin header, 1 pin [form="♂ (male)"]
  J58 = male pin header, 1 pin [form="♂ (male)"]
  J59 = male pin header, 1 pin [form="♂ (male)"]
  J60 = male pin header, 1 pin [form="♂ (male)"]
  J61 = male pin header, 1 pin [form="♂ (male)"]
  J62 = male pin header, 1 pin [form="♂ (male)"]
  J63 = male pin header, 1 pin [form="♂ (male)"]
  J64 = male pin header, 1 pin [form="♂ (male)"]
  J65 = male pin header, 1 pin [form="♂ (male)"]
  J66 = male pin header, 1 pin [form="♂ (male)"]
  J67 = male pin header, 1 pin [form="♂ (male)"]
  R32 = Resistor [tolerance=±5% power=0.25 resistance=2.2k package=THT]
  J68 = male pin header, 8 pins [form="♂ (male)"]
  R33 = Resistor [tolerance=±5% power=0.25 resistance=2.2k package=THT]
  J69 = male pin header, 9 pins [form="♂ (male)"]
  J70 = male pin header, 4 pins [form="♂ (male)"]
  J71 = male pin header, 4 pins [form="♂ (male)"]
  D1 = Rectifier Diode [part_number=1N4001 package="300 mil [THT]"]
  D2 = Rectifier Diode [part_number=1N4001 package="300 mil [THT]"]
  D3 = Rectifier Diode [part_number=1N4001 package="300 mil [THT]"]
  D4 = Rectifier Diode [part_number=1N4001 package="300 mil [THT]"]
  D5 = Rectifier Diode [part_number=1N4001 package="300 mil [THT]"]
  D6 = Rectifier Diode [part_number=1N4001 package="300 mil [THT]"]
  D7 = Rectifier Diode [part_number=1N4001 package="300 mil [THT]"]
  D8 = Rectifier Diode [part_number=1N4001 package="300 mil [THT]"]
  D9 = Rectifier Diode [part_number=1N4001 package="300 mil [THT]"]
  D10 = Rectifier Diode [part_number=1N4001 package="300 mil [THT]"]
  D11 = Rectifier Diode [part_number=1N4001 package="300 mil [THT]"]
  D12 = Rectifier Diode [part_number=1N4001 package="300 mil [THT]"]
  Track = Camdenboss CTB0158-3 [part_number=CTB0158-3 package=THT]
  Track1 = Camdenboss CTB0158-3 [part_number=CTB0158-3 package=THT]

nets:
  N1: U1.pin1, R1.Pin_1, J6.pin1, J22.pin1
  N2: U1.pin2, U1.pin4, U1.pin6, U1.pin8, U2.pin2, U2.pin4, U2.pin6, U2.pin8, J23.pin9
  N3: U1.pin3, J7.pin1, R5.Pin_1, J22.pin2
  N4: U1.pin5, J8.pin1, R6.Pin_1, J22.pin3
  N5: U1.pin7, J9.pin1, R7.Pin_1, J22.pin4
  GND: U1.pin9, U1.pin11, U1.pin13, U1.pin15, U2.pin9, U2.pin11, U2.pin13, U2.pin15, U3.GND, J1.pin1, J2.pin1, J3.pin1, U4.pin9, U4.pin11, U4.pin13, U4.pin15, U5.pin9, U5.pin11, U5.pin13, U5.pin15, U6.GND, J24.pin1, J25.pin1, J26.pin1, U7.pin9, U7.pin11, U7.pin13, U7.pin15, U8.pin9, U8.pin11, U8.pin13, U8.pin15, U9.GND, J47.pin1, J48.pin1, J49.pin1, J70.pin4, J71.pin4
  net JP03: U1.pin10, U3.P3, J4.pin4, J13.pin1
  net JP02: U1.pin12, U3.P2, J4.pin3, J12.pin1
  net JP01: U1.pin14, U3.P1, J4.pin2, J11.pin1
  net JP00: U1.pin16, U3.P0, J4.pin1, J10.pin1
  N6: U2.pin1, J14.pin1, R8.Pin_1, J22.pin5
  N7: U2.pin3, J15.pin1, R9.Pin_1, J22.pin6
  N8: U2.pin5, J16.pin1, R10.Pin_1, J22.pin7
  N9: U2.pin7, J17.pin1, R11.Pin_1, J22.pin8
  net JP07: U2.pin10, U3.P7, J5.pin1, J21.pin1
  net JP06: U2.pin12, U3.P6, J5.pin2, J20.pin1
  net JP05: U2.pin14, U3.P5, J5.pin3, J19.pin1
  net JP04: U2.pin16, U3.P4, J5.pin4, J18.pin1
  N10: U3.A0, J1.pin2, R2.Pin_1
  N11: U3.A1, J2.pin2, R3.Pin_1
  N12: U3.A2, J3.pin2, R4.Pin_1
  I2C_SCL: U3.SCL, U6.SCL, U9.SCL, J70.pin3, J71.pin3
  I2C_SDA: U3.SDA, U6.SDA, U9.SDA, J70.pin2, J71.pin2
  3.3V: U3.VCC, R2.Pin_0, R3.Pin_0, R4.Pin_0, U6.VCC, R20.Pin_0, R21.Pin_0, R22.Pin_0, U9.VCC, R31.Pin_0, R32.Pin_0, R33.Pin_0, J70.pin1, J71.pin1
  N13: R1.Pin_0, J23.pin1
  N14: R5.Pin_0, J23.pin2
  N15: R6.Pin_0, J23.pin3
  N16: R7.Pin_0, J23.pin4
  N17: R8.Pin_0, J23.pin5
  N18: R9.Pin_0, J23.pin6
  N19: R10.Pin_0, J23.pin7
  N20: R11.Pin_0, J23.pin8
  N21: U4.pin1, R15.Pin_1, J36.pin1, J45.pin5
  N22: U4.pin2, U4.pin4, U4.pin6, U4.pin8, U5.pin2, U5.pin4, U5.pin6, U5.pin8, J46.pin9
  N23: U4.pin3, R14.Pin_1, J35.pin1, J45.pin6
  N24: U4.pin5, R13.Pin_1, J34.pin1, J45.pin7
  N25: U4.pin7, R12.Pin_1, J33.pin1, J45.pin8
  net JP17: U4.pin10, U6.P7, J27.pin1, J29.pin1
  net JP16: U4.pin12, U6.P6, J27.pin2, J30.pin1
  net JP15: U4.pin14, U6.P5, J27.pin3, J31.pin1
  net JP14: U4.pin16, U6.P4, J27.pin4, J32.pin1
  N26: U5.pin1, R19.Pin_1, J44.pin1, J45.pin1
  N27: U5.pin3, R18.Pin_1, J43.pin1, J45.pin2
  N28: U5.pin5, R17.Pin_1, J42.pin1, J45.pin3
  N29: U5.pin7, R16.Pin_1, J41.pin1, J45.pin4
  net JP13: U5.pin10, U6.P3, J28.pin4, J37.pin1
  net JP12: U5.pin12, U6.P2, J28.pin3, J38.pin1
  net JP11: U5.pin14, U6.P1, J28.pin2, J39.pin1
  net JP10: U5.pin16, U6.P0, J28.pin1, J40.pin1
  N30: U6.A0, J26.pin2, R20.Pin_1
  N31: U6.A1, J25.pin2, R21.Pin_1
  N32: U6.A2, J24.pin2, R22.Pin_1
  N33: R12.Pin_0, J46.pin8
  N34: R13.Pin_0, J46.pin7
  N35: R14.Pin_0, J46.pin6
  N36: R15.Pin_0, J46.pin5
  N37: R16.Pin_0, J46.pin4
  N38: R17.Pin_0, J46.pin3
  N39: R18.Pin_0, J46.pin2
  N40: R19.Pin_0, J46.pin1
  N41: U7.pin1, R26.Pin_1, J59.pin1, J68.pin5
  N42: U7.pin2, U7.pin4, U7.pin6, U7.pin8, U8.pin2, U8.pin4, U8.pin6, U8.pin8, J69.pin9, Track1.pin1
  N43: U7.pin3, R25.Pin_1, J58.pin1, J68.pin6
  N44: U7.pin5, R24.Pin_1, J57.pin1, J68.pin7
  N45: U7.pin7, R23.Pin_1, J56.pin1, J68.pin8
  net JP27: U7.pin10, U9.P7, J50.pin1, J52.pin1
  net JP26: U7.pin12, U9.P6, J50.pin2, J53.pin1
  net JP25: U7.pin14, U9.P5, J50.pin3, J54.pin1
  net JP24: U7.pin16, U9.P4, J50.pin4, J55.pin1
  N46: U8.pin1, R30.Pin_1, J67.pin1, J68.pin1
  N47: U8.pin3, R29.Pin_1, J66.pin1, J68.pin2
  N48: U8.pin5, R28.Pin_1, J65.pin1, J68.pin3
  N49: U8.pin7, R27.Pin_1, J64.pin1, J68.pin4
  net JP23: U8.pin10, U9.P3, J51.pin4, J60.pin1
  net JP22: U8.pin12, U9.P2, J51.pin3, J61.pin1
  net JP21: U8.pin14, U9.P1, J51.pin2, J62.pin1
  net JP20: U8.pin16, U9.P0, J51.pin1, J63.pin1
  N50: U9.A0, J49.pin2, R31.Pin_1
  N51: U9.A1, J48.pin2, R32.Pin_1
  N52: U9.A2, J47.pin2, R33.Pin_1
  N53: R23.Pin_0, J69.pin8
  N54: R24.Pin_0, J69.pin7
  N55: R25.Pin_0, J69.pin6
  N56: R26.Pin_0, J69.pin5
  N57: R27.Pin_0, J69.pin4
  N58: R28.Pin_0, J69.pin3
  N59: R29.Pin_0, J69.pin2, Track1.pin3
  N60: R30.Pin_0, J69.pin1, Track1.pin2
  N61: D1.cathode, D4.anode, D7.cathode, D10.anode, Track.pin1
  N62: D1.anode, D2.cathode
  N63: D2.anode, D3.cathode
  N64: D3.anode, D6.cathode, Track.pin3
  N65: D4.cathode, D5.anode
  N66: D5.cathode, D6.anode
  N67: D7.anode, D8.cathode
  N68: D8.anode, D9.cathode
  N69: D9.anode, D12.cathode, Track.pin2
  N70: D10.cathode, D11.anode
  N71: D11.cathode, D12.anode
  Track Power Input: Track.terminal_1, Track1.terminal_1
  Track X: Track.terminal_2, Track1.terminal_2
  Track X+1: Track.terminal_3, Track1.terminal_3

notes:
  TrackInterface

custom parts:
  TLP620-4: Quad Photo-transistor optically coupled to two infrared emitting diodes connected in inverse parallel.
