# Fritzing sketch pcb_001 (saved by Fritzing 0.9.6b)
circuit board: 10cm x 7.5cm
breadboards: 1

parts:
  U01 = PCF8574 [package="DIP16 [THT]"]
  J4 = double row male pin header, 6 pins [form="♂ (male)"]
  2k2_Sil1 = female pin header, 8 pins [form="♀ (female)"]
  U02 = TLP620-4 [package="DIP (Dual Inline) [THT]"]
  J5 = male pin header, 4 pins [form="♂ (male)"]
  U05 = TLP620-4 [package="DIP (Dual Inline) [THT]"]
  U04 = PCF8574 [package="DIP16 [THT]"]
  U06 = TLP620-4 [package="DIP (Dual Inline) [THT]"]
  J9 = double row male pin header, 6 pins [form="♂ (male)"]
  2k2_Sil3 = female pin header, 8 pins [form="♀ (female)"]
  2k2_Sil4 = female pin header, 5 pins [form="♀ (female)"]
  2k2_Sil5 = female pin header, 5 pins [form="♀ (female)"]
  U08 = TLP620-4 [package="DIP (Dual Inline) [THT]"]
  U11 = TLP620-4 [package="DIP (Dual Inline) [THT]"]
  U07 = PCF8574 [package="DIP16 [THT]"]
  U10 = PCF8574 [package="DIP16 [THT]"]
  2k2_Sil6 = female pin header, 8 pins [form="♀ (female)"]
  2k2_Sil7 = female pin header, 8 pins [form="♀ (female)"]
  J10 = double row male pin header, 6 pins [form="♂ (male)"]
  J11 = double row male pin header, 6 pins [form="♂ (male)"]
  2k2_Sil8 = female pin header, 5 pins [form="♀ (female)"]
  2k2_Sil9 = female pin header, 5 pins [form="♀ (female)"]
  U09 = TLP620-4 [package="DIP (Dual Inline) [THT]"]
  J8 = male pin header, 5 pins [form="♂ (male)"]
  J12 = male pin header, 5 pins [form="♂ (male)"]
  J13 = male pin header, 5 pins [form="♂ (male)"]
  J6 = male pin header, 5 pins [form="♂ (male)" part_number=5556.05A]
  J7-4x470ohm = female pin header, 5 pins [form="♀ (female)" part_number=10F5347]
  R21 = Resistor [tolerance=±5% power=0.25 resistance=22 package=THT]
  R22 = Resistor [tolerance=±5% power=0.25 resistance=22 package=THT]
  R23 = Resistor [tolerance=±5% power=0.25 resistance=22 package=THT]
  R24 = Resistor [tolerance=±5% power=0.25 resistance=22 package=THT]
  J14-4x470ohm = female pin header, 5 pins [form="♀ (female)"]
  J15 = female pin header, 5 pins [form="♀ (female)"]
  J16 = female pin header, 5 pins [form="♀ (female)"]
  R25 = Resistor [tolerance=±5% power=0.25 resistance=22 package=THT]
  R26 = Resistor [tolerance=±5% power=0.25 resistance=22 package=THT]
  R27 = Resistor [tolerance=±5% power=0.25 resistance=22 package=THT]
  R28 = Resistor [tolerance=±5% power=0.25 resistance=22 package=THT]
  R29 = Resistor [tolerance=±5% power=0.25 resistance=22 package=THT]
  R30 = Resistor [tolerance=±5% power=0.25 resistance=22 package=THT]
  R31 = Resistor [tolerance=±5% power=0.25 resistance=22 package=THT]
  R32 = Resistor [tolerance=±5% power=0.25 resistance=22 package=THT]
  R33 = Resistor [tolerance=±5% power=0.25 resistance=22 package=THT]
  R34 = Resistor [tolerance=±5% power=0.25 resistance=220 package=THT]
  R35 = Resistor [tolerance=±5% power=0.25 resistance=22 package=THT]
  R36 = Resistor [tolerance=±5% power=0.25 resistance=22 package=THT]
  J18 = male pin header, 5 pins [form="♂ (male)"]
  J19 = male pin header, 5 pins [form="♂ (male)"]
  J20 = male pin header, 5 pins [form="♂ (male)"]
  J21 = male pin header, 5 pins [form="♂ (male)"]
  J22 = female pin header, 5 pins [form="♀ (female)"]
  J23 = female pin header, 5 pins [form="♀ (female)"]
  J24 = female pin header, 5 pins [form="♀ (female)"]
  J25 = female pin header, 5 pins [form="♀ (female)"]
  R37 = Resistor [tolerance=±5% power=0.25 resistance=220 package=THT]
  R38 = Resistor [tolerance=±5% power=0.25 resistance=220 package=THT]
  R39 = Resistor [tolerance=±5% power=0.25 resistance=220 package=THT]
  R40 = Resistor [tolerance=±5% power=0.25 resistance=220 package=THT]
  R41 = Resistor [tolerance=±5% power=0.25 resistance=220 package=THT]
  R42 = Resistor [tolerance=±5% power=0.25 resistance=220 package=THT]
  R43 = Resistor [tolerance=±5% power=0.25 resistance=220 package=THT]
  R44 = Resistor [tolerance=±5% power=0.25 resistance=220 package=THT]
  R45 = Resistor [tolerance=±5% power=0.25 resistance=22 package=THT]
  R46 = Resistor [tolerance=±5% power=0.25 resistance=220 package=THT]
  R47 = Resistor [tolerance=±5% power=0.25 resistance=22 package=THT]
  R48 = Resistor [tolerance=±5% power=0.25 resistance=22 package=THT]
  R49 = Resistor [tolerance=±5% power=0.25 resistance=22 package=THT]
  R50 = Resistor [tolerance=±5% power=0.25 resistance=22 package=THT]
  R51 = Resistor [tolerance=±5% power=0.25 resistance=22 package=THT]
  R52 = Resistor [tolerance=±5% power=0.25 resistance=22 package=THT]
  J26 = male pin header, 4 pins [form="♂ (male)"]
  U12 = TLP620-4 [package="DIP (Dual Inline) [THT]"]
  U03 = TLP620-4 [package="DIP (Dual Inline) [THT]"]
  J27 = female pin header, 2 pins [form="♀ (female)"]
  J28 = female pin header, 2 pins [form="♀ (female)"]

nets:
  N1: U01.A0, J4.pin6, 2k2_Sil1.pin2
  N2: U01.A1, J4.pin5, 2k2_Sil1.pin3
  N3: U01.A2, J4.pin4, 2k2_Sil1.pin4
  N4: U01.P0, 2k2_Sil1.pin5, U02.pin16
  N5: U01.P1, 2k2_Sil1.pin6, U02.pin14
  N6: U01.P2, 2k2_Sil1.pin7, U02.pin12
  N7: U01.P3, 2k2_Sil1.pin8, U02.pin10
  GND: U01.GND, J4.pin1, J4.pin2, J4.pin3, U02.pin9, U02.pin11, U02.pin13, U02.pin15, J5.pin4, U05.pin9, U05.pin11, U05.pin13, U05.pin15, U04.GND, U06.pin9, U06.pin11, U06.pin13, U06.pin15, J9.pin1, J9.pin2, J9.pin3, U08.pin9, U08.pin11, U08.pin13, U08.pin15, U11.pin9, U11.pin11, U11.pin13, U11.pin15, U07.GND, U10.GND, J10.pin1, J10.pin2, J10.pin3, J11.pin1, J11.pin2, J11.pin3, U09.pin9, U09.pin11, U09.pin13, U09.pin15, J26.pin4, U12.pin9, U12.pin11, U12.pin13, U12.pin15, U03.pin9, U03.pin11, U03.pin13, U03.pin15
  N8: U01.P4, 2k2_Sil5.pin2, U03.pin16
  N9: U01.P5, 2k2_Sil5.pin3, U03.pin14
  N10: U01.P6, 2k2_Sil5.pin4, U03.pin12
  N11: U01.P7, 2k2_Sil5.pin5, U03.pin10
  I2C-SCL: U01.SCL, J5.pin3, U04.SCL, U07.SCL, U10.SCL, J26.pin3
  I2C-SDA: U01.SDA, J5.pin2, U04.SDA, U07.SDA, U10.SDA, J26.pin2
  3.3V: U01.VCC, 2k2_Sil1.pin1, J5.pin1, U04.VCC, 2k2_Sil3.pin1, 2k2_Sil4.pin1, 2k2_Sil5.pin1, U07.VCC, U10.VCC, 2k2_Sil6.pin1, 2k2_Sil7.pin1, 2k2_Sil8.pin1, 2k2_Sil9.pin1, J26.pin1
  N12: U02.pin1, R33.Pin_1
  N13: U02.pin2, U02.pin4, U02.pin6, U02.pin8, U05.pin2, U05.pin4, U05.pin6, U05.pin8, U08.pin2, U08.pin4, U08.pin6, U08.pin8, U11.pin2, U11.pin4, U11.pin6, U11.pin8, J8.pin1, J12.pin1, J13.pin1, J6.pin1, J7-4x470ohm.pin1, J14-4x470ohm.pin1, J15.pin1, J16.pin1, J27.pin1, J27.pin2
  N14: U02.pin3, R34.Pin_1
  N15: U02.pin5, R35.Pin_1
  N16: U02.pin7, R36.Pin_1
  N17: U05.pin1, R24.Pin_1
  N18: U05.pin3, R23.Pin_1
  N19: U05.pin5, R22.Pin_1
  N20: U05.pin7, R21.Pin_1
  N21: U05.pin10, U04.P3, 2k2_Sil3.pin8
  N22: U05.pin12, U04.P2, 2k2_Sil3.pin7
  N23: U05.pin14, U04.P1, 2k2_Sil3.pin6
  N24: U05.pin16, U04.P0, 2k2_Sil3.pin5
  N25: U04.A0, J9.pin6, 2k2_Sil3.pin2
  N26: U04.A1, J9.pin5, 2k2_Sil3.pin3
  N27: U04.A2, J9.pin4, 2k2_Sil3.pin4
  N28: U04.P4, U06.pin16, 2k2_Sil4.pin2
  N29: U04.P5, U06.pin14, 2k2_Sil4.pin3
  N30: U04.P6, U06.pin12, 2k2_Sil4.pin4
  N31: U04.P7, U06.pin10, 2k2_Sil4.pin5
  N32: U06.pin1, R45.Pin_1
  N33: U06.pin2, U06.pin4, U06.pin6, U06.pin8, U09.pin2, U09.pin4, U09.pin6, U09.pin8, J18.pin1, J19.pin1, J20.pin1, J21.pin1, J22.pin1, J23.pin1, J24.pin1, J25.pin1, U12.pin2, U12.pin4, U12.pin6, U12.pin8, U03.pin2, U03.pin4, U03.pin6, U03.pin8, J28.pin1, J28.pin2
  N34: U06.pin3, R46.Pin_1
  N35: U06.pin5, R47.Pin_1
  N36: U06.pin7, R48.Pin_1
  N37: U08.pin1, R25.Pin_1
  N38: U08.pin3, R26.Pin_1
  N39: U08.pin5, R27.Pin_1
  N40: U08.pin7, R28.Pin_1
  N41: U08.pin10, U07.P3, 2k2_Sil6.pin8
  N42: U08.pin12, U07.P2, 2k2_Sil6.pin7
  N43: U08.pin14, U07.P1, 2k2_Sil6.pin6
  N44: U08.pin16, U07.P0, 2k2_Sil6.pin5
  N45: U11.pin1, R29.Pin_1
  N46: U11.pin3, R30.Pin_1
  N47: U11.pin5, R31.Pin_1
  N48: U11.pin7, R32.Pin_1
  L107-10: U11.pin10, U10.P3, 2k2_Sil7.pin8
  L107-12: U11.pin12, U10.P2, 2k2_Sil7.pin7
  L107-14: U11.pin14, U10.P1, 2k2_Sil7.pin6
  L107-16: U11.pin16, U10.P0, 2k2_Sil7.pin5
  N49: U07.A0, 2k2_Sil6.pin2, J10.pin6
  N50: U07.A1, 2k2_Sil6.pin3, J10.pin5
  N51: U07.A2, 2k2_Sil6.pin4, J10.pin4
  N52: U07.P4, 2k2_Sil8.pin2, U09.pin16
  N53: U07.P5, 2k2_Sil8.pin3, U09.pin14
  N54: U07.P6, 2k2_Sil8.pin4, U09.pin12
  N55: U07.P7, 2k2_Sil8.pin5, U09.pin10
  N56: U10.A0, 2k2_Sil7.pin2, J11.pin6
  N57: U10.A1, 2k2_Sil7.pin3, J11.pin5
  N58: U10.A2, 2k2_Sil7.pin4, J11.pin4
  L17-16: U10.P4, 2k2_Sil9.pin2, U12.pin16
  L17-14: U10.P5, 2k2_Sil9.pin3, U12.pin14
  L17-12: U10.P6, 2k2_Sil9.pin4, U12.pin12
  L17-10: U10.P7, 2k2_Sil9.pin5, U12.pin10
  N59: U09.pin1, R41.Pin_1
  N60: U09.pin3, R42.Pin_1
  N61: U09.pin5, R43.Pin_1
  N62: U09.pin7, R44.Pin_1
  N63: J8.pin2, J16.pin2, R29.Pin_0
  N64: J8.pin3, J16.pin3, R30.Pin_0
  N65: J8.pin4, J16.pin4, R31.Pin_0
  N66: J8.pin5, J16.pin5, R32.Pin_0
  N67: J12.pin2, J15.pin2, R25.Pin_0
  N68: J12.pin3, J15.pin3, R26.Pin_0
  N69: J12.pin4, J15.pin4, R27.Pin_0
  N70: J12.pin5, J15.pin5, R28.Pin_0
  N71: J13.pin2, R24.Pin_0, J14-4x470ohm.pin2
  N72: J13.pin3, R23.Pin_0, J14-4x470ohm.pin3
  N73: J13.pin4, R22.Pin_0, J14-4x470ohm.pin4
  N74: J13.pin5, R21.Pin_0, J14-4x470ohm.pin5
  N75: J6.pin2, J7-4x470ohm.pin2, R33.Pin_0
  N76: J6.pin3, J7-4x470ohm.pin3, R34.Pin_0
  N77: J6.pin4, J7-4x470ohm.pin4, R35.Pin_0
  N78: J6.pin5, J7-4x470ohm.pin5, R36.Pin_0
  N79: J18.pin2, J22.pin2, R37.Pin_0
  N80: J18.pin3, J22.pin3, R38.Pin_0
  N81: J18.pin4, J22.pin4, R39.Pin_0
  N82: J18.pin5, J22.pin5, R40.Pin_0
  N83: J19.pin2, J23.pin2, R41.Pin_0
  N84: J19.pin3, J23.pin3, R42.Pin_0
  N85: J19.pin4, J23.pin4, R43.Pin_0
  N86: J19.pin5, J23.pin5, R44.Pin_0
  N87: J20.pin2, J24.pin2, R45.Pin_0
  N88: J20.pin3, J24.pin3, R46.Pin_0
  N89: J20.pin4, J24.pin4, R47.Pin_0
  N90: J20.pin5, J24.pin5, R48.Pin_0
  N91: J21.pin2, J25.pin2, R49.Pin_0
  N92: J21.pin3, J25.pin3, R50.Pin_0
  N93: J21.pin4, J25.pin4, R51.Pin_0
  N94: J21.pin5, J25.pin5, R52.Pin_0
  N95: R37.Pin_1, U12.pin1
  N96: R38.Pin_1, U12.pin3
  N97: R39.Pin_1, U12.pin5
  N98: R40.Pin_1, U12.pin7
  N99: R49.Pin_1, U03.pin1
  N100: R50.Pin_1, U03.pin3
  N101: R51.Pin_1, U03.pin5
  N102: R52.Pin_1, U03.pin7

notes:
  Svenn-Erik K. Thomsen
  sekt1953@gmail.com
  3V3
  SDA
  SCL
  GND
  I2C
  TrackSensor

custom parts:
  TLP620-4: Quad Photo-transistor optically coupled to two infrared emitting diodes connected in inverse parallel.
