# Fritzing sketch SkindeInterface (saved by Fritzing 0.9.6b)
circuit board: 16.2147cm x 5.92195cm

parts:
  D1 = Rectifier Diode [part_number=1N4001 package="300 mil [THT]"]
  D2 = Rectifier Diode [part_number=1N4001 package="300 mil [THT]"]
  D3 = Rectifier Diode [part_number=1N4001 package="300 mil [THT]"]
  D4 = Rectifier Diode [part_number=1N4001 package="300 mil [THT]"]
  D5 = Rectifier Diode [part_number=1N4001 package="300 mil [THT]"]
  D6 = Rectifier Diode [part_number=1N4001 package="300 mil [THT]"]
  J1 = Camdenboss CTB0158-2 [part_number=CTB0158-2 package=THT]
  R1 = Resistor [tolerance=±5% power=0.25 resistance=220 package=THT]
  U2 = Sharp PC847X [package=THT]
  D7 = Rectifier Diode [part_number=1N4001 package="300 mil [THT]"]
  D8 = Rectifier Diode [part_number=1N4001 package="300 mil [THT]"]
  D9 = Rectifier Diode [part_number=1N4001 package="300 mil [THT]"]
  D10 = Rectifier Diode [part_number=1N4001 package="300 mil [THT]"]
  D11 = Rectifier Diode [part_number=1N4001 package="300 mil [THT]"]
  D12 = Rectifier Diode [part_number=1N4001 package="300 mil [THT]"]
  J2 = Camdenboss CTB0158-2 [part_number=CTB0158-2 package=THT]
  R2 = Resistor [tolerance=±5% power=0.25 resistance=220 package=THT]
  D14 = Rectifier Diode [part_number=1N4001 package="300 mil [THT]"]
  D13 = Rectifier Diode [part_number=1N4001 package="300 mil [THT]"]
  D15 = Rectifier Diode [part_number=1N4001 package="300 mil [THT]"]
  D16 = Rectifier Diode [part_number=1N4001 package="300 mil [THT]"]
  D17 = Rectifier Diode [part_number=1N4001 package="300 mil [THT]"]
  D18 = Rectifier Diode [part_number=1N4001 package="300 mil [THT]"]
  J3 = Camdenboss CTB0158-2 [part_number=CTB0158-2 package=THT]
  R3 = Resistor [tolerance=±5% power=0.25 resistance=220 package=THT]
  D20 = Rectifier Diode [part_number=1N4001 package="300 mil [THT]"]
  D19 = Rectifier Diode [part_number=1N4001 package="300 mil [THT]"]
  D21 = Rectifier Diode [part_number=1N4001 package="300 mil [THT]"]
  D22 = Rectifier Diode [part_number=1N4001 package="300 mil [THT]"]
  D23 = Rectifier Diode [part_number=1N4001 package="300 mil [THT]"]
  D24 = Rectifier Diode [part_number=1N4001 package="300 mil [THT]"]
  J4 = Camdenboss CTB0158-2 [part_number=CTB0158-2 package=THT]
  R4 = Resistor [tolerance=±5% power=0.25 resistance=220 package=THT]
  J5 = Camdenboss CTB0158-5 [part_number=CTB0158-5 package=THT]

nets:
  N1: D1.cathode, D4.anode, J1.pin2, R1.Pin_0
  N2: D1.anode, D2.cathode
  N3: D2.anode, D3.cathode
  N4: D3.anode, D6.cathode, J1.pin1, U2.Pin_2
  N5: D4.cathode, D5.anode
  N6: D5.cathode, D6.anode
  N7: R1.Pin_1, U2.Pin_1
  N8: U2.Pin_3, R2.Pin_1
  N9: U2.Pin_4, D9.anode, D12.cathode, J2.pin1
  N10: U2.Pin_5, R3.Pin_1
  N11: U2.Pin_6, D15.anode, D18.cathode, J3.pin1
  N12: U2.Pin_7, R4.Pin_1
  N13: U2.Pin_8, D21.anode, D24.cathode, J4.pin1
  N14: U2.Pin_9, U2.Pin_11, U2.Pin_13, U2.Pin_15, J5.pin5
  N15: U2.Pin_10, J5.pin4
  N16: U2.Pin_12, J5.pin3
  N17: U2.Pin_14, J5.pin2
  N18: U2.Pin_16, J5.pin1
  N19: D7.cathode, D10.anode, J2.pin2, R2.Pin_0
  N20: D7.anode, D8.cathode
  N21: D8.anode, D9.cathode
  N22: D10.cathode, D11.anode
  N23: D11.cathode, D12.anode
  N24: D14.cathode, D13.anode
  N25: D14.anode, D15.cathode
  N26: D13.cathode, D16.anode, J3.pin2, R3.Pin_0
  N27: D16.cathode, D17.anode
  N28: D17.cathode, D18.anode
  N29: D20.cathode, D19.anode
  N30: D20.anode, D21.cathode
  N31: D19.cathode, D22.anode, J4.pin2, R4.Pin_0
  N32: D22.cathode, D23.anode
  N33: D23.cathode, D24.anode

notes:
  Kørespænding
  Skinde afsnit
