# Fritzing sketch Sporbesættelse (saved by Fritzing 0.9.6b)
circuit board: 10cm x 10cm

parts:
  D1 = Rectifier Diode [part_number=1N5400 package="300 mil [THT]"]
  J1 = Camdenboss CTB0158-5 [part_number=CTB0158-5 package=THT]
  D2 = Rectifier Diode [part_number=1N5400 package="300 mil [THT]"]
  D3 = Rectifier Diode [part_number=1N5400 package="300 mil [THT]"]
  D4 = Rectifier Diode [part_number=1N5400 package="300 mil [THT]"]
  D5 = Rectifier Diode [part_number=1N5400 package="300 mil [THT]"]
  D6 = Rectifier Diode [part_number=1N5400 package="300 mil [THT]"]
  D8 = Rectifier Diode [part_number=1N5400 package="300 mil [THT]"]
  D9 = Rectifier Diode [part_number=1N5400 package="300 mil [THT]"]
  D10 = Rectifier Diode [part_number=1N5400 package="300 mil [THT]"]
  D11 = Rectifier Diode [part_number=1N5400 package="300 mil [THT]"]
  D12 = Rectifier Diode [part_number=1N5400 package="300 mil [THT]"]
  D7 = Rectifier Diode [part_number=1N5400 package="300 mil [THT]"]
  D15 = Rectifier Diode [part_number=1N5400 package="300 mil [THT]"]
  D14 = Rectifier Diode [part_number=1N5400 package="300 mil [THT]"]
  D16 = Rectifier Diode [part_number=1N5400 package="300 mil [THT]"]
  D13 = Rectifier Diode [part_number=1N5400 package="300 mil [THT]"]
  D18 = Rectifier Diode [part_number=1N5400 package="300 mil [THT]"]
  D17 = Rectifier Diode [part_number=1N5400 package="300 mil [THT]"]
  D21 = Rectifier Diode [part_number=1N5400 package="300 mil [THT]"]
  D20 = Rectifier Diode [part_number=1N5400 package="300 mil [THT]"]
  D19 = Rectifier Diode [part_number=1N5400 package="300 mil [THT]"]
  D24 = Rectifier Diode [part_number=1N5400 package="300 mil [THT]"]
  D23 = Rectifier Diode [part_number=1N5400 package="300 mil [THT]"]
  U1 = Sharp PC847X [package=THT]
  C1 = Electrolytic Capacitor [capacitance=560µF voltage=35V package="100 mil [THT, electrolytic]"]
  C2 = Electrolytic Capacitor [capacitance=560µF voltage=35V package="100 mil [THT, electrolytic]"]
  C3 = Electrolytic Capacitor [capacitance=560µF voltage=35V package="100 mil [THT, electrolytic]"]
  C4 = Electrolytic Capacitor [capacitance=560µF voltage=35V package="100 mil [THT, electrolytic]"]
  J2 = Camdenboss CTB0158-6 [part_number=CTB0158-6 package=THT]
  R4 = Resistor [tolerance=±5% resistance=180 power=0.25 package="0805 [SMD]"]
  R3 = Resistor [tolerance=±5% resistance=180 power=0.25 package="0805 [SMD]"]
  R2 = Resistor [tolerance=±5% resistance=180 power=0.25 package="0805 [SMD]"]
  R1 = Resistor [tolerance=±5% resistance=180 power=0.25 package="0805 [SMD]"]
  D22 = Rectifier Diode [part_number=1N5400 package="300 mil [THT]"]

nets:
  N1: D1.cathode, D2.anode
  N2: D1.anode, J1.pin1, D4.cathode, D10.cathode, D7.anode, D16.cathode, D13.anode, D19.anode, U1.Pin_2, U1.Pin_4, U1.Pin_6, U1.Pin_8, D22.cathode
  N3: J1.pin2, D3.cathode, D6.anode, R1.Pin_0
  N4: J1.pin3, D9.cathode, D12.anode, R2.Pin_0
  N5: J1.pin4, D15.cathode, D18.anode, R3.Pin_0
  N6: J1.pin5, D21.cathode, D24.anode, R4.Pin_0
  N7: D2.cathode, D3.anode
  N8: D4.anode, D5.cathode
  N9: D5.anode, D6.cathode
  N10: D8.cathode, D9.anode
  N11: D8.anode, D7.cathode
  N12: D10.anode, D11.cathode
  N13: D11.anode, D12.cathode
  N14: D15.anode, D14.cathode
  N15: D14.anode, D13.cathode
  N16: D16.anode, D17.cathode
  N17: D18.cathode, D17.anode
  N18: D21.anode, D20.cathode
  N19: D20.anode, D19.cathode
  N20: D24.cathode, D23.anode
  N21: D23.cathode, D22.anode
  N22: U1.Pin_1, R1.Pin_1
  N23: U1.Pin_3, R2.Pin_1
  N24: U1.Pin_5, R3.Pin_1
  N25: U1.Pin_7, R4.Pin_1
  N26: U1.Pin_9, C4.+, J2.pin5
  N27: U1.Pin_10, U1.Pin_12, U1.Pin_14, U1.Pin_16, J2.pin1
  N28: U1.Pin_11, C3.+, J2.pin4
  N29: U1.Pin_13, C2.+, J2.pin3
  N30: U1.Pin_15, C1.+, J2.pin2
  N31: C1.-, C2.-, C3.-, C4.-, J2.pin6

notes:
  1N5400
  560µF
