# Fritzing sketch Sporbesættelse_002 (saved by Fritzing 0.9.6b)
circuit board: 10cm x 10cm
perfboards: 1

parts:
  D1 = Rectifier Diode [part_number=1N5400 package="300 mil [THT]"]
  D2 = Rectifier Diode [part_number=1N5400 package="300 mil [THT]"]
  D3 = Rectifier Diode [part_number=1N5400 package="300 mil [THT]"]
  D4 = Rectifier Diode [part_number=1N5400 package="300 mil [THT]"]
  D5 = Rectifier Diode [part_number=1N5400 package="300 mil [THT]"]
  D6 = Rectifier Diode [part_number=1N5400 package="300 mil [THT]"]
  D8 = Rectifier Diode [part_number=1N5400 package="300 mil [THT]"]
  D9 = Rectifier Diode [part_number=1N5400 package="300 mil [THT]"]
  D10 = Rectifier Diode [part_number=1N5400 package="300 mil [THT]"]
  D11 = Rectifier Diode [part_number=1N5400 package="300 mil [THT]"]
  D12 = Rectifier Diode [part_number=1N5400 package="300 mil [THT]"]
  D7 = Rectifier Diode [part_number=1N5400 package="300 mil [THT]"]
  D15 = Rectifier Diode [part_number=1N5400 package="300 mil [THT]"]
  D14 = Rectifier Diode [part_number=1N5400 package="300 mil [THT]"]
  D16 = Rectifier Diode [part_number=1N5400 package="300 mil [THT]"]
  D13 = Rectifier Diode [part_number=1N5400 package="300 mil [THT]"]
  D18 = Rectifier Diode [part_number=1N5400 package="300 mil [THT]"]
  D17 = Rectifier Diode [part_number=1N5400 package="300 mil [THT]"]
  D21 = Rectifier Diode [part_number=1N5400 package="300 mil [THT]"]
  D20 = Rectifier Diode [part_number=1N5400 package="300 mil [THT]"]
  D19 = Rectifier Diode [part_number=1N5400 package="300 mil [THT]"]
  D24 = Rectifier Diode [part_number=1N5400 package="300 mil [THT]"]
  D23 = Rectifier Diode [part_number=1N5400 package="300 mil [THT]"]
  D22 = Rectifier Diode [part_number=1N5400 package="300 mil [THT]"]
  R1 = Resistor [tolerance=±5% power=0.25 resistance=180 package=THT]
  R2 = Resistor [tolerance=±5% power=0.25 resistance=180 package=THT]
  R3 = Resistor [tolerance=±5% power=0.25 resistance=180 package=THT]
  R4 = Resistor [tolerance=±5% power=0.25 resistance=180 package=THT]
  J1 = Camdenboss CTB0158-10 [part_number=CTB0158-10 package=THT]

nets:
  N1: D1.cathode, D2.anode
  N2: D1.anode, D4.cathode, D10.cathode, D7.anode, D16.cathode, D13.anode, D19.anode, D22.cathode, J1.pin1, J1.pin2
  N3: D2.cathode, D3.anode
  N4: D3.cathode, D6.anode, R1.Pin_1, J1.pin4
  N5: D4.anode, D5.cathode
  N6: D5.anode, D6.cathode
  N7: D8.cathode, D9.anode
  N8: D8.anode, D7.cathode
  N9: D9.cathode, D12.anode, R2.Pin_1, J1.pin6
  N10: D10.anode, D11.cathode
  N11: D11.anode, D12.cathode
  N12: D15.cathode, D18.anode, R3.Pin_1, J1.pin8
  N13: D15.anode, D14.cathode
  N14: D14.anode, D13.cathode
  N15: D16.anode, D17.cathode
  N16: D18.cathode, D17.anode
  N17: D21.cathode, D24.anode, R4.Pin_1, J1.pin10
  N18: D21.anode, D20.cathode
  N19: D20.anode, D19.cathode
  N20: D24.cathode, D23.anode
  N21: D23.cathode, D22.anode
  N22: R1.Pin_0, J1.pin3
  N23: R2.Pin_0, J1.pin5
  N24: R3.Pin_0, J1.pin7
  N25: R4.Pin_0, J1.pin9

notes:
  1N5400 / 1N5402
