# Fritzing sketch SporskifteStyring (saved by Fritzing 0.9.6b)
breadboards: 1

parts:
  U1 = PCF8574 [package="DIP16 [THT]"]
  U2 = Sharp PC847X [package=THT]
  M1 = DC Motor [part_number="TORTOISE SLOW MOTION SWITCH MACHINE"]
  R1 = Resistor [tolerance=±5% power=0.25 resistance=100 package=THT]
  R2 = Resistor [tolerance=±5% power=0.25 resistance=100 package=THT]
  R3 = Resistor [tolerance=±5% power=0.25 resistance=100 package=THT]
  R4 = Resistor [tolerance=±5% power=0.25 resistance=100 package=THT]
  S1 = Toggle Switch [package=THT]
  R5 = Resistor [tolerance=±5% power=0.25 resistance=10k package=THT]
  R6 = Resistor [tolerance=±5% power=0.25 resistance=10k package=THT]
  D1 = Schottky Diode [part_number=1N5817 package="300 mil [THT]"]
  D2 = Schottky Diode [part_number=1N5817 package="300 mil [THT]"]
  D3 = Schottky Diode [part_number=1N5817 package="300 mil [THT]"]
  D4 = Schottky Diode [part_number=1N5817 package="300 mil [THT]"]
  LED1 = LED - 5mm [color="Red (633nm)" current=0.030 package="5 mm [THT]"]

nets:
  GND: U1.GND, U2.Pin_9, U2.Pin_13, S1.COM, D2.anode, D4.anode
  N1: U1.P4, S1.L2, R5.Pin_1
  N2: U1.P5, S1.L1, R6.Pin_1
  N3: U1.P6, R2.Pin_0, R3.Pin_0
  N4: U1.P7, R1.Pin_0, R4.Pin_0
  3.3V: U1.VCC, U2.Pin_1, U2.Pin_3, U2.Pin_5, U2.Pin_7, R5.Pin_0, R6.Pin_0
  N5: U2.Pin_2, R1.Pin_1
  N6: U2.Pin_4, R2.Pin_1
  N7: U2.Pin_6, R3.Pin_1
  N8: U2.Pin_8, R4.Pin_1
  N9: U2.Pin_10, U2.Pin_11, M1.pin_2, D3.anode, D4.cathode
  N10: U2.Pin_12, U2.Pin_16, D1.cathode, D3.cathode, LED1.cathode
  N11: U2.Pin_14, U2.Pin_15, M1.pin_1, D1.anode, D2.cathode
  12V: LED1.anode
