# Fritzing sketch principle_track_detection (saved by Fritzing 0.9.6b)
breadboards: 1

parts:
  D1 = Rectifier Diode [part_number=1N4001 package="300 mil [THT]"]
  D2 = Rectifier Diode [part_number=1N4001 package="300 mil [THT]"]
  D3 = Rectifier Diode [part_number=1N4001 package="300 mil [THT]"]
  D4 = Rectifier Diode [part_number=1N4001 package="300 mil [THT]"]
  D5 = Rectifier Diode [part_number=1N4001 package="300 mil [THT]"]
  D6 = Rectifier Diode [part_number=1N4001 package="300 mil [THT]"]
  trainpower_AC_10KHz_20VPP = Screw terminal - 2 pins [package=THT]
  R1 = Resistor [tolerance=±5% power=0.25 resistance=22 package=THT]
  U1 = TLP620 [package="DIP (Dual Inline) [THT]"]
  traintrack_x = Screw terminal - 2 pins [package=THT]
  Vagon = Resistor [tolerance=±5% power=0.25 resistance=2.2k package=THT]
  Tack_Capacitor = Ceramic Capacitor [capacitance=100nF voltage=35V package="100 mil [THT, multilayer]"]
  R2 = Resistor [tolerance=±5% power=0.25 resistance=220 package=THT]
  U2 = PCF8574 [package="DIP16 [THT]"]
  R3 = Resistor [tolerance=±5% power=0.25 resistance=470 package=THT]

nets:
  N1: D1.cathode, D2.anode
  N2: D1.anode, D5.cathode, trainpower_AC_10KHz_20VPP.pin1, U1.pin1, R3.Pin_0
  N3: D2.cathode, D3.anode
  N4: D3.cathode, D4.anode, R1.Pin_0, traintrack_x.pin1, Vagon.Pin_0, Tack_Capacitor.1, R3.Pin_1
  N5: D4.cathode, D6.anode
  N6: D5.anode, D6.cathode
  N7: trainpower_AC_10KHz_20VPP.pin2, traintrack_x.pin2, Vagon.Pin_1, Tack_Capacitor.0
  N8: R1.Pin_1, U1.pin2
  GND: U1.pin3, U2.GND
  N9: U1.pin4, R2.Pin_1, U2.P1
  3.3V: R2.Pin_0, U2.VCC

custom parts:
  TLP620: Photo-transistor optically coupled to two infrared emitting diodes connected in inverse parallel.
